// Logisim project DivideBy3Clock.circ as structural Verilog: 1 circuit, main circuit main
module main (
  input  in_1
);

  wire and_1_out, clock_1_out, d_ff_1_q, d_ff_2_q, d_ff_3_q, d_ff_4_q, d_ff_5_q, d_ff_6_q, d_ff_7_q,
       d_ff_8_q, d_ff_9_q, d_ff_10_q, d_ff_11_q, d_ff_12_q, digital_oscilloscope_1_p1, multiplexer_1_out,
       multiplexer_2_out, multiplexer_3_out, multiplexer_4_out, multiplexer_5_out, multiplexer_6_out,
       not_1_out, not_2_out, not_3_out, not_4_out, not_5_out, not_6_out, not_7_out, not_8_out, not_9_out,
       not_10_out, not_11_out, not_12_out, not_13_out, not_14_out, not_15_out, not_16_out, not_17_out,
       not_18_out, not_19_out, not_20_out, not_21_out, not_22_out, not_23_out, not_24_out, not_25_out;

  Clock clock_1 (.out(clock_1_out));
  and and_1 (and_1_out, clock_1_out, in_1);
  not not_1 (not_1_out, and_1_out);
  not not_2 (not_2_out, in_1);
  // NOT_Gate not_3 has open pins: in=open, out=not_3_out
  // NOT_Gate not_4 has open pins: in=open, out=not_4_out
  not not_5 (not_5_out, in_1);
  D_Flip_Flop d_ff_1 (.clk(not_1_out), .D(d_ff_2_q), .Q(d_ff_1_q), .preset(not_7_out), .reset(not_6_out));  // open: Qn
  D_Flip_Flop d_ff_2 (.clk(not_1_out), .D(d_ff_7_q), .Q(d_ff_2_q), .preset(not_2_out), .reset(not_3_out));  // open: Qn
  // NOT_Gate not_6 has open pins: in=open, out=not_6_out
  not not_7 (not_7_out, in_1);
  D_Flip_Flop d_ff_3 (.clk(and_1_out), .D(d_ff_11_q), .Q(d_ff_3_q), .preset(not_9_out), .reset(not_8_out));  // open: Qn
  // NOT_Gate not_8 has open pins: in=open, out=not_8_out
  not not_9 (not_9_out, in_1);
  D_Flip_Flop d_ff_4 (
    .clk(not_1_out), .D(d_ff_5_q), .Q(d_ff_4_q), .preset(not_10_out), .reset(not_11_out));  // open: Qn
  D_Flip_Flop d_ff_5 (.clk(not_1_out), .D(d_ff_9_q), .Q(d_ff_5_q), .preset(not_5_out), .reset(not_4_out));  // open: Qn
  // NOT_Gate not_10 has open pins: in=open, out=not_10_out
  not not_11 (not_11_out, in_1);
  D_Flip_Flop d_ff_6 (
    .clk(and_1_out), .D(d_ff_12_q), .Q(d_ff_6_q), .preset(not_12_out), .reset(not_13_out));  // open: Qn
  // NOT_Gate not_12 has open pins: in=open, out=not_12_out
  not not_13 (not_13_out, in_1);
  D_Flip_Flop d_ff_7 (
    .clk(not_1_out), .D(d_ff_1_q), .Q(d_ff_7_q), .preset(not_14_out), .reset(not_15_out));  // open: Qn
  // NOT_Gate not_14 has open pins: in=open, out=not_14_out
  not not_15 (not_15_out, in_1);
  D_Flip_Flop d_ff_8 (
    .clk(and_1_out), .D(d_ff_3_q), .Q(d_ff_8_q), .preset(not_17_out), .reset(not_16_out));  // open: Qn
  // NOT_Gate not_16 has open pins: in=open, out=not_16_out
  not not_17 (not_17_out, in_1);
  // NOT_Gate not_18 has open pins: in=open, out=not_18_out
  D_Flip_Flop d_ff_9 (
    .clk(not_1_out), .D(d_ff_4_q), .Q(d_ff_9_q), .preset(not_19_out), .reset(not_20_out));  // open: Qn
  not not_19 (not_19_out, in_1);
  // NOT_Gate not_20 has open pins: in=open, out=not_20_out
  D_Flip_Flop d_ff_10 (
    .clk(and_1_out), .D(d_ff_6_q), .Q(d_ff_10_q), .preset(not_22_out), .reset(not_23_out));  // open: Qn
  not not_21 (not_21_out, in_1);
  // NOT_Gate not_22 has open pins: in=open, out=not_22_out
  not not_23 (not_23_out, in_1);
  D_Flip_Flop d_ff_11 (
    .clk(and_1_out), .D(d_ff_8_q), .Q(d_ff_11_q), .preset(not_18_out), .reset(not_24_out));  // open: Qn
  not not_24 (not_24_out, in_1);
  D_Flip_Flop d_ff_12 (
    .clk(and_1_out), .D(d_ff_10_q), .Q(d_ff_12_q), .preset(not_21_out), .reset(not_25_out));  // open: Qn
  // NOT_Gate not_25 has open pins: in=open, out=not_25_out
  Multiplexer multiplexer_1 (.in0(d_ff_2_q), .in1(d_ff_3_q), .out(multiplexer_1_out), .sel(and_1_out));
  Multiplexer multiplexer_2 (.in0(d_ff_1_q), .in1(d_ff_8_q), .out(multiplexer_2_out), .sel(and_1_out));
  Multiplexer multiplexer_3 (.in0(d_ff_5_q), .in1(d_ff_6_q), .out(multiplexer_3_out), .sel(and_1_out));
  Multiplexer multiplexer_4 (.in0(d_ff_4_q), .in1(d_ff_10_q), .out(multiplexer_4_out), .sel(and_1_out));
  Multiplexer multiplexer_5 (.in0(d_ff_7_q), .in1(d_ff_11_q), .out(multiplexer_5_out), .sel(and_1_out));
  Multiplexer multiplexer_6 (.in0(d_ff_9_q), .in1(d_ff_12_q), .out(multiplexer_6_out), .sel(and_1_out));
  // Digital_Oscilloscope #(.nState(16)) digital_oscilloscope_1: pin names not known; wires that end beside it: digital_oscilloscope_1_p1, multiplexer_1_out, multiplexer_2_out, multiplexer_5_out, multiplexer_3_out, multiplexer_4_out, multiplexer_6_out
  Clock clock_2 (.out(digital_oscilloscope_1_p1));

  // Other names for the same wires on the sheet: RSTB = in_1
endmodule
