// Logisim project 652_CPU_2.circ as structural Verilog: 1 circuit, main circuit main
module main (
);

  wire Clk12Mhz, Clk25Mhz, Clk50Mhz, Clk100Mhz, Clk200Mhz, digital_oscilloscope_1_p2;

  // Digital_Oscilloscope #(.frontlines("falling"), .nState(24)) digital_oscilloscope_1: pin names not known; wires that end beside it: Clk100Mhz, digital_oscilloscope_1_p2
  or or_1 (digital_oscilloscope_1_p2, Clk25Mhz, Clk12Mhz);
  Clock clock_1 (.out(Clk200Mhz));
  Counter #(.max('hf), .width(4)) counter_1 (
    .Q({Clk12Mhz, Clk25Mhz, Clk50Mhz, Clk100Mhz}), .clk(Clk200Mhz));  // open: load, D, count, carry, up, clr

  // Notes on the sheet:
  //   200Mhz = 5ns (2.5+2.5)
  //   100Mhz = 10ns
  //   50Mhz = 20ns
  //   25Mhz = 40ns
  //   12.5Mhz = 80ns (40+40 or 20+60)
endmodule
