// Logisim project 658_CPU_Evolution.circ as structural Verilog: 8 circuits, main circuit CPU_Board
module CPU_Board (
  input  INT0,
  input  INT1,
  input  INT2,
  input  INT3,
  input  INT4,
  input  INT5,
  input  INT6,
  input  INT7,
  output External_Device_Valid
);

  wire Address_Stage, Address_Stage_B, Address_Valid, and_1_out, and_3_out, and_5_out, and_6_out, and_7_out,
       and_8_out, and_9_out, and_13_out, BA_Latch_B, Bank_out, Data_Latch_B, Data_out, decoder_1_out0,
       decoder_1_out1, decoder_1_out2, decoder_1_out3, decoder_1_out4, decoder_1_out5, decoder_1_out6,
       decoder_1_out7, Device_Valid, IDV, IDV_1, In_out, IRQ, IRQB, L_31MHz, L_62MHz, L_125MHz,
       L_125MHz_bbe51f64_out, L_128K_Address, not_1_out, not_3_out, not_4_out, not_5_out, not_6_out,
       not_7_out, not_8_out, not_9_out, not_10_out, not_12_out, not_13_out, not_14_out, not_16_out,
       not_17_out, not_19_out, not_26_out, not_27_out, not_29_out, not_30_out, not_32_out, or_2_out,
       or_4_out, or_5_out, or_6_out, or_7_out, or_8_out, or_9_out, or_10_out, or_11_out, Out_out,
       pull_resistor_1_node, Read, Read_B, undriven, VDA, VPA, VPB;
  wire [3:1] priority_encoder_1_out;
  wire [3:3] counter_1_q;
  wire [7:0] BA_Latch_q, BA_Latch_t, controlled_buffer_1_out, controlled_buffer_4_out,
       controlled_buffer_5_out, D_BA, latch_8bit_3_state_1_t, pull_resistor_2_node, Read_Data_Latch_t,
       transceiver_8bit_1_q, w65c816s_1_addr16, w65c816s_1_data7_w, w65c816s_1_ic, Write_Data_Latch_q,
       Write_Data_Latch_t;
  wire [15:0] A;
  wire [23:16] or_1_out;

  // Probe on BA_Latch_t
  Latch_8bit_3_State BA_Latch (.T(BA_Latch_t), .Q(BA_Latch_q), .D(D_BA), .LEB(BA_Latch_B), .OEB(pull_resistor_1_node));
  Pull_Resistor pull_resistor_1 (.node(pull_resistor_1_node));
  not not_1 (not_1_out, VPB);
  and and_1 (and_1_out, not_1_out, A[3], A[2], A[1]);
  and and_2 (IRQ, undriven, and_1_out);
  not not_2 (IRQB, undriven);
  Priority_Encoder priority_encoder_1 (
    .in0(INT0), .in1(INT1), .in2(INT2), .in3(INT3), .in4(INT4), .in5(INT5), .in6(INT6), .in7(INT7),
    .out(priority_encoder_1_out));  // open: en_in
  // Probe on {or_1_out, A}
  and and_3 (and_3_out, not_4_out, not_5_out, not_6_out);
  and and_4 (L_128K_Address, and_3_out, and_6_out);
  assign or_1_out = w65c816s_1_addr16 | {8{1'b0}};  // OR_Gate or_1, 8 bits wide
  not not_3 (not_3_out, BA_Latch_q[0]);
  not not_4 (not_4_out, BA_Latch_q[1]);
  not not_5 (not_5_out, BA_Latch_q[2]);
  not not_6 (not_6_out, BA_Latch_q[3]);
  not not_7 (not_7_out, BA_Latch_q[4]);
  not not_8 (not_8_out, BA_Latch_q[5]);
  not not_9 (not_9_out, BA_Latch_q[6]);
  and and_5 (and_5_out, not_3_out, not_4_out, not_5_out, not_6_out);
  and and_6 (and_6_out, not_7_out, not_8_out, not_9_out, not_12_out);
  and and_7 (and_7_out, and_5_out, and_6_out);
  not not_10 (not_10_out, IRQB);
  // NOT_Gate not_11 has open pins: in=1'b1, out=open
  W65C816S w65c816s_1 (
    .VPB(VPB), .IC(w65c816s_1_ic), .DATA0_W(w65c816s_1_data7_w[7]), .DATA1_W(w65c816s_1_data7_w[6]),
    .DATA2_W(w65c816s_1_data7_w[5]), .DATA3_W(w65c816s_1_data7_w[4]), .DATA4_W(w65c816s_1_data7_w[3]),
    .DATA5_W(w65c816s_1_data7_w[2]), .DATA6_W(w65c816s_1_data7_w[1]), .DATA7_W(w65c816s_1_data7_w[0]),
    .R_WB(Read), .ADDR0(A[0]), .ADDR1(A[1]), .ADDR2(A[2]), .ADDR3(A[3]), .ADDR4(A[4]), .ADDR5(A[5]),
    .ADDR6(A[6]), .ADDR7(A[7]), .ADDR8(A[8]), .ADDR9(A[9]), .ADDR10(A[10]), .ADDR11(A[11]), .ADDR12(A[12]),
    .ADDR13(A[13]), .ADDR14(A[14]), .ADDR15(A[15]), .ADDR16(w65c816s_1_addr16[0]),
    .ADDR17(w65c816s_1_addr16[1]), .ADDR18(w65c816s_1_addr16[2]), .ADDR19(w65c816s_1_addr16[3]),
    .ADDR20(w65c816s_1_addr16[4]), .ADDR21(w65c816s_1_addr16[5]), .ADDR22(w65c816s_1_addr16[6]),
    .ADDR23(w65c816s_1_addr16[7]), .DA(VPA), .PA(VDA), .DATA1_R(controlled_buffer_4_out[6]),
    .DATA2_R(controlled_buffer_4_out[5]), .DATA3_R(controlled_buffer_4_out[4]),
    .DATA4_R(controlled_buffer_4_out[3]), .DATA5_R(controlled_buffer_4_out[2]),
    .DATA6_R(controlled_buffer_4_out[1]), .DATA7_R(controlled_buffer_4_out[0]),
    .DATA0_R(controlled_buffer_4_out[7]), .IRQ(not_10_out), .PHI2(Address_Stage));  // open: NMI
  // Probe on w65c816s_1_ic
  assign controlled_buffer_1_out = Data_out ? w65c816s_1_data7_w : 8'bz;  // Controlled_Buffer controlled_buffer_1
  assign controlled_buffer_1_out = Bank_out ? or_1_out : 8'bz;  // Controlled_Buffer controlled_buffer_2
  assign D_BA = Out_out ? controlled_buffer_1_out : 8'bz;  // Controlled_Buffer controlled_buffer_3
  not not_12 (not_12_out, BA_Latch_q[7]);
  buf Bank (Bank_out, Address_Stage);
  // Probe on controlled_buffer_4_out
  // Probe on w65c816s_1_data7_w
  assign controlled_buffer_4_out = In_out ? controlled_buffer_5_out : 8'bz;  // Controlled_Buffer controlled_buffer_4
  assign controlled_buffer_5_out = Bank_out ? pull_resistor_2_node : 8'bz;  // Controlled_Buffer controlled_buffer_5
  assign controlled_buffer_5_out = Data_out ? D_BA : 8'bz;  // Controlled_Buffer controlled_buffer_6
  Pull_Resistor #(.pull("X")) pull_resistor_2 (.node(pull_resistor_2_node));
  or or_2 (or_2_out, Address_Stage, ~Read);  // OR_Gate
  buf Out (Out_out, or_2_out);
  not In (In_out, or_2_out);
  not Data (Data_out, Address_Stage);
  not not_13 (not_13_out, A[8]);
  and and_8 (and_8_out, A[15], A[14], A[13], A[12]);
  and and_9 (and_9_out, A[11], A[10], A[9], not_13_out);
  and and_10 (Device_Valid, and_8_out, and_9_out);
  or or_3 (Address_Valid, VDA, VPA);
  and and_11 (IDV, Device_Valid, A[7], and_7_out);
  not not_14 (not_14_out, A[7]);
  not not_15 (Read_B, Read);
  // Probe on A[3:0]
  // Probe on A[7:4]
  and and_12 (External_Device_Valid, Device_Valid, not_14_out, and_7_out);
  Transceiver_8bit transceiver_8bit_1 (.Q(transceiver_8bit_1_q), .D(A[15:8]), .OEB(IRQ));
  Transceiver_8bit transceiver_8bit_2 (
    .Q(transceiver_8bit_1_q), .D({4'b0000, priority_encoder_1_out, A[0]}), .OEB(not_16_out));
  // Probe on {4'b0000, priority_encoder_1_out, A[0]}
  not not_16 (not_16_out, IRQ);
  or or_4 (or_4_out, Read_B, Data_Latch_B);
  or or_5 (or_5_out, Read_B, Address_Stage);
  // Probe on Read_Data_Latch_t
  // Probe on Write_Data_Latch_q
  Latch_8bit_3_State Read_Data_Latch (
    .T(Read_Data_Latch_t), .Q(D_BA), .D(Write_Data_Latch_q), .LEB(or_4_out), .OEB(or_5_out));
  // Probe on D_BA
  // Probe on A[6:4]
  Decoder #(.enable("false"), .select(3)) decoder_1 (
    .out0(decoder_1_out0), .out1(decoder_1_out1), .out2(decoder_1_out2), .out3(decoder_1_out3),
    .out4(decoder_1_out4), .out5(decoder_1_out5), .out6(decoder_1_out6), .out7(decoder_1_out7), .sel(A[6:4]));
  not not_17 (not_17_out, decoder_1_out0);
  // NOT_Gate not_18 has open pins: in=decoder_1_out1, out=open
  not not_19 (not_19_out, IDV);
  or or_6 (or_6_out, Address_Stage_B, Read_B);
  or or_7 (or_7_out, or_6_out, not_19_out, not_17_out);
  // Probe on latch_8bit_3_state_1_t
  Latch_8bit_3_State latch_8bit_3_state_1 (
    .T(latch_8bit_3_state_1_t), .Q(D_BA), .D(D_BA), .LEB(or_11_out), .OEB(or_7_out));
  or or_8 (or_8_out, Read, Data_Latch_B);
  or or_9 (or_9_out, Address_Stage, Read);
  // Probe on Write_Data_Latch_t
  Latch_8bit_3_State Write_Data_Latch (
    .T(Write_Data_Latch_t), .Q(Write_Data_Latch_q), .D(D_BA), .LEB(or_8_out), .OEB(or_9_out));
  // NOT_Gate not_20 has open pins: in=decoder_1_out2, out=open
  // NOT_Gate not_21 has open pins: in=decoder_1_out3, out=open
  // NOT_Gate not_22 has open pins: in=decoder_1_out4, out=open
  // NOT_Gate not_23 has open pins: in=decoder_1_out5, out=open
  // NOT_Gate not_24 has open pins: in=decoder_1_out6, out=open
  // NOT_Gate not_25 has open pins: in=decoder_1_out7, out=open
  not not_26 (not_26_out, IDV_1);
  or or_10 (or_10_out, Address_Stage, Read);
  or or_11 (or_11_out, not_17_out, not_26_out, or_10_out);
  // Probe on D_BA
  not not_27 (not_27_out, L_125MHz_bbe51f64_out);
  Counter #(.max('hf), .width(4)) counter_1 (
    .Q({counter_1_q[3], Address_Stage, L_31MHz, L_62MHz}), .clk(L_125MHz_bbe51f64_out));  // open: load, D, count, carry, up, clr
  Clock L_125MHz_bbe51f64 (.out(L_125MHz_bbe51f64_out));
  not not_28 (L_125MHz, not_27_out);
  not not_29 (not_29_out, L_62MHz);
  LED led_1 (.in(Address_Stage));
  not not_30 (not_30_out, L_31MHz);
  not not_31 (Address_Stage_B, Address_Stage);
  or or_12 (BA_Latch_B, Address_Stage_B, L_31MHz, not_29_out);
  or or_13 (Data_Latch_B, Address_Stage, L_31MHz, L_62MHz);
  // Probe on {BA_Latch_q[0], transceiver_8bit_1_q, A[7:0]}
  not not_32 (not_32_out, Device_Valid);
  and and_13 (and_13_out, Address_Valid, not_32_out, L_128K_Address, Address_Stage_B);
  RAM #(.addrWidth(17), .databus("bidir"), .trigger("high"), .\type ("nonvolatile")) ram_1 (
    .addr({BA_Latch_q[0], transceiver_8bit_1_q, A[7:0]}), .we(Read), .oe(and_13_out),
    .data(Write_Data_Latch_q));  // open: clk

  // Other names for the same wires on the sheet: Data_Stage_B = Address_Stage; L_16MHz = Address_Stage;
  //   PHI2 = Address_Stage; Data_Stage = Address_Stage_B; Write = Read_B; RWB = Read; Write_B = Read

  // Notes on the sheet:
  //   Bank Address
  //   Bank
  //   Address hi
  //   Address lo
  //   In 64K Address
  //   Read
  //   W65C816
  //   Write
  //   Internal Device Valid
  //   Device Address
  //   Device ID
endmodule

module W65C816S (
  input  DATA0_R,
  input  DATA1_R,
  input  DATA2_R,
  input  DATA3_R,
  input  DATA4_R,
  input  DATA5_R,
  input  DATA6_R,
  input  DATA7_R,
  input  NMI,
  input  IRQ,
  input  PHI2,
  output DATA0_W,
  output DATA1_W,
  output DATA2_W,
  output DATA3_W,
  output DATA4_W,
  output DATA5_W,
  output DATA6_W,
  output DATA7_W,
  output R_WB,
  output ADDR0,
  output ADDR1,
  output ADDR2,
  output ADDR3,
  output ADDR4,
  output ADDR5,
  output ADDR6,
  output ADDR7,
  output ADDR8,
  output ADDR9,
  output ADDR10,
  output ADDR11,
  output ADDR12,
  output ADDR13,
  output ADDR14,
  output ADDR15,
  output ADDR16,
  output ADDR17,
  output ADDR18,
  output ADDR19,
  output ADDR20,
  output ADDR21,
  output ADDR22,
  output ADDR23,
  output DA,
  output PA,
  output VPB,
  output [7:0] IC
);

  wire and_1_out, and_2_out, and_3_out, and_4_out, and_5_out, and_6_out, and_7_out, counter_1_q, d_ff_1_q,
       mpu_int_emulation_1_busy, mpu_int_emulation_1_da, mpu_int_emulation_1_pa, mpu_int_emulation_1_r_wb,
       mpu_prg_emulation_1_busy, mpu_prg_emulation_1_da, mpu_prg_emulation_1_pa, mpu_prg_emulation_1_r_wb,
       not_1_out, not_2_out, not_3_out, not_4_out, not_5_out, not_6_out, not_7_out, not_8_out, not_9_out,
       or_1_out, or_2_out;
  wire [7:0] adder_1_out, controlled_buffer_9_out, mpu_int_emulation_1_data, mpu_int_emulation_1_ic,
       mpu_prg_emulation_1_data, mpu_prg_emulation_1_ic;
  wire [15:0] mpu_int_emulation_1_addr, mpu_prg_emulation_1_addr;

  Counter #(.max('h1), .trigger("falling"), .width(1)) counter_1 (
    .Q(counter_1_q), .clk(mpu_prg_emulation_1_busy), .clr(mpu_prg_emulation_1_busy));  // open: load, D, count, carry, up
  not not_1 (not_1_out, NMI);
  not not_2 (not_2_out, IRQ);
  or or_1 (or_1_out, counter_1_q, mpu_prg_emulation_1_busy);
  not not_3 (not_3_out, mpu_int_emulation_1_busy);
  and and_1 (and_1_out, not_1_out, not_2_out);
  and and_2 (and_2_out, or_1_out, not_3_out);
  not not_4 (not_4_out, and_2_out);
  not not_5 (not_5_out, mpu_prg_emulation_1_busy);
  D_Flip_Flop #(.trigger("high")) d_ff_1 (
    .clk(not_6_out), .D(not_6_out), .Q(d_ff_1_q), .reset(mpu_int_emulation_1_busy));  // open: Qn, preset
  not not_6 (not_6_out, and_1_out);
  and and_3 (and_3_out, not_5_out, d_ff_1_q);
  and and_4 (and_4_out, PHI2, mpu_int_emulation_1_busy);
  and and_5 (and_5_out, PHI2, not_7_out);
  not not_7 (not_7_out, mpu_int_emulation_1_busy);
  or or_2 (or_2_out, and_3_out, and_4_out);
  not not_8 (not_8_out, mpu_prg_emulation_1_r_wb);
  LED led_1 (.in(and_2_out));
  MPU_PRG_Emulation mpu_prg_emulation_1 (
    .IC(mpu_prg_emulation_1_ic), .DATA(mpu_prg_emulation_1_data), .BUSY(mpu_prg_emulation_1_busy),
    .R_WB(mpu_prg_emulation_1_r_wb), .ADDR(mpu_prg_emulation_1_addr), .PA(mpu_prg_emulation_1_pa),
    .DA(mpu_prg_emulation_1_da), .PHI2(and_5_out));
  // Probe on mpu_prg_emulation_1_ic
  LED led_2 (.in(not_4_out));
  MPU_INT_Emulation mpu_int_emulation_1 (
    .IC(mpu_int_emulation_1_ic), .DATA(mpu_int_emulation_1_data), .BUSY(mpu_int_emulation_1_busy),
    .R_WB(mpu_int_emulation_1_r_wb), .ADDR(mpu_int_emulation_1_addr), .DA(mpu_int_emulation_1_da),
    .PA(mpu_int_emulation_1_pa), .VPB(VPB), .PHI2(or_2_out), .IRQB(not_2_out), .NMIB(not_1_out));
  // Probe on mpu_int_emulation_1_ic
  Adder adder_1 (.a(mpu_int_emulation_1_ic), .b(8'h10), .out(adder_1_out), .cin(and_2_out));  // open: cout
  // Probe on mpu_prg_emulation_1_data
  assign {DATA7_W, DATA6_W, DATA5_W, DATA4_W, DATA3_W, DATA2_W, DATA1_W, DATA0_W} = and_6_out ? mpu_prg_emulation_1_data : 8'bz;  // Controlled_Buffer controlled_buffer_1
  and and_6 (and_6_out, and_2_out, not_8_out);
  // Probe on mpu_int_emulation_1_data
  assign {DATA7_W, DATA6_W, DATA5_W, DATA4_W, DATA3_W, DATA2_W, DATA1_W, DATA0_W} = and_7_out ? mpu_int_emulation_1_data : 8'bz;  // Controlled_Buffer controlled_buffer_2
  and and_7 (and_7_out, not_4_out, not_9_out);
  not not_9 (not_9_out, mpu_int_emulation_1_r_wb);
  assign R_WB = and_2_out ? mpu_prg_emulation_1_r_wb : 1'bz;  // Controlled_Buffer controlled_buffer_3
  assign R_WB = not_4_out ? mpu_int_emulation_1_r_wb : 1'bz;  // Controlled_Buffer controlled_buffer_4
  assign {ADDR15, ADDR14, ADDR13, ADDR12, ADDR11, ADDR10, ADDR9, ADDR8, ADDR7, ADDR6, ADDR5, ADDR4, ADDR3, ADDR2, ADDR1, ADDR0} = and_2_out ? mpu_prg_emulation_1_addr : 16'bz;  // Controlled_Buffer controlled_buffer_5
  assign {ADDR15, ADDR14, ADDR13, ADDR12, ADDR11, ADDR10, ADDR9, ADDR8, ADDR7, ADDR6, ADDR5, ADDR4, ADDR3, ADDR2, ADDR1, ADDR0} = not_4_out ? mpu_int_emulation_1_addr : 16'bz;  // Controlled_Buffer controlled_buffer_6
  // Probe on {DATA7_W, DATA6_W, DATA5_W, DATA4_W, DATA3_W, DATA2_W, DATA1_W, DATA0_W}
  assign IC = and_2_out ? mpu_prg_emulation_1_ic : 8'bz;  // Controlled_Buffer controlled_buffer_7
  assign IC = not_4_out ? adder_1_out : 8'bz;  // Controlled_Buffer controlled_buffer_8
  assign controlled_buffer_9_out = R_WB ? {DATA7_R, DATA6_R, DATA5_R, DATA4_R, DATA3_R, DATA2_R, DATA1_R, DATA0_R} : 8'bz;  // Controlled_Buffer controlled_buffer_9
  assign DA = and_2_out ? mpu_prg_emulation_1_da : 1'bz;  // Controlled_Buffer controlled_buffer_10
  assign PA = and_2_out ? mpu_prg_emulation_1_pa : 1'bz;  // Controlled_Buffer controlled_buffer_11
  Pull_Resistor pull_resistor_1 (.node(ADDR16));
  assign DA = not_4_out ? mpu_int_emulation_1_pa : 1'bz;  // Controlled_Buffer controlled_buffer_12
  assign PA = not_4_out ? mpu_int_emulation_1_da : 1'bz;  // Controlled_Buffer controlled_buffer_13

  assign ADDR17 = ADDR16;
  assign ADDR18 = ADDR16;
  assign ADDR19 = ADDR16;
  assign ADDR20 = ADDR16;
  assign ADDR21 = ADDR16;
  assign ADDR22 = ADDR16;
  assign ADDR23 = ADDR16;

  // Notes on the sheet:
  //   DATA0_W: pull=up
  //   DATA1_W: pull=up
  //   DATA2_W: pull=up
  //   DATA3_W: pull=up
  //   DATA4_W: pull=up
  //   DATA5_W: pull=up
  //   DATA6_W: pull=up
  //   DATA7_W: pull=up
  //   NMI: pull=up
  //   IRQ: pull=up
endmodule

module Memory_Copier (
  input  Copy_ROM,
  input  Copy_Latch,
  input  ABORT,
  input  Write,
  input  D0,
  input  D1,
  input  D2,
  input  D3,
  input  D4,
  input  D5,
  input  D6,
  input  D7
);

  wire and_1_out, Clk_out, controlled_buffer_1_out, controlled_buffer_2_out, controlled_buffer_3_out,
       counter_1_carry, counter_2_carry, d_ff_1_q, d_ff_2_q, not_1_out, not_2_out, or_1_out, or_2_out,
       or_3_out, pull_resistor_1_node, pull_resistor_2_node, pull_resistor_3_node, pull_resistor_4_node,
       pull_resistor_5_node;
  wire [3:0] counter_2_q;
  wire [7:0] controlled_buffer_4_out, register_1_q, rom_1_data;
  wire [11:0] counter_1_q;

  Clock Clk (.out(Clk_out));
  assign controlled_buffer_1_out = pull_resistor_1_node ? Copy_ROM : 1'bz;  // Controlled_Buffer controlled_buffer_1
  Pull_Resistor #(.pull(1)) pull_resistor_1 (.node(pull_resistor_1_node));
  assign controlled_buffer_2_out = pull_resistor_2_node ? Copy_Latch : 1'bz;  // Controlled_Buffer controlled_buffer_2
  Pull_Resistor #(.pull(1)) pull_resistor_2 (.node(pull_resistor_2_node));
  assign controlled_buffer_3_out = pull_resistor_3_node ? ABORT : 1'bz;  // Controlled_Buffer controlled_buffer_3
  Pull_Resistor #(.pull(1)) pull_resistor_3 (.node(pull_resistor_3_node));
  not not_1 (not_1_out, Write);
  or or_1 (or_1_out, controlled_buffer_1_out, controlled_buffer_2_out, controlled_buffer_3_out, or_3_out);
  D_Flip_Flop #(.trigger("high")) d_ff_1 (
    .clk(controlled_buffer_1_out), .D(controlled_buffer_1_out), .Q(d_ff_1_q), .reset(or_3_out));  // open: Qn, preset
  D_Flip_Flop #(.trigger("high")) d_ff_2 (
    .clk(controlled_buffer_2_out), .D(controlled_buffer_2_out), .Q(d_ff_2_q), .reset(or_3_out));  // open: Qn, preset
  not not_2 (not_2_out, or_1_out);
  or or_2 (or_2_out, d_ff_1_q, d_ff_2_q);
  or or_3 (or_3_out, counter_2_carry, controlled_buffer_3_out);
  Register #(.trigger("high")) register_1 (
    .D({D7, D6, D5, D4, D3, D2, D1, D0}), .en(not_1_out), .Q(register_1_q), .clk(not_1_out));  // open: clr
  and and_1 (and_1_out, Clk_out, not_2_out, or_2_out);
  Counter #(.max('hfff), .width(12)) counter_1 (
    .Q(counter_1_q), .carry(counter_1_carry), .clk(and_1_out), .clr(or_1_out));  // open: load, D, count, up
  Counter #(.max('hf), .width(4)) counter_2 (
    .Q(counter_2_q), .carry(counter_2_carry), .clk(counter_1_carry), .clr(or_1_out));  // open: load, D, count, up
  ROM #(.addrWidth(16)) rom_1 (.addr({counter_2_q, counter_1_q}), .data(rom_1_data));
  assign controlled_buffer_4_out = d_ff_1_q ? rom_1_data : 8'bz;  // Controlled_Buffer controlled_buffer_4
  assign controlled_buffer_4_out = d_ff_2_q ? register_1_q : 8'bz;  // Controlled_Buffer controlled_buffer_5
  Pull_Resistor pull_resistor_4 (.node(pull_resistor_4_node));
  // Probe on {counter_2_q, counter_1_q}
  RAM #(.addrWidth(16), .databus("bidir"), .enables("line"), .trigger("high")) ram_1 (
    .addr({counter_2_q, counter_1_q}), .data(controlled_buffer_4_out));  // open: we, oe, clk
  Pull_Resistor #(.pull(1)) pull_resistor_5 (.node(pull_resistor_5_node));
  // Probe on controlled_buffer_4_out

  // Notes on the sheet:
  //   contents of rom_1 (hex, n*v repeats v):
  //   40 9c c3 1a 7e b9 ef f3 b6 16 c2 83 d7 11 dd f2 85 ad b6 ac 57 d0 d7 a1 18 84 1b 86 7 38 f6 14 19 fd
  //   ab 45 33 ca 94 9b 71 b9 5e 5a 63 49 4c ca 4c 9b 70 77 62 b6 f6 72 12 c4 5b 8e 3a 54 af a5 6e 97 d7
  //   d1 35 a4 ce b4 4a b5 e0 b2 dc 69 ef 33 d0 1 af e4 fb a5 eb f3 69 9d bf 57 9a 99 dc 6 c0 ea c9 3e 4
  //   c7 1d bf c0 8b c7 c c3 f3 47 ae 90 61 f3 71 a0 1c 35 a6 9d 8f c8 61 a7 87 ff b9 90 76 ff c 20 b4 1
  //   3a 52 b9 93 e6 96 65 d5 b9 e 3a bc a0 d3 9d 53 a 2e 1a f6 2b e0 9e 97 3d 5c bb fb bb 9 e9 fa a6 82
  //   c1 c3 c1 d6 41 17 d5 c9 b 8a ef 12 a7 c7 9e 9d be ca 37 c7 5e 24 12 a6 3a 3b cb 3f e7 88 83 cf 21 d9
  //   1d 4 5 8e 83 41 56 dd df df ba f e4 68 fb c2 4 db 47 26 b8 ec 71 41 bc 42 2e 2c 51 b8 5a 54 7a 9e 33
  //   bb 41 f6 9a 35 f1 b8 55 ad 5a 10 50 5f 11 9c d9 1d af af e1 8b e 92 3f 64 90 bf ed b4 59 25 49 1c 90
  //   68 56 12 a3 1f fa 20 82 15 3f 21 e0 8a 94 89 76 70 a 9b 41 af 98 b1 c0 62 58 78 38 19 c9 32 f1 17 c
  //   f4 77 92 28 e7 da f7 47 89 f0 24 f8 e9 8f ad 6c ef d5 19 ba 93 61 23 1c 22 98 fb 31 7e e2 83 3a 5b
  //   eb 93 5f 84 e4 36 e8 15 c0 ec 85 bf 79 e8 87 9 4a 50 25 8a f3 81 ba 31 f9 49 3 7e e4 2c 62 c7 81 a1
  //   1e 75 1f 53 a2 46 d2 61 bb 8a b4 9f db 67 20 d4 5a 16 f6 fb b0 24 db 84 bd b3 78 92 3 b8 b7 3b e7 3c
  //   a cc f5 9c a5 3 1a ca c0 54 e8 8b d7 25 d7 b7 ea 13 80 7d bf 2d e1 9e 1c 35 9c ae f e3 39 58 27 22
  //   61 97 b9 52 22 ff 1c 85 2f f3 ef c3 1d ed 4f 48 a8 bb 23 c2 ed bd 51 95 af 29 7 17 94 48 f4 d5 66 b8
  //   8d cd 53 a9 4a b3 2e 20 e8 2e ac 38 a5 19 a9 5e 88 c4 63 91 98 31 bb a9 20 59 77 8e f3 65 83 7d a3
  //   f6 2d 47 c9 5f 66 93 42 e6 5 18 6c 8 4 e5 6e b3 c1 9b 6f 8b 3f ae db 27 64 a8 a2 52 3a 67 7a 4c 30
  //   5b 19 7 57 ca 7c 6b a6 e 25 94 37 d2 55 10 89 59 57 22 bd b8 b6 3 da 18 83 1d a f6 91 4f dc 64 ba 2d
  //   81 47 18 3d 10 98 4e 3c c4 a4 be 59 39 4d d1 76 b4 47 33 6b 59 5d 14 44 73 ab 6a 7e b1 e2 2c 4f 64
  //   88 95 dc c4 37 68 82 29 db 27 f 53 f5 5b 7 a3 db d0 e1 61 f6 d7 48 f5 4 84 5b 2f 55 ee ee 80 f 73 c9
  //   40 6b f3 e5 e7 f6 11 b3 55 d2 76 55 c f4 f e3 71 65 4b a9 10 82 5e 65 d6 3d 82 8b 56 5a 32 82 5 b4
  //   6f e4 7f 77 fc c3 c1 65 a2 e0 6d 12 6e f3 b 28 ef e7 44 a5 7a 1c 26 1a 67 a4 64 eb 52 88 93 92 5c 1
  //   6f dd 68 c0 15 2c 60 28 48 b5 6f 8f ae c1 45 82 11 ed 57 0 9f 6b 1d bb 2b 40 53 5b 6b 85 3a bb 38 a7
  //   d6 2a d3 a8 2e ad 1c 5d 90 39 da af cb fb f7 db 74 90 c1 b2 24 4e 2b db b5 7b b d 89 91 5b 57 c4 82
  //   79 5a 8d ef 68 8a 52 70 e 71 3 d0 75 ed 53 4e c 6e fb de e4 3a f8 68 f4 aa c9 5 56 6c b3 46 89 c0 fe
  //   6e ae bc 36 b3 cc 89 6b 82 d a4 73 b9 0 1f 24 ec d6 df 9c a2 a6 dd 7a 96 ab 66 23 f7 81 5b ff a9 6d
  //   73 ba 84 93 75 85 91 3e 80 54 51 1d 45 1e f6 81 48 21 a9 a2 24 1c c3 d8 c4 94 16 e3 ac 11 22 24 2f
  //   60 61 e3 b7 d0 7d 88 2 75 96 e3 60 69 7e 65 f7 7 fd 66 0 2f e 5e 8 86 21 2d 31 b5 58 55 70 a6 cc 3b
  //   ce cb c6 6b a8 58 7 d2 f0 85 2 3 6a ce 1e 73 f1 33 f6 be b1 7a 99 e1 6b 69 cb 7f b6 e 43 1d 39 f8 ec
  //   67 f3 7c 26 6a 74 f2 4 d9 23 f6 8c 49 77 a8 fa 76 3f ee fe 7d db ae fb 21 81 16 48 8 7a d5 70 fc 63
  //   60 72 2b 6e 2f 2 68 a0 ff c7 69 12 f 9c 8 31 63 d1 83 ff 5 68 bd 51 40 59 7c f e4 d0 aa 78 86 6b 95
  //   5d be 7d 30 63 69 4f 51 42 e6 5b f2 9 59 90 71 58 ec 92 d1 a6 a f8 f8 7a a3 8d f0 b3 6d 91 28 c1 1e
  //   f6 b1 ea b4 a4 82 87 ae b6 b5 46 50 bc c9 67 e4 f9 df 0 f5 a3 fe 3a 94 27 50 92 94 63 64 1a cf eb 6b
  //   b7 60 46 7c 61 e7 2f d2 67 c9 d6 9 aa 6e 1d 66 df 82 dc d ce 36 1e 49 96 7d 63 c9 e8 51 de de 48 ec
  //   b5 c0 50 11 45 c7 ee 42 5c b3 a2 8 7e e5 c3 2f 21 a5 b8 8 f2 5b 3f a7 10 d7 ab 23 4d 8a 1e da 71 cc
  //   d5 ac 77 15 5a 3c cf 45 d0 33 9c de 2c 7e f4 45 76 8c 24 6 e 92 ea e e2 c7 b9 f0 ba a9 fa 21 6e 38
  //   47 3d 2b 37 af 41 b2 70 f7 d0 9a ed d4 6f 8a 40 32 ca 81 bd 70 ee f bc a3 8e 9a d9 d0 3f 9c 35 34 bd
  //   e0 b3 7d 25 ca 3d e 3a 8d fe 40 a2 73 a6 9d 27 19 aa 24 f7 b1 82 89 e5 40 ea 73 a7 df 23 bd 17 fb 31
  //   b7 73 96 1b 63 9e 85 2f ba 5e b0 3c e5 9d 56 d8 85 a9 48 99 ed 75 2a 5c 63 d7 b7 82 64 c9 fb 2f de
  //   a9 97 8b 75 7a 2 2 c0 22 c3 84 8a ac b9 c6 13 84 54 81 4d be da af 20 50 a4 d2 a8 54 60 2e 73 49 4e
  //   b c4 50 83 f5 d4 70 2a fd c d3 c0 f6 4e 8 55 b9 2b 40 ce 63 2a 92 26 93 8 39 a9 ae f4 d1 39 1c d0 9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
endmodule

module Latch_8bit_3_State (
  input  [7:0] D,
  input  LEB,
  input  OEB,
  output [7:0] T,
  output [7:0] Q
);

  wire not_1_out, not_2_out, pull_resistor_1_node;

  Pull_Resistor #(.pull(1)) pull_resistor_1 (.node(pull_resistor_1_node));
  not not_1 (not_1_out, LEB);
  assign Q = not_2_out ? T : 8'bz;  // Controlled_Buffer controlled_buffer_1
  Register #(.trigger("high")) register_1 (.D(D), .en(pull_resistor_1_node), .Q(T), .clk(not_1_out));  // open: clr
  not not_2 (not_2_out, OEB);
endmodule

module Transceiver_8bit (
  input  [7:0] D,
  input  OEB,
  output [7:0] Q
);

  wire not_1_out;

  assign Q = not_1_out ? D : 8'bz;  // Controlled_Buffer controlled_buffer_1
  not not_1 (not_1_out, OEB);
endmodule

module MPU_INT_Emulation (
  input  PHI2,
  input  IRQB,
  input  NMIB,
  output [7:0] IC,
  output [7:0] DATA,
  output BUSY,
  output R_WB,
  output [15:0] ADDR,
  output DA,
  output PA,
  output VPB
);

  wire and_1_out, comparator_1_eq, comparator_2_eq, counter_1_carry, not_1_out, not_2_out, not_3_out,
       not_4_out, range_test_1_out_4, range_test_2_out_4, xnor_1_out;
  wire [7:0] counter_2_q, undriven;
  wire [15:0] adder_1_out, controlled_buffer_1_out, controlled_buffer_4_out;

  not not_1 (not_1_out, IRQB);
  and and_1 (and_1_out, not_1_out, NMIB);
  not not_2 (not_2_out, NMIB);
  assign controlled_buffer_1_out = not_2_out ? 16'hffea : 16'bz;  // Controlled_Buffer controlled_buffer_1
  assign controlled_buffer_1_out = and_1_out ? 16'hffee : 16'bz;  // Controlled_Buffer controlled_buffer_2
  assign controlled_buffer_1_out = xnor_1_out ? 16'hffcc : 16'bz;  // Controlled_Buffer controlled_buffer_3
  xnor xnor_1 (xnor_1_out, not_2_out, and_1_out);
  Counter #(.max('h7), .width(3)) counter_1 (
    .Q(IC[2:0]), .carry(counter_1_carry), .clk(PHI2));  // open: load, D, count, up, clr
  Counter counter_2 (.Q(counter_2_q), .clk(PHI2), .clr(counter_1_carry));  // open: load, D, count, carry, up
  assign controlled_buffer_4_out = comparator_1_eq ? {16{1'b0}} : 16'bz;  // Controlled_Buffer controlled_buffer_4
  Comparator #(.mode("unsigned"), .width(3)) comparator_1 (
    .a(IC[2:0]), .b(3'b101), .eq(comparator_1_eq));  // open: gt, lt
  not not_3 (not_3_out, comparator_1_eq);
  assign controlled_buffer_4_out = not_3_out ? 16'h1 : 16'bz;  // Controlled_Buffer controlled_buffer_5
  Random Write_Data ();  // open: clk, next, out, clr
  not not_4 (not_4_out, R_WB);
  Counter #(.max('h1), .width(1)) counter_3 (.Q(R_WB), .clk(counter_1_carry));  // open: load, D, count, carry, up, clr
  Range_Test range_test_1 (.out_4(range_test_1_out_4), .MIN(3'b010), .D(IC[2:0]), .MAX(3'b100));
  Comparator #(.mode("unsigned"), .width(3)) comparator_2 (
    .a(IC[2:0]), .b(3'b111), .eq(comparator_2_eq));  // open: gt, lt
  Range_Test range_test_2 (.out_4(range_test_2_out_4), .MIN(3'b000), .D(IC[2:0]), .MAX(3'b001));
  Range_Test range_test_3 (.out_4(PA), .MIN(3'b101), .D(IC[2:0]), .MAX(3'b110));
  Adder #(.width(16)) adder_1 (
    .a(controlled_buffer_1_out), .b(controlled_buffer_4_out), .out(adder_1_out));  // open: cin, cout
  assign DATA = not_4_out ? undriven : 8'bz;  // Controlled_Buffer controlled_buffer_6
  assign ADDR = DA ? {8'h1, counter_2_q} : 16'bz;  // Controlled_Buffer controlled_buffer_7
  or or_1 (DA, range_test_1_out_4, comparator_2_eq);
  assign ADDR = range_test_2_out_4 ? 16'hcece : 16'bz;  // Controlled_Buffer controlled_buffer_8
  assign ADDR = PA ? adder_1_out : 16'bz;  // Controlled_Buffer controlled_buffer_9
  // Probe on adder_1_out
  Pull_Resistor pull_resistor_1 (.node(BUSY));
  not not_5 (BUSY, counter_1_carry);
  not not_6 (VPB, PA);

  assign IC[7:3] = {5{1'b0}};

  // Notes on the sheet:
  //   DA
  //   None
  //   PA
endmodule

module MPU_PRG_Emulation (
  input  PHI2,
  output [7:0] IC,
  output [7:0] DATA,
  output BUSY,
  output R_WB,
  output [15:0] ADDR,
  output PA,
  output DA
);

  wire comparator_1_eq, comparator_2_eq, counter_1_carry, counter_2_carry, not_1_out, not_2_out, not_3_out,
       or_1_out, range_test_2_out_4;
  wire [7:0] undriven_2;
  wire [15:0] adder_1_out, controlled_buffer_1_out, controlled_buffer_3_out, counter_4_q, undriven;

  Counter #(.max('h7), .width(3)) counter_1 (
    .Q(IC[2:0]), .carry(counter_1_carry), .clk(PHI2));  // open: load, D, count, up, clr
  Counter #(.max('h3), .width(2)) counter_2 (.carry(counter_2_carry), .clk(DA));  // open: load, D, count, Q, up, clr
  // Random #(.width(16)) Address: pin names not known; wires that end beside it: counter_1_carry, counter_2_carry
  Comparator #(.mode("unsigned"), .width(3)) comparator_1 (
    .a(IC[2:0]), .b(3'b111), .eq(comparator_1_eq));  // open: gt, lt
  Random Write_Data ();  // open: clk, next, out, clr
  Range_Test range_test_1 (.out_4(PA), .MIN(3'b000), .D(IC[2:0]), .MAX(3'b001));
  or or_1 (or_1_out, counter_1_carry, comparator_2_eq);
  Comparator #(.mode("unsigned"), .width(3)) comparator_2 (
    .a(IC[2:0]), .b(3'b001), .eq(comparator_2_eq));  // open: gt, lt
  Range_Test range_test_2 (.out_4(range_test_2_out_4), .MIN(3'b010), .D(IC[2:0]), .MAX(3'b011));
  assign controlled_buffer_1_out = not_1_out ? undriven : 16'bz;  // Controlled_Buffer controlled_buffer_1
  not not_1 (not_1_out, counter_2_carry);
  assign controlled_buffer_1_out = counter_2_carry ? 16'hfe80 : 16'bz;  // Controlled_Buffer controlled_buffer_2
  assign controlled_buffer_3_out = comparator_1_eq ? {16{1'b0}} : 16'bz;  // Controlled_Buffer controlled_buffer_3
  not not_2 (not_2_out, comparator_1_eq);
  assign controlled_buffer_3_out = not_2_out ? 16'h1 : 16'bz;  // Controlled_Buffer controlled_buffer_4
  assign DATA = not_3_out ? undriven_2 : 8'bz;  // Controlled_Buffer controlled_buffer_5
  not not_3 (not_3_out, R_WB);
  Counter #(.max('h1), .width(1)) counter_3 (.Q(R_WB), .clk(counter_1_carry));  // open: load, D, count, carry, up, clr
  Counter #(.max('hffff), .width(16)) counter_4 (
    .Q(counter_4_q), .clk(or_1_out));  // open: load, D, count, carry, up, clr
  Range_Test range_test_3 (.out_4(DA), .MIN(3'b100), .D(IC[2:0]), .MAX(3'b111));
  Adder #(.width(16)) adder_1 (
    .a(controlled_buffer_1_out), .b(controlled_buffer_3_out), .out(adder_1_out));  // open: cin, cout
  not not_4 (BUSY, counter_1_carry);
  assign ADDR = PA ? counter_4_q : 16'bz;  // Controlled_Buffer controlled_buffer_6
  assign ADDR = range_test_2_out_4 ? 16'hcece : 16'bz;  // Controlled_Buffer controlled_buffer_7
  assign ADDR = DA ? adder_1_out : 16'bz;  // Controlled_Buffer controlled_buffer_8

  assign IC[7:3] = {5{1'b0}};

  // Notes on the sheet:
  //   DATA: pull=up
  //   PA
  //   None
  //   DA
endmodule

module Range_Test (
  input  [2:0] MIN,
  input  [2:0] D,
  input  [2:0] MAX,
  output out_4
);

  wire comparator_1_eq, comparator_1_gt, comparator_2_eq, comparator_2_lt, or_1_out, or_2_out;

  Comparator #(.mode("unsigned"), .width(3)) comparator_1 (
    .a(D), .b(MIN), .gt(comparator_1_gt), .eq(comparator_1_eq));  // open: lt
  Comparator #(.mode("unsigned"), .width(3)) comparator_2 (
    .a(D), .b(MAX), .eq(comparator_2_eq), .lt(comparator_2_lt));  // open: gt
  or or_1 (or_1_out, comparator_1_gt, comparator_1_eq);
  or or_2 (or_2_out, comparator_2_eq, comparator_2_lt);
  and and_1 (out_4, or_1_out, or_2_out);
endmodule
