// Logisim project 658_CPU_Evolution2.circ as structural Verilog: 1 circuit, main circuit main
module main (
  input  INT0,
  input  INT1,
  input  INT2,
  input  INT3,
  input  INT4,
  input  INT5,
  input  INT6,
  input  INT7
);

  wire A_128K_B, and_2_out, and_3_out, and_7_out, BA0_3_LOW, BA4_7_LOW, clock_2_out, DEVICE, ds1813_1_p2,
       IRAM_A17, IRQ_B, IRQ_V, lvc4245_5_p1, NMI_B, not_1_out, not_2_out, not_3_out, not_4_out, not_5_out,
       not_6_out, not_7_out, not_8_out, not_9_out, not_10_out, not_11_out, not_12_out, not_13_out,
       not_14_out, not_15_out, not_17_out, or_1_out, or_2_out, PHI2, pull_resistor_1_node,
       pull_resistor_3_node, pull_resistor_4_node, pull_resistor_5_node, pull_resistor_6_node,
       pull_resistor_9_node, RWB, VA_B, VDA, VP_B, VPA, wdc65816_1_p7, wdc65816_1_p12;
  wire [2:0] priority_encoder_1_out;
  wire [3:0] A0_3;
  wire [7:0] A8_15, BA0_7, D, IRAM_A0_7, IRAM_A8_16;
  wire [7:1] lvc4245_4_p4;
  wire [7:4] A0_7;
  wire [7:7] pull_resistor_8_node;

  Clock clock_1 (.out(PHI2));
  Clock clock_2 (.out(clock_2_out));
  // DS1813 ds1813_1: pin names not known; wires that end beside it: clock_2_out, ds1813_1_p2
  not not_1 (not_1_out, VDA);
  not not_2 (not_2_out, VPA);
  Pull_Resistor #(.pull(1)) pull_resistor_1 (.node(pull_resistor_1_node));
  and and_1 (VA_B, not_1_out, not_2_out);
  not not_3 (not_3_out, BA0_7[0]);
  not not_4 (not_4_out, BA0_7[1]);
  not not_5 (not_5_out, BA0_7[2]);
  not not_6 (not_6_out, BA0_7[3]);
  not not_7 (not_7_out, BA0_7[4]);
  not not_8 (not_8_out, BA0_7[5]);
  not not_9 (not_9_out, BA0_7[6]);
  not not_10 (not_10_out, BA0_7[7]);
  not not_11 (not_11_out, A8_15[3]);
  and and_2 (and_2_out, A8_15[4], A8_15[5], A8_15[6], A8_15[7]);
  // WDC65816 wdc65816_1: pin names not known; wires that end beside it: pull_resistor_1_node, IRQ_B, NMI_B, ds1813_1_p2, PHI2, {A8_15, A0_7, A0_3}, wdc65816_1_p7, RWB, VDA, VPA, VP_B, wdc65816_1_p12
  and and_3 (and_3_out, not_4_out, not_5_out, not_6_out);
  and and_4 (BA0_3_LOW, not_3_out, not_4_out, not_5_out, not_6_out);
  and and_5 (BA4_7_LOW, not_7_out, not_8_out, not_9_out, not_10_out);
  and and_6 (DEVICE, not_11_out, and_2_out, BA0_3_LOW, BA4_7_LOW);
  nand nand_1 (A_128K_B, and_3_out, BA4_7_LOW);
  Pull_Resistor #(.pull(1)) pull_resistor_2 (.node(wdc65816_1_p12));
  // Probe on {A8_15, A0_7, A0_3}
  // Probe on wdc65816_1_p7
  or or_1 (or_1_out, VA_B, DEVICE, A_128K_B, IRQ_V);
  or or_2 (or_2_out, DEVICE, A_128K_B, VA_B);
  Pull_Resistor pull_resistor_3 (.node(pull_resistor_3_node));
  Pull_Resistor pull_resistor_4 (.node(pull_resistor_4_node));
  Pull_Resistor pull_resistor_5 (.node(pull_resistor_5_node));
  Pull_Resistor pull_resistor_6 (.node(pull_resistor_6_node));
  not not_12 (not_12_out, PHI2);
  not not_13 (not_13_out, PHI2);
  // LVC573 lvc573_1: pin names not known; wires that end beside it: pull_resistor_6_node, wdc65816_1_p7, not_12_out, BA0_7
  // LVC4245 lvc4245_1: pin names not known; wires that end beside it: not_13_out, wdc65816_1_p7, RWB, D
  // LVC4245 lvc4245_2: pin names not known; wires that end beside it: or_1_out, {A0_7, A0_3}, pull_resistor_3_node, IRAM_A0_7
  // LVC4245 lvc4245_3: pin names not known; wires that end beside it: or_2_out, A8_15, pull_resistor_4_node, IRAM_A8_16
  // LVC4245 lvc4245_4: pin names not known; wires that end beside it: or_2_out, BA0_7, pull_resistor_5_node, {lvc4245_4_p4, IRAM_A17}
  // Probe on BA0_7
  // Probe on D
  Pull_Resistor #(.pull(1)) pull_resistor_7 (.node(NMI_B));
  // Probe on {IRAM_A17, IRAM_A8_16, IRAM_A0_7}
  and and_7 (and_7_out, A0_3[1], A0_3[2], A0_3[3], not_14_out);
  not not_14 (not_14_out, VP_B);
  RAM #(.addrWidth(17), .databus("bidir"), .enables("line"), .trigger("high"), .\type ("nonvolatile")) ram_1 (
    .addr({IRAM_A17, IRAM_A8_16, IRAM_A0_7}), .data(D));  // open: we, oe, clk
  not not_15 (not_15_out, RWB);
  Pull_Resistor pull_resistor_8 (.node(pull_resistor_8_node[7]));
  and and_8 (IRQ_V, and_7_out, lvc4245_5_p1);
  not not_16 (IRQ_B, lvc4245_5_p1);
  Priority_Encoder priority_encoder_1 (
    .in0(INT0), .in1(INT1), .in2(INT2), .in3(INT3), .in4(INT4), .in5(INT5), .in6(INT6), .in7(INT7),
    .out(priority_encoder_1_out));  // open: en_in
  not not_17 (not_17_out, IRQ_V);
  Pull_Resistor pull_resistor_9 (.node(pull_resistor_9_node));
  // LVC4245 lvc4245_5: pin names not known; wires that end beside it: lvc4245_5_p1, not_17_out, {{4{pull_resistor_8_node[7]}}, priority_encoder_1_out, A0_3[0]}, pull_resistor_9_node, IRAM_A0_7
  // Probe on D

  // Other names for the same wires on the sheet: A0_7[3:0] = A0_3; A4_7[3:0] = A0_7

  // Notes on the sheet:
  //   Valid Address
  //   Bank Decode
  //   Device Decode
endmodule
