// Logisim project 658_Test.circ as structural Verilog: 2 circuits, main circuit main
module main (
);

  wire clock_1_out, microprocessor_w65c816_1_p3, microprocessor_w65c816_1_p4, not_1_out, not_2_out,
       pull_resistor_7_node;
  wire [7:0] n8_bit_bus_transceiver_lvc4245_1_p4, n8_bit_latch_lvc573_1_p3;
  wire [15:0] microprocessor_w65c816_1_p2;

  Clock clock_1 (.out(clock_1_out));
  Pull_Resistor #(.pull(1)) pull_resistor_1 ();  // open: node
  Pull_Resistor #(.pull(1)) pull_resistor_2 ();  // open: node
  Pull_Resistor #(.pull(1)) pull_resistor_3 ();  // open: node
  Pull_Resistor #(.pull(1)) pull_resistor_4 ();  // open: node
  // Microprocessor__W65C816 microprocessor_w65c816_1: pin names not known; wires that end beside it: clock_1_out, microprocessor_w65c816_1_p2, microprocessor_w65c816_1_p3, microprocessor_w65c816_1_p4
  Pull_Resistor #(.pull(1)) pull_resistor_5 ();  // open: node
  Pull_Resistor pull_resistor_6 ();  // open: node
  not not_1 (not_1_out, clock_1_out);
  // _8_bit_Latch__LVC573 8_bit_latch_lvc573_1: pin names not known; wires that end beside it: microprocessor_w65c816_1_p3, not_1_out, n8_bit_latch_lvc573_1_p3
  // _8_bit_Bus_Transceiver__LVC4245 8_bit_bus_transceiver_lvc4245_1: pin names not known; wires that end beside it: not_1_out, microprocessor_w65c816_1_p3, microprocessor_w65c816_1_p4, n8_bit_bus_transceiver_lvc4245_1_p4
  not not_2 (not_2_out, microprocessor_w65c816_1_p4);
  // Probe on {n8_bit_latch_lvc573_1_p3[2:0], microprocessor_w65c816_1_p2}
  RAM #(.trigger("high"), .addrWidth(19), .\type ("nonvolatile"), .databus("bidir"), .enables("line")) ram_1 (
    .addr({n8_bit_latch_lvc573_1_p3[2:0], microprocessor_w65c816_1_p2}),
    .data(n8_bit_bus_transceiver_lvc4245_1_p4));  // open: we, oe, clk
  SRAM_Chipifier sram_chipifier_1 (
    .CEB(pull_resistor_7_node), .OEB(not_2_out), .WEB(microprocessor_w65c816_1_p4));  // open: OE, WE, E
  Pull_Resistor pull_resistor_7 (.node(pull_resistor_7_node));
  // Probe on n8_bit_bus_transceiver_lvc4245_1_p4
endmodule

module SRAM_Chipifier (
  input  OEB,
  input  WEB,
  input  CEB,
  output OE,
  output WE,
  output E
);

  nor nor_1 (OE, OEB, CEB);
  nor nor_2 (WE, WEB, CEB);
  Pull_Resistor #(.pull(1)) pull_resistor_1 (.node(E));
endmodule
