// Logisim project Address Decode.circ as structural Verilog: 11 circuits, main circuit CPU Board
module CPU_Board (
  input  in_1,
  input  in_2,
  input  in_3,
  input  in_4,
  input  in_5,
  input  in_6,
  input  in_7,
  input  in_8,
  input  in_9,
  input  in_10,
  input  in_11,
  input  in_12,
  input  in_13,
  input  in_14,
  input  in_15,
  input  in_16
);

  wire and_1_out, and_2_out, and_3_out, interrupt_decode_1_int, interrupt_latch_1_irqb,
       interrupt_latch_1_nmib, interrupt_select_1_irq, interrupt_select_1_nmi, not_1_out, not_2_out,
       or_1_out, PHI2, pull_resistor_1_node, undriven, w65c816s_1_da, w65c816s_1_pa, w65c816s_1_r_wb,
       w65c816s_1_vpb;
  wire [3:0] interrupt_decode_1_int_addr0;
  wire [6:0] interrupt_latch_1_lint_addr1;
  wire [7:0] controlled_buffer_1_out, controlled_buffer_2_out, multiplexer_1_out, pull_resistor_2_node,
       ram_1_data, ram_2_data, w65c816s_1_addr0, w65c816s_1_addr8, w65c816s_1_addr16, w65c816s_1_data7__w,
       w65c816s_1_ic;

  Clock u_PHI2 (.out(PHI2));
  Pull_Resistor pull_resistor_1 (.node(pull_resistor_1_node));
  Pull_Resistor pull_resistor_2 (.node(pull_resistor_2_node));
  Interrupt_Select interrupt_select_1 (
    .INT_ADDR0(interrupt_decode_1_int_addr0[0]), .INT_ADDR1(interrupt_decode_1_int_addr0[1]),
    .INT_ADDR2(interrupt_decode_1_int_addr0[2]), .INT_ADDR3(interrupt_decode_1_int_addr0[3]),
    .INT(interrupt_decode_1_int), .Write(pull_resistor_1_node), .D0(pull_resistor_2_node[0]),
    .D1(pull_resistor_2_node[1]), .D2(pull_resistor_2_node[2]), .D3(pull_resistor_2_node[3]),
    .D4(pull_resistor_2_node[4]), .D5(pull_resistor_2_node[5]), .D6(pull_resistor_2_node[6]),
    .D7(pull_resistor_2_node[7]), .NMI(interrupt_select_1_nmi), .IRQ(interrupt_select_1_irq));
  Interrupt_Decode interrupt_decode_1 (
    .INT0(in_1), .INT1(in_2), .INT2(in_3), .INT3(in_4), .INT4(in_5), .INT5(in_6), .INT6(in_7), .INT7(in_8),
    .INT8(in_9), .INT9(in_10), .INT10(in_11), .INT11(in_12), .INT12(in_13), .INT13(in_14), .INT14(in_15),
    .INT15(in_16), .INT_ADDR0(interrupt_decode_1_int_addr0[0]), .INT_ADDR1(interrupt_decode_1_int_addr0[1]),
    .INT_ADDR2(interrupt_decode_1_int_addr0[2]), .INT_ADDR3(interrupt_decode_1_int_addr0[3]),
    .INT(interrupt_decode_1_int));
  Interrupt_Latch interrupt_latch_1 (
    .PHI2(PHI2), .INT_ADDR0(interrupt_decode_1_int_addr0[3]), .INT_ADDR1(interrupt_decode_1_int_addr0[2]),
    .INT_ADDR2(interrupt_decode_1_int_addr0[1]), .INT_ADDR3(interrupt_decode_1_int_addr0[0]),
    .NMI(interrupt_select_1_nmi), .IRQ(interrupt_select_1_irq), .LINT_ADDR1(interrupt_latch_1_lint_addr1[0]),
    .LINT_ADDR2(interrupt_latch_1_lint_addr1[1]), .LINT_ADDR3(interrupt_latch_1_lint_addr1[2]),
    .LINT_ADDR4(interrupt_latch_1_lint_addr1[3]), .LINT_ADDR5(interrupt_latch_1_lint_addr1[4]),
    .LINT_ADDR6(interrupt_latch_1_lint_addr1[5]), .LINT_ADDR7(interrupt_latch_1_lint_addr1[6]),
    .IRQB(interrupt_latch_1_irqb), .NMIB(interrupt_latch_1_nmib), .INT(interrupt_decode_1_int));
  // Probe on {w65c816s_1_addr16, w65c816s_1_addr8, w65c816s_1_addr0}
  W65C816S w65c816s_1 (
    .PHI2(PHI2), .NMIB(interrupt_latch_1_nmib), .IRQB(interrupt_latch_1_irqb),
    .DATA0__R(controlled_buffer_1_out[7]), .DATA1__R(controlled_buffer_1_out[6]),
    .DATA2__R(controlled_buffer_1_out[5]), .DATA3__R(controlled_buffer_1_out[4]),
    .DATA4__R(controlled_buffer_1_out[3]), .DATA5__R(controlled_buffer_1_out[2]),
    .DATA6__R(controlled_buffer_1_out[1]), .DATA7__R(controlled_buffer_1_out[0]),
    .DATA0__W(w65c816s_1_data7__w[7]), .DATA1__W(w65c816s_1_data7__w[6]), .DATA2__W(w65c816s_1_data7__w[5]),
    .DATA3__W(w65c816s_1_data7__w[4]), .DATA4__W(w65c816s_1_data7__w[3]), .DATA5__W(w65c816s_1_data7__w[2]),
    .DATA6__W(w65c816s_1_data7__w[1]), .DATA7__W(w65c816s_1_data7__w[0]), .R_WB(w65c816s_1_r_wb),
    .ADDR0(w65c816s_1_addr0[0]), .ADDR1(w65c816s_1_addr0[1]), .ADDR2(w65c816s_1_addr0[2]),
    .ADDR3(w65c816s_1_addr0[3]), .ADDR4(w65c816s_1_addr0[4]), .ADDR5(w65c816s_1_addr0[5]),
    .ADDR6(w65c816s_1_addr0[6]), .ADDR7(w65c816s_1_addr0[7]), .ADDR8(w65c816s_1_addr8[0]),
    .ADDR9(w65c816s_1_addr8[1]), .ADDR10(w65c816s_1_addr8[2]), .ADDR11(w65c816s_1_addr8[3]),
    .ADDR12(w65c816s_1_addr8[4]), .ADDR13(w65c816s_1_addr8[5]), .ADDR14(w65c816s_1_addr8[6]),
    .ADDR15(w65c816s_1_addr8[7]), .ADDR16(w65c816s_1_addr16[0]), .ADDR17(w65c816s_1_addr16[1]),
    .ADDR18(w65c816s_1_addr16[2]), .ADDR19(w65c816s_1_addr16[3]), .ADDR20(w65c816s_1_addr16[4]),
    .ADDR21(w65c816s_1_addr16[5]), .ADDR22(w65c816s_1_addr16[6]), .ADDR23(w65c816s_1_addr16[7]),
    .DA(w65c816s_1_da), .PA(w65c816s_1_pa), .VPB(w65c816s_1_vpb), .IC(w65c816s_1_ic));
  // Probe on w65c816s_1_ic
  or or_1 (or_1_out, w65c816s_1_pa, w65c816s_1_da);
  Multiplexer #(.width(8)) multiplexer_1 (
    .in0({interrupt_latch_1_lint_addr1, w65c816s_1_addr0[0]}), .in1(w65c816s_1_addr0),
    .out(multiplexer_1_out), .sel(w65c816s_1_vpb));  // open: en
  assign controlled_buffer_1_out = w65c816s_1_r_wb ? controlled_buffer_2_out : 8'bz;  // Controlled_Buffer controlled_buffer_1
  not not_1 (not_1_out, w65c816s_1_r_wb);
  assign controlled_buffer_2_out = not_1_out ? w65c816s_1_data7__w : 8'bz;  // Controlled_Buffer controlled_buffer_2
  // Probe on controlled_buffer_2_out
  // Probe on {w65c816s_1_addr8, multiplexer_1_out}
  RAM #(.addrWidth(15)) ram_1 (
    .addr({w65c816s_1_addr8[6:0], multiplexer_1_out}), .data(ram_1_data), .sel(and_1_out), .clk(PHI2),
    .ld(w65c816s_1_r_wb));  // open: clr
  Bus_Transceiver bus_transceiver_1 (
    .Enable(and_1_out), .R_WB(w65c816s_1_r_wb), .in_1(ram_1_data), .out_5(ram_1_data),
    .out_6(controlled_buffer_2_out), .in_4(controlled_buffer_2_out));
  and and_1 (and_1_out, and_3_out, not_2_out);
  and and_2 (and_2_out, and_3_out, w65c816s_1_addr8[7]);
  not not_2 (not_2_out, w65c816s_1_addr8[7]);
  and and_3 (and_3_out, undriven, or_1_out);
  RAM #(.addrWidth(15)) ram_2 (
    .addr({w65c816s_1_addr8[6:0], multiplexer_1_out}), .data(ram_2_data), .sel(and_2_out), .clk(PHI2),
    .ld(w65c816s_1_r_wb));  // open: clr
  Bus_Transceiver bus_transceiver_2 (
    .Enable(and_2_out), .R_WB(w65c816s_1_r_wb), .in_1(ram_2_data), .out_5(ram_2_data),
    .out_6(controlled_buffer_2_out), .in_4(controlled_buffer_2_out));

  // Notes on the sheet:
  //   Address         Bus
  //   IRQ B
  //   N MIB
  //   W65C816
  //   D A
  //   P A
  //   VP B
  //   R WB
  //   Data  Bus
endmodule

module W65C816S (
  input  DATA0__R,
  input  DATA1__R,
  input  DATA2__R,
  input  DATA3__R,
  input  DATA4__R,
  input  DATA5__R,
  input  DATA6__R,
  input  DATA7__R,
  input  PHI2,
  input  NMIB,
  input  IRQB,
  output DATA0__W,
  output DATA1__W,
  output DATA2__W,
  output DATA3__W,
  output DATA4__W,
  output DATA5__W,
  output DATA6__W,
  output DATA7__W,
  output R_WB,
  output ADDR0,
  output ADDR1,
  output ADDR2,
  output ADDR3,
  output ADDR4,
  output ADDR5,
  output ADDR6,
  output ADDR7,
  output ADDR8,
  output ADDR9,
  output ADDR10,
  output ADDR11,
  output ADDR12,
  output ADDR13,
  output ADDR14,
  output ADDR15,
  output ADDR16,
  output ADDR17,
  output ADDR18,
  output ADDR19,
  output ADDR20,
  output ADDR21,
  output ADDR22,
  output ADDR23,
  output DA,
  output PA,
  output VPB,
  output [7:0] IC
);

  wire and_1_out, and_2_out, and_3_out, and_4_out, and_5_out, counter_1_q, d_ff_1_q,
       mpu_int_emulation_1_busy, mpu_int_emulation_1_da, mpu_int_emulation_1_pa, mpu_int_emulation_1_r_wb,
       mpu_prg_emulation_1_busy, mpu_prg_emulation_1_da, mpu_prg_emulation_1_pa, mpu_prg_emulation_1_r_wb,
       not_1_out, not_2_out, not_3_out, not_4_out, not_5_out, or_1_out, or_2_out;
  wire [7:0] adder_1_out, controlled_buffer_9_out, mpu_int_emulation_1_data, mpu_int_emulation_1_ic,
       mpu_prg_emulation_1_data, mpu_prg_emulation_1_ic;
  wire [15:0] mpu_int_emulation_1_addr, mpu_prg_emulation_1_addr;

  Counter #(.width(1), .max('h1), .trigger("falling")) counter_1 (
    .Q(counter_1_q), .clk(mpu_prg_emulation_1_busy), .clr(mpu_prg_emulation_1_busy));  // open: load, D, count, carry
  or or_1 (or_1_out, counter_1_q, mpu_prg_emulation_1_busy);
  not not_1 (not_1_out, mpu_int_emulation_1_busy);
  and and_1 (and_1_out, or_1_out, not_1_out);
  not not_2 (not_2_out, and_1_out);
  and and_2 (and_2_out, NMIB, IRQB);
  not not_3 (not_3_out, mpu_prg_emulation_1_busy);
  D_Flip_Flop #(.trigger("high")) d_ff_1 (
    .clk(not_4_out), .D(not_4_out), .Q(d_ff_1_q), .reset(mpu_int_emulation_1_busy));  // open: Qn, preset, en
  not not_4 (not_4_out, and_2_out);
  and and_3 (and_3_out, not_3_out, d_ff_1_q);
  and and_4 (and_4_out, PHI2, mpu_int_emulation_1_busy);
  and and_5 (and_5_out, PHI2, not_5_out);
  not not_5 (not_5_out, mpu_int_emulation_1_busy);
  or or_2 (or_2_out, and_3_out, and_4_out);
  LED led_1 (.in(and_1_out));
  MPU_PRG_Emulation mpu_prg_emulation_1 (
    .PHI2(and_5_out), .DATA(mpu_prg_emulation_1_data), .R_WB(mpu_prg_emulation_1_r_wb),
    .ADDR(mpu_prg_emulation_1_addr), .DA(mpu_prg_emulation_1_da), .PA(mpu_prg_emulation_1_pa),
    .BUSY(mpu_prg_emulation_1_busy), .IC(mpu_prg_emulation_1_ic));
  // Probe on mpu_prg_emulation_1_ic
  LED led_2 (.in(not_2_out));
  MPU_INT_Emulation mpu_int_emulation_1 (
    .PHI2(or_2_out), .IRQB(NMIB), .NMIB(IRQB), .DATA(mpu_int_emulation_1_data),
    .BUSY(mpu_int_emulation_1_busy), .R_WB(mpu_int_emulation_1_r_wb), .ADDR(mpu_int_emulation_1_addr),
    .DA(mpu_int_emulation_1_da), .PA(mpu_int_emulation_1_pa), .VPB(VPB), .IC(mpu_int_emulation_1_ic));
  // Probe on mpu_int_emulation_1_ic
  Adder adder_1 (.a(mpu_int_emulation_1_ic), .b(8'h10), .out(adder_1_out), .cin(and_1_out));  // open: cout
  assign {DATA7__W, DATA6__W, DATA5__W, DATA4__W, DATA3__W, DATA2__W, DATA1__W, DATA0__W} = and_1_out ? mpu_prg_emulation_1_data : 8'bz;  // Controlled_Buffer controlled_buffer_1
  assign {DATA7__W, DATA6__W, DATA5__W, DATA4__W, DATA3__W, DATA2__W, DATA1__W, DATA0__W} = not_2_out ? mpu_int_emulation_1_data : 8'bz;  // Controlled_Buffer controlled_buffer_2
  assign R_WB = and_1_out ? mpu_prg_emulation_1_r_wb : 1'bz;  // Controlled_Buffer controlled_buffer_3
  assign R_WB = not_2_out ? mpu_int_emulation_1_r_wb : 1'bz;  // Controlled_Buffer controlled_buffer_4
  assign {ADDR15, ADDR14, ADDR13, ADDR12, ADDR11, ADDR10, ADDR9, ADDR8, ADDR7, ADDR6, ADDR5, ADDR4, ADDR3, ADDR2, ADDR1, ADDR0} = and_1_out ? mpu_prg_emulation_1_addr : 16'bz;  // Controlled_Buffer controlled_buffer_5
  assign {ADDR15, ADDR14, ADDR13, ADDR12, ADDR11, ADDR10, ADDR9, ADDR8, ADDR7, ADDR6, ADDR5, ADDR4, ADDR3, ADDR2, ADDR1, ADDR0} = not_2_out ? mpu_int_emulation_1_addr : 16'bz;  // Controlled_Buffer controlled_buffer_6
  assign IC = and_1_out ? mpu_prg_emulation_1_ic : 8'bz;  // Controlled_Buffer controlled_buffer_7
  assign IC = not_2_out ? adder_1_out : 8'bz;  // Controlled_Buffer controlled_buffer_8
  assign controlled_buffer_9_out = R_WB ? {DATA7__R, DATA6__R, DATA5__R, DATA4__R, DATA3__R, DATA2__R, DATA1__R, DATA0__R} : 8'bz;  // Controlled_Buffer controlled_buffer_9
  assign DA = and_1_out ? mpu_prg_emulation_1_da : 1'bz;  // Controlled_Buffer controlled_buffer_10
  assign PA = and_1_out ? mpu_prg_emulation_1_pa : 1'bz;  // Controlled_Buffer controlled_buffer_11
  Pull_Resistor pull_resistor_1 (.node(ADDR16));
  assign DA = not_2_out ? mpu_int_emulation_1_pa : 1'bz;  // Controlled_Buffer controlled_buffer_12
  assign PA = not_2_out ? mpu_int_emulation_1_da : 1'bz;  // Controlled_Buffer controlled_buffer_13

  assign ADDR17 = ADDR16;
  assign ADDR18 = ADDR16;
  assign ADDR19 = ADDR16;
  assign ADDR20 = ADDR16;
  assign ADDR21 = ADDR16;
  assign ADDR22 = ADDR16;
  assign ADDR23 = ADDR16;
endmodule

module Interrupt_Decode (
  input  INT0,
  input  INT1,
  input  INT2,
  input  INT3,
  input  INT4,
  input  INT5,
  input  INT6,
  input  INT7,
  input  INT8,
  input  INT9,
  input  INT10,
  input  INT11,
  input  INT12,
  input  INT13,
  input  INT14,
  input  INT15,
  output INT_ADDR0,
  output INT_ADDR1,
  output INT_ADDR2,
  output INT_ADDR3,
  output INT
);

  wire and_1_out, not_1_out, pull_resistor_2_node, pull_resistor_4_node, undriven, undriven_2;
  wire [3:0] pull_resistor_1_node, pull_resistor_3_node;

  Pull_Resistor pull_resistor_1 (.node(pull_resistor_1_node[3]));
  assign {INT_ADDR3, INT_ADDR2, INT_ADDR1, INT_ADDR0} = and_1_out ? pull_resistor_1_node : 4'bz;  // Controlled_Buffer controlled_buffer_1
  and and_1 (and_1_out, undriven, not_1_out);
  not not_1 (not_1_out, undriven_2);
  // Probe on pull_resistor_1_node[2:0]
  Priority_Encoder #(.disabled(0)) priority_encoder_1 (
    .in0(INT0), .in1(INT1), .in2(INT2), .in3(INT3), .in4(INT4), .in5(INT5), .in6(INT6), .in7(INT7),
    .out(pull_resistor_1_node[2:0]), .en_in(pull_resistor_2_node));
  Pull_Resistor #(.pull(1)) pull_resistor_2 (.node(pull_resistor_2_node));
  Pull_Resistor #(.pull(1)) pull_resistor_3 (.node(pull_resistor_3_node[3]));
  // Probe on pull_resistor_3_node[2:0]
  Priority_Encoder #(.disabled(0)) priority_encoder_2 (
    .in0(INT8), .in1(INT9), .in2(INT10), .in3(INT11), .in4(INT12), .in5(INT13), .in6(INT14), .in7(INT15),
    .out(pull_resistor_3_node[2:0]), .en_in(pull_resistor_4_node));
  // Probe on {INT_ADDR3, INT_ADDR2, INT_ADDR1, INT_ADDR0}
  // Probe on {INT_ADDR3, INT_ADDR2, INT_ADDR1, INT_ADDR0}
  assign {INT_ADDR3, INT_ADDR2, INT_ADDR1, INT_ADDR0} = undriven_2 ? pull_resistor_3_node : 4'bz;  // Controlled_Buffer controlled_buffer_2
  Pull_Resistor #(.pull(1)) pull_resistor_4 (.node(pull_resistor_4_node));
  // Probe on {INT_ADDR3, INT_ADDR2, INT_ADDR1, INT_ADDR0}
  or or_1 (INT, undriven, undriven_2);
endmodule

module Interrupt_Select (
  input  INT_ADDR0,
  input  INT_ADDR1,
  input  INT_ADDR2,
  input  INT_ADDR3,
  input  INT,
  input  Write,
  input  D0,
  input  D1,
  input  D2,
  input  D3,
  input  D4,
  input  D5,
  input  D6,
  input  D7,
  output NMI,
  output IRQ
);

  wire multiplexer_1_out, not_1_out, not_2_out, not_3_out, or_1_out, or_2_out, or_3_out;
  wire [7:0] register_1_q;

  not not_1 (not_1_out, INT);
  not not_2 (not_2_out, Write);
  Register #(.trigger("high")) register_1 (
    .D({D7, D6, D5, D4, D3, D2, D1, D0}), .en(not_2_out), .Q(register_1_q), .clk(not_2_out));  // open: clr
  // Probe on {INT_ADDR2, INT_ADDR1, INT_ADDR0}
  Multiplexer #(.select(3)) multiplexer_1 (
    .in0(register_1_q[0]), .in1(register_1_q[1]), .in2(register_1_q[2]), .in3(register_1_q[3]),
    .in4(register_1_q[4]), .in5(register_1_q[5]), .in6(register_1_q[6]), .in7(register_1_q[7]),
    .out(multiplexer_1_out), .sel({INT_ADDR2, INT_ADDR1, INT_ADDR0}));  // open: en
  or or_1 (or_1_out, INT_ADDR3, multiplexer_1_out);
  or or_2 (or_2_out, not_1_out, or_1_out);
  not not_3 (not_3_out, or_1_out);
  or or_3 (or_3_out, not_3_out, not_1_out);
  not not_4 (NMI, or_2_out);
  not not_5 (IRQ, or_3_out);
endmodule

module Interrupt_Latch (
  input  PHI2,
  input  INT,
  input  INT_ADDR0,
  input  INT_ADDR1,
  input  INT_ADDR2,
  input  INT_ADDR3,
  input  NMI,
  input  IRQ,
  output LINT_ADDR1,
  output LINT_ADDR2,
  output LINT_ADDR3,
  output LINT_ADDR4,
  output LINT_ADDR5,
  output LINT_ADDR6,
  output LINT_ADDR7,
  output IRQB,
  output NMIB
);

  wire and_1_out, counter_1_q, d_ff_1_q, not_1_out, or_1_out, pull_resistor_3_node;
  wire [0:0] register_1_q;
  wire [7:0] pull_resistor_1_node;

  Pull_Resistor pull_resistor_1 (.node(pull_resistor_1_node[0]));
  Pull_Resistor pull_resistor_2 (.node(pull_resistor_1_node[7]));
  Register #(.trigger("high")) register_1 (
    .D({{3{pull_resistor_1_node[7]}}, INT_ADDR3, INT_ADDR2, INT_ADDR1, INT_ADDR0, pull_resistor_1_node[0]}),
    .Q({LINT_ADDR7, LINT_ADDR6, LINT_ADDR5, LINT_ADDR4, LINT_ADDR3, LINT_ADDR2, LINT_ADDR1, register_1_q[0]}),
    .clk(INT));  // open: en, clr
  D_Flip_Flop #(.trigger("high")) d_ff_1 (
    .clk(INT), .D(pull_resistor_3_node), .Q(d_ff_1_q), .reset(not_1_out));  // open: Qn, preset, en
  Pull_Resistor #(.pull(1)) pull_resistor_3 (.node(pull_resistor_3_node));
  D_Flip_Flop #(.trigger("high")) d_ff_2 (.clk(INT), .D(NMI), .Qn(NMIB), .reset(not_1_out));  // open: Q, preset, en
  and and_1 (and_1_out, PHI2, d_ff_1_q);
  D_Flip_Flop #(.trigger("high")) d_ff_3 (.clk(INT), .D(IRQ), .Qn(IRQB), .reset(not_1_out));  // open: Q, preset, en
  Counter #(.width(1), .max('h1)) counter_1 (.Q(counter_1_q), .clk(or_1_out));  // open: load, D, count, carry, clr
  or or_1 (or_1_out, and_1_out, INT);
  not not_1 (not_1_out, counter_1_q);

  // Notes on the sheet:
  //   Use two D Flip-flops for the counter
endmodule

module Memory_Copier (
  input  Copy_ROM,
  input  Copy_Latch,
  input  ABORT,
  input  Write,
  input  D0,
  input  D1,
  input  D2,
  input  D3,
  input  D4,
  input  D5,
  input  D6,
  input  D7
);

  wire and_1_out, Clk_out, controlled_buffer_1_out, controlled_buffer_2_out, controlled_buffer_3_out,
       counter_1_carry, counter_2_carry, d_ff_1_q, d_ff_2_q, not_1_out, not_2_out, or_1_out, or_2_out,
       or_3_out, pull_resistor_1_node, pull_resistor_2_node, pull_resistor_3_node, pull_resistor_4_node;
  wire [3:0] counter_2_q;
  wire [7:0] controlled_buffer_4_out, register_1_q, rom_1_data;
  wire [11:0] counter_1_q;

  Clock Clk (.out(Clk_out));
  assign controlled_buffer_1_out = pull_resistor_1_node ? Copy_ROM : 1'bz;  // Controlled_Buffer controlled_buffer_1
  Pull_Resistor #(.pull(1)) pull_resistor_1 (.node(pull_resistor_1_node));
  assign controlled_buffer_2_out = pull_resistor_2_node ? Copy_Latch : 1'bz;  // Controlled_Buffer controlled_buffer_2
  Pull_Resistor #(.pull(1)) pull_resistor_2 (.node(pull_resistor_2_node));
  assign controlled_buffer_3_out = pull_resistor_3_node ? ABORT : 1'bz;  // Controlled_Buffer controlled_buffer_3
  Pull_Resistor #(.pull(1)) pull_resistor_3 (.node(pull_resistor_3_node));
  not not_1 (not_1_out, Write);
  or or_1 (or_1_out, controlled_buffer_1_out, controlled_buffer_2_out, controlled_buffer_3_out, or_3_out);
  D_Flip_Flop #(.trigger("high")) d_ff_1 (
    .clk(controlled_buffer_1_out), .D(controlled_buffer_1_out), .Q(d_ff_1_q), .reset(or_3_out));  // open: Qn, preset, en
  D_Flip_Flop #(.trigger("high")) d_ff_2 (
    .clk(controlled_buffer_2_out), .D(controlled_buffer_2_out), .Q(d_ff_2_q), .reset(or_3_out));  // open: Qn, preset, en
  or or_2 (or_2_out, d_ff_1_q, d_ff_2_q);
  or or_3 (or_3_out, counter_2_carry, controlled_buffer_3_out);
  not not_2 (not_2_out, or_1_out);
  and and_1 (and_1_out, Clk_out, not_2_out, or_2_out);
  Register #(.trigger("high")) register_1 (
    .D({D7, D6, D5, D4, D3, D2, D1, D0}), .en(not_1_out), .Q(register_1_q), .clk(not_1_out));  // open: clr
  Counter #(.width(12), .max('hfff)) counter_1 (
    .Q(counter_1_q), .carry(counter_1_carry), .clk(and_1_out), .clr(or_1_out));  // open: load, D, count
  Counter #(.width(4), .max('hf)) counter_2 (
    .Q(counter_2_q), .carry(counter_2_carry), .clk(counter_1_carry), .clr(or_1_out));  // open: load, D, count
  ROM #(.addrWidth(16)) rom_1 (.addr({counter_2_q, counter_1_q}), .data(rom_1_data), .sel(d_ff_1_q));
  // Probe on {counter_2_q, counter_1_q}
  assign controlled_buffer_4_out = d_ff_1_q ? rom_1_data : 8'bz;  // Controlled_Buffer controlled_buffer_4
  assign controlled_buffer_4_out = d_ff_2_q ? register_1_q : 8'bz;  // Controlled_Buffer controlled_buffer_5
  Pull_Resistor pull_resistor_4 (.node(pull_resistor_4_node));
  // Probe on controlled_buffer_4_out
  RAM #(.addrWidth(16)) ram_1 (
    .addr({counter_2_q, counter_1_q}), .data(controlled_buffer_4_out), .clk(and_1_out),
    .ld(pull_resistor_4_node));  // open: sel, clr

  // Notes on the sheet:
  //   contents of rom_1 (hex, n*v repeats v):
  //   40 9c c3 1a 7e b9 ef f3 b6 16 c2 83 d7 11 dd f2 85 ad b6 ac 57 d0 d7 a1 18 84 1b 86 7 38 f6 14 19 fd
  //   ab 45 33 ca 94 9b 71 b9 5e 5a 63 49 4c ca 4c 9b 70 77 62 b6 f6 72 12 c4 5b 8e 3a 54 af a5 6e 97 d7
  //   d1 35 a4 ce b4 4a b5 e0 b2 dc 69 ef 33 d0 1 af e4 fb a5 eb f3 69 9d bf 57 9a 99 dc 6 c0 ea c9 3e 4
  //   c7 1d bf c0 8b c7 c c3 f3 47 ae 90 61 f3 71 a0 1c 35 a6 9d 8f c8 61 a7 87 ff b9 90 76 ff c 20 b4 1
  //   3a 52 b9 93 e6 96 65 d5 b9 e 3a bc a0 d3 9d 53 a 2e 1a f6 2b e0 9e 97 3d 5c bb fb bb 9 e9 fa a6 82
  //   c1 c3 c1 d6 41 17 d5 c9 b 8a ef 12 a7 c7 9e 9d be ca 37 c7 5e 24 12 a6 3a 3b cb 3f e7 88 83 cf 21 d9
  //   1d 4 5 8e 83 41 56 dd df df ba f e4 68 fb c2 4 db 47 26 b8 ec 71 41 bc 42 2e 2c 51 b8 5a 54 7a 9e 33
  //   bb 41 f6 9a 35 f1 b8 55 ad 5a 10 50 5f 11 9c d9 1d af af e1 8b e 92 3f 64 90 bf ed b4 59 25 49 1c 90
  //   68 56 12 a3 1f fa 20 82 15 3f 21 e0 8a 94 89 76 70 a 9b 41 af 98 b1 c0 62 58 78 38 19 c9 32 f1 17 c
  //   f4 77 92 28 e7 da f7 47 89 f0 24 f8 e9 8f ad 6c ef d5 19 ba 93 61 23 1c 22 98 fb 31 7e e2 83 3a 5b
  //   eb 93 5f 84 e4 36 e8 15 c0 ec 85 bf 79 e8 87 9 4a 50 25 8a f3 81 ba 31 f9 49 3 7e e4 2c 62 c7 81 a1
  //   1e 75 1f 53 a2 46 d2 61 bb 8a b4 9f db 67 20 d4 5a 16 f6 fb b0 24 db 84 bd b3 78 92 3 b8 b7 3b e7 3c
  //   a cc f5 9c a5 3 1a ca c0 54 e8 8b d7 25 d7 b7 ea 13 80 7d bf 2d e1 9e 1c 35 9c ae f e3 39 58 27 22
  //   61 97 b9 52 22 ff 1c 85 2f f3 ef c3 1d ed 4f 48 a8 bb 23 c2 ed bd 51 95 af 29 7 17 94 48 f4 d5 66 b8
  //   8d cd 53 a9 4a b3 2e 20 e8 2e ac 38 a5 19 a9 5e 88 c4 63 91 98 31 bb a9 20 59 77 8e f3 65 83 7d a3
  //   f6 2d 47 c9 5f 66 93 42 e6 5 18 6c 8 4 e5 6e b3 c1 9b 6f 8b 3f ae db 27 64 a8 a2 52 3a 67 7a 4c 30
  //   5b 19 7 57 ca 7c 6b a6 e 25 94 37 d2 55 10 89 59 57 22 bd b8 b6 3 da 18 83 1d a f6 91 4f dc 64 ba 2d
  //   81 47 18 3d 10 98 4e 3c c4 a4 be 59 39 4d d1 76 b4 47 33 6b 59 5d 14 44 73 ab 6a 7e b1 e2 2c 4f 64
  //   88 95 dc c4 37 68 82 29 db 27 f 53 f5 5b 7 a3 db d0 e1 61 f6 d7 48 f5 4 84 5b 2f 55 ee ee 80 f 73 c9
  //   40 6b f3 e5 e7 f6 11 b3 55 d2 76 55 c f4 f e3 71 65 4b a9 10 82 5e 65 d6 3d 82 8b 56 5a 32 82 5 b4
  //   6f e4 7f 77 fc c3 c1 65 a2 e0 6d 12 6e f3 b 28 ef e7 44 a5 7a 1c 26 1a 67 a4 64 eb 52 88 93 92 5c 1
  //   6f dd 68 c0 15 2c 60 28 48 b5 6f 8f ae c1 45 82 11 ed 57 0 9f 6b 1d bb 2b 40 53 5b 6b 85 3a bb 38 a7
  //   d6 2a d3 a8 2e ad 1c 5d 90 39 da af cb fb f7 db 74 90 c1 b2 24 4e 2b db b5 7b b d 89 91 5b 57 c4 82
  //   79 5a 8d ef 68 8a 52 70 e 71 3 d0 75 ed 53 4e c 6e fb de e4 3a f8 68 f4 aa c9 5 56 6c b3 46 89 c0 fe
  //   6e ae bc 36 b3 cc 89 6b 82 d a4 73 b9 0 1f 24 ec d6 df 9c a2 a6 dd 7a 96 ab 66 23 f7 81 5b ff a9 6d
  //   73 ba 84 93 75 85 91 3e 80 54 51 1d 45 1e f6 81 48 21 a9 a2 24 1c c3 d8 c4 94 16 e3 ac 11 22 24 2f
  //   60 61 e3 b7 d0 7d 88 2 75 96 e3 60 69 7e 65 f7 7 fd 66 0 2f e 5e 8 86 21 2d 31 b5 58 55 70 a6 cc 3b
  //   ce cb c6 6b a8 58 7 d2 f0 85 2 3 6a ce 1e 73 f1 33 f6 be b1 7a 99 e1 6b 69 cb 7f b6 e 43 1d 39 f8 ec
  //   67 f3 7c 26 6a 74 f2 4 d9 23 f6 8c 49 77 a8 fa 76 3f ee fe 7d db ae fb 21 81 16 48 8 7a d5 70 fc 63
  //   60 72 2b 6e 2f 2 68 a0 ff c7 69 12 f 9c 8 31 63 d1 83 ff 5 68 bd 51 40 59 7c f e4 d0 aa 78 86 6b 95
  //   5d be 7d 30 63 69 4f 51 42 e6 5b f2 9 59 90 71 58 ec 92 d1 a6 a f8 f8 7a a3 8d f0 b3 6d 91 28 c1 1e
  //   f6 b1 ea b4 a4 82 87 ae b6 b5 46 50 bc c9 67 e4 f9 df 0 f5 a3 fe 3a 94 27 50 92 94 63 64 1a cf eb 6b
  //   b7 60 46 7c 61 e7 2f d2 67 c9 d6 9 aa 6e 1d 66 df 82 dc d ce 36 1e 49 96 7d 63 c9 e8 51 de de 48 ec
  //   b5 c0 50 11 45 c7 ee 42 5c b3 a2 8 7e e5 c3 2f 21 a5 b8 8 f2 5b 3f a7 10 d7 ab 23 4d 8a 1e da 71 cc
  //   d5 ac 77 15 5a 3c cf 45 d0 33 9c de 2c 7e f4 45 76 8c 24 6 e 92 ea e e2 c7 b9 f0 ba a9 fa 21 6e 38
  //   47 3d 2b 37 af 41 b2 70 f7 d0 9a ed d4 6f 8a 40 32 ca 81 bd 70 ee f bc a3 8e 9a d9 d0 3f 9c 35 34 bd
  //   e0 b3 7d 25 ca 3d e 3a 8d fe 40 a2 73 a6 9d 27 19 aa 24 f7 b1 82 89 e5 40 ea 73 a7 df 23 bd 17 fb 31
  //   b7 73 96 1b 63 9e 85 2f ba 5e b0 3c e5 9d 56 d8 85 a9 48 99 ed 75 2a 5c 63 d7 b7 82 64 c9 fb 2f de
  //   a9 97 8b 75 7a 2 2 c0 22 c3 84 8a ac b9 c6 13 84 54 81 4d be da af 20 50 a4 d2 a8 54 60 2e 73 49 4e
  //   b c4 50 83 f5 d4 70 2a fd c d3 c0 f6 4e 8 55 b9 2b 40 ce 63 2a 92 26 93 8 39 a9 ae f4 d1 39 1c d0 9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
endmodule

module Device_Decode (
  input  ADDR0,
  input  ADDR1,
  input  ADDR2,
  input  ADDR3,
  input  ADDR4,
  input  ADDR5,
  input  ADDR6,
  input  ADDR7,
  input  ADDR8,
  input  ADDR9,
  input  ADDR10,
  input  ADDR11,
  input  ADDR12,
  input  ADDR13,
  input  ADDR14,
  input  ADDR15,
  input  ADDR16,
  input  ADDR17,
  input  ADDR18,
  input  ADDR19,
  input  ADDR20,
  input  ADDR21,
  input  ADDR22,
  input  ADDR23
);

  wire and_1_out, and_2_out, not_1_out, not_2_out, or_1_out, or_2_out, or_3_out, or_4_out;

  and and_1 (and_1_out, ADDR12, ADDR13, ADDR14, ADDR15);
  or or_1 (or_1_out, ADDR16, ADDR17, ADDR18);
  or or_2 (or_2_out, ADDR19, ADDR20);
  or or_3 (or_3_out, ADDR21, ADDR22, ADDR23);
  // Probe on {ADDR10, ADDR9, ADDR8, ADDR7, ADDR6, ADDR5, ADDR4}
  not not_1 (not_1_out, ADDR11);
  not not_2 (not_2_out, or_4_out);
  or or_4 (or_4_out, or_1_out, or_2_out, or_3_out);
  and and_2 (and_2_out, not_1_out, and_1_out, not_2_out);
endmodule

module MPU_INT_Emulation (
  input  PHI2,
  input  IRQB,
  input  NMIB,
  output [7:0] IC,
  output [7:0] DATA,
  output BUSY,
  output R_WB,
  output [15:0] ADDR,
  output DA,
  output PA,
  output VPB
);

  wire and_1_out, comparator_1_eq, comparator_2_eq, counter_1_carry, not_1_out, not_2_out, not_3_out,
       not_4_out, range_test_1_out_4, range_test_2_out_4, xnor_1_out;
  wire [7:0] counter_2_q, Write_Data_out;
  wire [15:0] adder_1_out, controlled_buffer_1_out, controlled_buffer_4_out;

  not not_1 (not_1_out, IRQB);
  not not_2 (not_2_out, NMIB);
  and and_1 (and_1_out, not_1_out, NMIB);
  assign controlled_buffer_1_out = not_2_out ? 16'hffea : 16'bz;  // Controlled_Buffer controlled_buffer_1
  assign controlled_buffer_1_out = and_1_out ? 16'hffee : 16'bz;  // Controlled_Buffer controlled_buffer_2
  xnor xnor_1 (xnor_1_out, not_2_out, and_1_out);
  Counter #(.width(3), .max('h7)) counter_1 (
    .Q(IC[2:0]), .carry(counter_1_carry), .clk(PHI2));  // open: load, D, count, clr
  assign controlled_buffer_1_out = xnor_1_out ? 16'hffcc : 16'bz;  // Controlled_Buffer controlled_buffer_3
  Comparator #(.width(3), .mode("unsigned")) comparator_1 (
    .a(IC[2:0]), .b(3'b101), .eq(comparator_1_eq));  // open: gt, lt
  Range_Test range_test_1 (.MIN(3'b010), .MAX(3'b100), .out_4(range_test_1_out_4), .D(IC[2:0]));
  Counter counter_2 (.Q(counter_2_q), .clk(PHI2), .clr(counter_1_carry));  // open: load, D, count, carry
  Range_Test range_test_2 (.MIN(3'b000), .MAX(3'b001), .out_4(range_test_2_out_4), .D(IC[2:0]));
  Range_Test range_test_3 (.MIN(3'b101), .MAX(3'b110), .out_4(PA), .D(IC[2:0]));
  assign controlled_buffer_4_out = comparator_1_eq ? {16{1'b0}} : 16'bz;  // Controlled_Buffer controlled_buffer_4
  not not_3 (not_3_out, comparator_1_eq);
  assign controlled_buffer_4_out = not_3_out ? 16'h1 : 16'bz;  // Controlled_Buffer controlled_buffer_5
  assign DATA = not_4_out ? Write_Data_out : 8'bz;  // Controlled_Buffer controlled_buffer_6
  Random Write_Data (.clk(not_4_out), .out(Write_Data_out));  // open: next, clr
  not not_4 (not_4_out, R_WB);
  Counter #(.width(1), .max('h1)) counter_3 (.Q(R_WB), .clk(counter_1_carry));  // open: load, D, count, carry, clr
  assign ADDR = DA ? {8'h1, counter_2_q} : 16'bz;  // Controlled_Buffer controlled_buffer_7
  or or_1 (DA, range_test_1_out_4, comparator_2_eq);
  Comparator #(.width(3), .mode("unsigned")) comparator_2 (
    .a(IC[2:0]), .b(3'b111), .eq(comparator_2_eq));  // open: gt, lt
  assign ADDR = range_test_2_out_4 ? 16'hcece : 16'bz;  // Controlled_Buffer controlled_buffer_8
  assign ADDR = PA ? adder_1_out : 16'bz;  // Controlled_Buffer controlled_buffer_9
  Adder #(.width(16)) adder_1 (
    .a(controlled_buffer_1_out), .b(controlled_buffer_4_out), .out(adder_1_out));  // open: cin, cout
  // Probe on adder_1_out
  Pull_Resistor pull_resistor_1 (.node(BUSY));
  not not_5 (BUSY, counter_1_carry);
  not not_6 (VPB, PA);
  // Probe on ADDR

  assign IC[7:3] = {5{1'b0}};

  // Notes on the sheet:
  //   DA
  //   None
  //   PA
endmodule

module MPU_PRG_Emulation (
  input  PHI2,
  output [7:0] IC,
  output [7:0] DATA,
  output BUSY,
  output R_WB,
  output [15:0] ADDR,
  output DA,
  output PA
);

  wire comparator_1_eq, comparator_2_eq, counter_1_carry, not_1_out, not_2_out, or_1_out,
       pull_resistor_1_node, range_test_2_out_4, undriven;
  wire [7:0] Write_Data_out;
  wire [15:0] adder_1_out, Address_out, controlled_buffer_1_out, counter_3_q;

  Counter #(.width(3), .max('h7)) counter_1 (
    .Q(IC[2:0]), .carry(counter_1_carry), .clk(PHI2));  // open: load, D, count, clr
  Random #(.width(16)) Address (.clk(counter_1_carry), .next(pull_resistor_1_node), .out(Address_out));  // open: clr
  Pull_Resistor #(.pull(1)) pull_resistor_1 (.node(pull_resistor_1_node));
  Comparator #(.width(3), .mode("unsigned")) comparator_1 (
    .a(IC[2:0]), .b(3'b111), .eq(comparator_1_eq));  // open: gt, lt
  Range_Test range_test_1 (.MIN(3'b000), .MAX(3'b001), .out_4(PA), .D(IC[2:0]));
  or or_1 (or_1_out, counter_1_carry, comparator_2_eq);
  Comparator #(.width(3), .mode("unsigned")) comparator_2 (
    .a(IC[2:0]), .b(3'b001), .eq(comparator_2_eq));  // open: gt, lt
  Range_Test range_test_2 (.MIN(3'b010), .MAX(3'b011), .out_4(range_test_2_out_4), .D(IC[2:0]));
  Range_Test range_test_3 (.MIN(3'b100), .MAX(3'b111), .out_4(DA), .D(IC[2:0]));
  assign controlled_buffer_1_out = comparator_1_eq ? {16{1'b0}} : 16'bz;  // Controlled_Buffer controlled_buffer_1
  not not_1 (not_1_out, comparator_1_eq);
  assign controlled_buffer_1_out = not_1_out ? 16'h1 : 16'bz;  // Controlled_Buffer controlled_buffer_2
  Random Write_Data (.clk(not_2_out), .next(undriven), .out(Write_Data_out));  // open: clr
  assign DATA = not_2_out ? Write_Data_out : 8'bz;  // Controlled_Buffer controlled_buffer_3
  not not_2 (not_2_out, R_WB);
  Counter #(.width(1), .max('h1)) counter_2 (.Q(R_WB), .clk(counter_1_carry));  // open: load, D, count, carry, clr
  assign ADDR = PA ? counter_3_q : 16'bz;  // Controlled_Buffer controlled_buffer_4
  Counter #(.width(16), .max('hffff)) counter_3 (.Q(counter_3_q), .clk(or_1_out));  // open: load, D, count, carry, clr
  assign ADDR = range_test_2_out_4 ? 16'hcece : 16'bz;  // Controlled_Buffer controlled_buffer_5
  assign ADDR = DA ? adder_1_out : 16'bz;  // Controlled_Buffer controlled_buffer_6
  Adder #(.width(16)) adder_1 (.a(Address_out), .b(controlled_buffer_1_out), .out(adder_1_out));  // open: cin, cout
  not not_3 (BUSY, counter_1_carry);
  // Probe on ADDR

  assign IC[7:3] = {5{1'b0}};

  // Notes on the sheet:
  //   PA
  //   None
  //   DA
endmodule

module Range_Test (
  input  [2:0] MIN,
  input  [2:0] D,
  input  [2:0] MAX,
  output out_4
);

  wire comparator_1_eq, comparator_1_gt, comparator_2_eq, comparator_2_lt, or_1_out, or_2_out;

  Comparator #(.width(3), .mode("unsigned")) comparator_1 (
    .a(D), .b(MIN), .gt(comparator_1_gt), .eq(comparator_1_eq));  // open: lt
  Comparator #(.width(3), .mode("unsigned")) comparator_2 (
    .a(D), .b(MAX), .eq(comparator_2_eq), .lt(comparator_2_lt));  // open: gt
  or or_1 (or_1_out, comparator_1_gt, comparator_1_eq);
  or or_2 (or_2_out, comparator_2_eq, comparator_2_lt);
  and and_1 (out_4, or_1_out, or_2_out);
endmodule

module Bus_Transceiver (
  input  [7:0] in_1,
  input  Enable,
  input  R_WB,
  input  [7:0] in_4,
  output [7:0] out_5,
  output [7:0] out_6
);

  wire and_1_out, and_2_out, not_1_out;

  and and_1 (and_1_out, Enable, R_WB);
  assign out_6 = and_1_out ? in_1 : 8'bz;  // Controlled_Buffer controlled_buffer_1
  and and_2 (and_2_out, not_1_out, Enable);
  not not_1 (not_1_out, R_WB);
  assign out_5 = and_2_out ? in_4 : 8'bz;  // Controlled_Buffer controlled_buffer_2
endmodule
