// Logisim project Clock Divider.circ as structural Verilog: 1 circuit, main circuit Clock Dividers
module Clock_Dividers (
);

  wire and_1_out, and_2_out, and_3_out, and_4_out, and_5_out, and_6_out, and_7_out, and_8_out, and_9_out,
       and_10_out, and_11_out, and_12_out, and_13_out, and_14_out, and_15_out, and_17_out, and_18_out,
       and_19_out, and_20_out, and_21_out, clock_1_out, d_ff_1_q, d_ff_2_q, d_ff_3_q, d_ff_4_q, d_ff_5_q,
       d_ff_6_q, d_ff_7_q, d_ff_8_q, d_ff_9_q, d_ff_10_q, d_ff_11_q, d_ff_12_q, d_ff_13_q, d_ff_14_qn,
       d_ff_15_q, d_ff_16_q, d_ff_17_q, d_ff_18_q, d_ff_19_q, d_ff_20_q, d_ff_21_q, d_ff_22_q, d_ff_23_q,
       d_ff_24_q, d_ff_25_qn, d_ff_26_q, d_ff_27_q, d_ff_28_q, d_ff_29_q, d_ff_30_q, d_ff_31_q, not_1_out,
       not_2_out, not_3_out, not_4_out, not_5_out, not_6_out, not_7_out, not_8_out, not_9_out, not_10_out,
       not_11_out, not_12_out, not_13_out, not_14_out, not_15_out, not_16_out, not_17_out, not_18_out,
       not_19_out, not_20_out, not_21_out, not_22_out, not_23_out, not_24_out, not_25_out, not_26_out,
       not_27_out, not_28_out, not_29_out, not_30_out, not_31_out, not_32_out, not_33_out, not_34_out,
       not_35_out, not_36_out, not_37_out, not_38_out, not_39_out, not_40_out, not_41_out, or_1_out,
       or_2_out, or_3_out, or_4_out, or_5_out, or_6_out, or_7_out, or_8_out, or_9_out, or_10_out, or_11_out,
       or_12_out, or_13_out;
  wire [3:0] counter_1_q, counter_2_q, counter_3_q;
  wire [15:0] counter_4_q, counter_5_q, counter_6_q, counter_7_q, counter_8_q, counter_9_q, counter_10_q,
       counter_11_q, counter_12_q, counter_13_q, counter_14_q, counter_15_q, counter_16_q, counter_17_q,
       divider_1_out, divider_2_out, divider_3_out, divider_4_out, divider_5_out, divider_6_out,
       divider_7_out, divider_8_out, divider_9_out, divider_10_out, divider_11_out, divider_12_out,
       divider_13_out;

  Clock clock_1 (.out(clock_1_out));
  Counter #(.width(4), .max('hf)) counter_1 (
    .Q(counter_1_q), .clk(clock_1_out), .clr(and_7_out));  // open: load, D, count, carry
  Counter #(.width(4), .max('hf)) counter_2 (
    .Q(counter_2_q), .clk(clock_1_out), .clr(and_15_out));  // open: load, D, count, carry
  Counter #(.width(4), .max('hf)) counter_3 (
    .Q(counter_3_q), .clk(clock_1_out), .clr(and_8_out));  // open: load, D, count, carry
  D_Flip_Flop d_ff_1 (.clk(clock_1_out), .D(not_1_out), .Q(d_ff_1_q));  // open: Qn, preset, en, reset
  not not_1 (not_1_out, d_ff_1_q);
  not not_2 (not_2_out, d_ff_13_q);
  and and_1 (and_1_out, not_2_out, not_3_out);
  not not_3 (not_3_out, d_ff_5_q);
  not not_4 (not_4_out, d_ff_6_q);
  and and_2 (and_2_out, not_4_out, d_ff_14_qn);
  D_Flip_Flop d_ff_2 (.clk(clock_1_out), .D(not_5_out), .Q(d_ff_2_q));  // open: Qn, preset, en, reset
  not not_5 (not_5_out, d_ff_2_q);
  or or_1 (or_1_out, d_ff_25_qn, not_6_out);
  not not_6 (not_6_out, d_ff_20_q);
  not not_7 (not_7_out, d_ff_8_q);
  and and_3 (and_3_out, not_7_out, not_8_out, d_ff_26_q);
  not not_8 (not_8_out, d_ff_21_q);
  not not_9 (not_9_out, d_ff_9_q);
  and and_4 (and_4_out, not_9_out, not_10_out);
  not not_10 (not_10_out, d_ff_27_q);
  D_Flip_Flop d_ff_3 (.clk(clock_1_out), .D(not_11_out), .Q(d_ff_3_q));  // open: Qn, preset, en, reset
  not not_11 (not_11_out, d_ff_16_q);
  not not_12 (not_12_out, counter_1_q[2]);
  not not_13 (not_13_out, counter_1_q[3]);
  not not_14 (not_14_out, d_ff_23_q);
  and and_5 (and_5_out, not_14_out, not_15_out);
  not not_15 (not_15_out, d_ff_11_q);
  not not_16 (not_16_out, d_ff_30_q);
  and and_6 (and_6_out, not_16_out, not_17_out);
  not not_17 (not_17_out, d_ff_11_q);
  D_Flip_Flop d_ff_4 (.clk(clock_1_out), .D(not_18_out), .Q(d_ff_4_q));  // open: Qn, preset, en, reset
  not not_18 (not_18_out, d_ff_4_q);
  not not_19 (not_19_out, counter_3_q[3]);
  D_Flip_Flop d_ff_5 (.clk(clock_1_out), .D(and_1_out), .Q(d_ff_5_q));  // open: Qn, preset, en, reset
  D_Flip_Flop d_ff_6 (.clk(clock_1_out), .D(and_2_out), .Q(d_ff_6_q));  // open: Qn, preset, en, reset
  not not_20 (not_20_out, d_ff_15_q);
  D_Flip_Flop d_ff_7 (.clk(clock_1_out), .D(or_1_out), .Q(d_ff_7_q));  // open: Qn, preset, en, reset
  D_Flip_Flop d_ff_8 (.clk(clock_1_out), .D(and_3_out), .Q(d_ff_8_q));  // open: Qn, preset, en, reset
  D_Flip_Flop d_ff_9 (.clk(clock_1_out), .D(and_4_out), .Q(d_ff_9_q));  // open: Qn, preset, en, reset
  not not_21 (not_21_out, d_ff_22_q);
  not not_22 (not_22_out, d_ff_9_q);
  D_Flip_Flop d_ff_10 (.clk(clock_1_out), .D(d_ff_3_q), .Q(d_ff_10_q));  // open: Qn, preset, en, reset
  and and_7 (and_7_out, counter_1_q[0], counter_1_q[1], not_12_out, not_13_out);
  D_Flip_Flop d_ff_11 (.clk(clock_1_out), .D(or_2_out), .Q(d_ff_11_q));  // open: Qn, preset, en, reset
  or or_2 (or_2_out, and_5_out, and_6_out);
  D_Flip_Flop d_ff_12 (.clk(d_ff_4_q), .D(not_23_out), .Q(d_ff_12_q));  // open: Qn, preset, en, reset
  not not_23 (not_23_out, d_ff_12_q);
  and and_8 (and_8_out, counter_3_q[0], counter_3_q[1], counter_3_q[2], not_19_out);
  D_Flip_Flop d_ff_13 (.clk(clock_1_out), .D(d_ff_5_q), .Q(d_ff_13_q));  // open: Qn, preset, en, reset
  D_Flip_Flop d_ff_14 (.clk(clock_1_out), .D(d_ff_6_q), .Qn(d_ff_14_qn));  // open: Q, preset, en, reset
  D_Flip_Flop d_ff_15 (.clk(d_ff_2_q), .D(not_20_out), .Q(d_ff_15_q));  // open: Qn, preset, en, reset
  and and_9 (and_9_out, d_ff_20_q, d_ff_25_qn);
  or or_3 (or_3_out, and_9_out, d_ff_7_q);
  not not_24 (not_24_out, d_ff_26_q);
  and and_10 (and_10_out, not_24_out, not_25_out);
  not not_25 (not_25_out, d_ff_8_q);
  and and_11 (and_11_out, d_ff_9_q, not_21_out);
  or or_4 (or_4_out, and_11_out, and_12_out);
  and and_12 (and_12_out, not_22_out, d_ff_22_q);
  D_Flip_Flop d_ff_16 (.clk(clock_1_out), .D(d_ff_10_q), .Q(d_ff_16_q));  // open: Qn, preset, en, reset
  D_Flip_Flop d_ff_17 (.clk(and_7_out), .D(not_26_out), .Q(d_ff_17_q));  // open: Qn, preset, en, reset
  not not_26 (not_26_out, d_ff_17_q);
  and and_13 (and_13_out, d_ff_11_q, not_27_out);
  not not_27 (not_27_out, d_ff_23_q);
  not not_28 (not_28_out, d_ff_11_q);
  and and_14 (and_14_out, not_28_out, d_ff_23_q);
  not not_29 (not_29_out, counter_2_q[0]);
  not not_30 (not_30_out, counter_2_q[1]);
  and and_15 (and_15_out, not_29_out, not_30_out, counter_2_q[2], not_31_out);
  not not_31 (not_31_out, counter_2_q[3]);
  and and_16 (and_15_out, counter_2_q[0], counter_2_q[1], not_32_out, not_33_out);
  not not_32 (not_32_out, counter_2_q[2]);
  not not_33 (not_33_out, counter_2_q[3]);
  not not_34 (not_34_out, d_ff_24_q);
  D_Flip_Flop d_ff_18 (.clk(and_8_out), .D(not_35_out), .Q(d_ff_18_q));  // open: Qn, preset, en, reset
  not not_35 (not_35_out, d_ff_18_q);
  not not_36 (not_36_out, clock_1_out);
  D_Flip_Flop d_ff_19 (.clk(not_36_out), .D(d_ff_13_q), .Q(d_ff_19_q));  // open: Qn, preset, en, reset
  or or_5 (or_5_out, and_17_out, d_ff_6_q);
  and and_17 (and_17_out, or_5_out, or_6_out);
  or or_6 (or_6_out, clock_1_out, d_ff_14_qn);
  D_Flip_Flop d_ff_20 (.clk(clock_1_out), .D(or_3_out), .Q(d_ff_20_q));  // open: Qn, preset, en, reset
  D_Flip_Flop d_ff_21 (.clk(clock_1_out), .D(and_10_out), .Q(d_ff_21_q));  // open: Qn, preset, en, reset
  D_Flip_Flop d_ff_22 (.clk(clock_1_out), .D(or_4_out), .Q(d_ff_22_q));  // open: Qn, preset, en, reset
  D_Flip_Flop d_ff_23 (.clk(clock_1_out), .D(or_7_out), .Q(d_ff_23_q));  // open: Qn, preset, en, reset
  or or_7 (or_7_out, and_13_out, and_14_out);
  not not_37 (not_37_out, d_ff_28_q);
  D_Flip_Flop d_ff_24 (.clk(d_ff_12_q), .D(not_34_out), .Q(d_ff_24_q));  // open: Qn, preset, en, reset
  or or_8 (or_8_out, d_ff_19_q, d_ff_13_q);
  D_Flip_Flop d_ff_25 (.clk(clock_1_out), .D(d_ff_20_q), .Qn(d_ff_25_qn));  // open: Q, preset, en, reset
  D_Flip_Flop d_ff_26 (.clk(clock_1_out), .D(d_ff_21_q), .Q(d_ff_26_q));  // open: Qn, preset, en, reset
  D_Flip_Flop d_ff_27 (.clk(clock_1_out), .D(and_18_out), .Q(d_ff_27_q));  // open: Qn, preset, en, reset
  and and_18 (and_18_out, d_ff_9_q, d_ff_22_q);
  not not_38 (not_38_out, d_ff_23_q);
  D_Flip_Flop d_ff_28 (.clk(and_15_out), .D(not_37_out), .Q(d_ff_28_q));  // open: Qn, preset, en, reset
  or or_9 (or_9_out, and_21_out, d_ff_8_q);
  or or_10 (or_10_out, clock_1_out, not_39_out);
  not not_39 (not_39_out, d_ff_21_q);
  not not_40 (not_40_out, clock_1_out);
  and and_19 (and_19_out, d_ff_11_q, d_ff_23_q);
  or or_11 (or_11_out, and_19_out, and_20_out);
  and and_20 (and_20_out, d_ff_30_q, not_38_out);
  and and_21 (and_21_out, or_9_out, or_10_out);
  D_Flip_Flop d_ff_29 (.clk(not_40_out), .D(d_ff_22_q), .Q(d_ff_29_q));  // open: Qn, preset, en, reset
  or or_12 (or_12_out, d_ff_29_q, d_ff_22_q);
  not not_41 (not_41_out, clock_1_out);
  D_Flip_Flop d_ff_30 (.clk(clock_1_out), .D(or_11_out), .Q(d_ff_30_q));  // open: Qn, preset, en, reset
  // Probe on counter_4_q
  Counter #(.width(16), .max('hffff)) counter_4 (
    .Q(counter_4_q), .clk(clock_1_out));  // open: load, D, count, carry, clr
  LED led_1 (.in(clock_1_out));
  Counter #(.width(16), .max('hffff)) counter_5 (.Q(counter_5_q), .clk(d_ff_1_q));  // open: load, D, count, carry, clr
  // Probe on counter_5_q
  LED led_2 (.in(d_ff_1_q));
  Counter #(.width(16), .max('hffff)) counter_6 (.Q(counter_6_q), .clk(or_8_out));  // open: load, D, count, carry, clr
  // Probe on counter_6_q
  LED led_3 (.in(or_8_out));
  // Probe on counter_7_q
  Counter #(.width(16), .max('hffff)) counter_7 (
    .Q(counter_7_q), .clk(and_17_out));  // open: load, D, count, carry, clr
  LED led_4 (.in(and_17_out));
  // Probe on counter_8_q
  Counter #(.width(16), .max('hffff)) counter_8 (.Q(counter_8_q), .clk(d_ff_15_q));  // open: load, D, count, carry, clr
  LED led_5 (.in(d_ff_15_q));
  // Probe on counter_9_q
  Counter #(.width(16), .max('hffff)) counter_9 (.Q(counter_9_q), .clk(d_ff_7_q));  // open: load, D, count, carry, clr
  LED led_6 (.in(d_ff_7_q));
  Counter #(.width(16), .max('hffff)) counter_10 (
    .Q(counter_10_q), .clk(and_21_out));  // open: load, D, count, carry, clr
  // Probe on counter_10_q
  LED led_7 (.in(and_21_out));
  // Probe on counter_11_q
  Counter #(.width(16), .max('hffff)) counter_11 (
    .Q(counter_11_q), .clk(or_12_out));  // open: load, D, count, carry, clr
  LED led_8 (.in(or_12_out));
  Counter #(.width(16), .max('hffff)) counter_12 (
    .Q(counter_12_q), .clk(d_ff_16_q));  // open: load, D, count, carry, clr
  // Probe on counter_12_q
  LED led_9 (.in(d_ff_16_q));
  Counter #(.width(16), .max('hffff)) counter_13 (
    .Q(counter_13_q), .clk(d_ff_17_q));  // open: load, D, count, carry, clr
  // Probe on counter_13_q
  LED led_10 (.in(d_ff_17_q));
  D_Flip_Flop d_ff_31 (.clk(not_41_out), .D(d_ff_23_q), .Q(d_ff_31_q));  // open: Qn, preset, en, reset
  // Probe on counter_14_q
  Counter #(.width(16), .max('hffff)) counter_14 (
    .Q(counter_14_q), .clk(or_13_out));  // open: load, D, count, carry, clr
  or or_13 (or_13_out, d_ff_31_q, d_ff_23_q);
  LED led_11 (.in(or_13_out));
  // Probe on counter_15_q
  Counter #(.width(16), .max('hffff)) counter_15 (
    .Q(counter_15_q), .clk(d_ff_28_q));  // open: load, D, count, carry, clr
  LED led_12 (.in(d_ff_28_q));
  // Probe on counter_16_q
  Counter #(.width(16), .max('hffff)) counter_16 (
    .Q(counter_16_q), .clk(d_ff_24_q));  // open: load, D, count, carry, clr
  LED led_13 (.in(d_ff_24_q));
  Counter #(.width(16), .max('hffff)) counter_17 (
    .Q(counter_17_q), .clk(d_ff_18_q));  // open: load, D, count, carry, clr
  // Probe on counter_17_q
  LED led_14 (.in(d_ff_18_q));
  // Probe on divider_1_out
  // Probe on divider_2_out
  // Probe on divider_3_out
  // Probe on divider_4_out
  // Probe on divider_5_out
  // Probe on divider_6_out
  // Probe on divider_7_out
  // Probe on divider_8_out
  // Probe on divider_9_out
  // Probe on divider_10_out
  // Probe on divider_11_out
  // Probe on divider_12_out
  // Probe on divider_13_out
  Divider #(.width(16)) divider_1 (.a(counter_4_q), .b(16'h2), .out(divider_1_out));  // open: upper, rem
  Divider #(.width(16)) divider_2 (.a(counter_4_q), .b(16'h3), .out(divider_2_out));  // open: upper, rem
  Divider #(.width(16)) divider_3 (.a(counter_4_q), .b(16'h3), .out(divider_3_out));  // open: upper, rem
  Divider #(.width(16)) divider_4 (.a(counter_4_q), .b(16'h4), .out(divider_4_out));  // open: upper, rem
  Divider #(.width(16)) divider_5 (.a(counter_4_q), .b(16'h5), .out(divider_5_out));  // open: upper, rem
  Divider #(.width(16)) divider_6 (.a(counter_4_q), .b(16'h5), .out(divider_6_out));  // open: upper, rem
  Divider #(.width(16)) divider_7 (.a(counter_4_q), .b(16'h5), .out(divider_7_out));  // open: upper, rem
  Divider #(.width(16)) divider_8 (.a(counter_4_q), .b(16'h6), .out(divider_8_out));  // open: upper, rem
  Divider #(.width(16)) divider_9 (.a(counter_4_q), .b(16'h6), .out(divider_9_out));  // open: upper, rem
  Divider #(.width(16)) divider_10 (.a(counter_4_q), .b(16'h7), .out(divider_10_out));  // open: upper, rem
  Divider #(.width(16)) divider_11 (.a(counter_4_q), .b(16'h6), .out(divider_11_out));  // open: upper, rem
  Divider #(.width(16)) divider_12 (.a(counter_4_q), .b(16'h8), .out(divider_12_out));  // open: upper, rem
  Divider #(.width(16)) divider_13 (.a(counter_4_q), .b(16'he), .out(divider_13_out));  // open: upper, rem

  // Notes on the sheet:
  //   Divide by 2 (50 / 50)
  //   Divide by 3 (50 / 50)
  //   Divide by 3 (50 / 50)
  //   Divide by 4 (50 / 50)
  //   Divide by 5 (60 / 40)
  //   Divide by 5 (50 / 50)
  //   Divide by 5 (50 / 50)
  //   Divide by 6 (50 / 50)
  //   Divide by 6 (50 / 50)
  //   Divide by 7 (50 / 50)
  //   Divide by 6 (50 / 50)
  //   Divide by 8 (50 / 50)
  //   Divide by 14 (50 / 50)
endmodule
