// Logisim project Counter_Reset.circ as structural Verilog: 1 circuit, main circuit main
module main (
);

  wire clock_1_out, not_1_out, pull_resistor_1_node, pull_resistor_2_node, pull_resistor_3_node,
       pull_resistor_4_node, pull_resistor_6_node;
  wire [1:0] counter_1_q;
  wire [3:0] lvc161_1_p6, pull_resistor_5_node;

  Clock clock_1 (.out(clock_1_out));
  Counter #(.max('h3), .width(2)) counter_1 (
    .Q(counter_1_q), .clk(clock_1_out));  // open: load, D, count, carry, up, clr
  Pull_Resistor pull_resistor_1 (.node(pull_resistor_1_node));
  not not_1 (not_1_out, pull_resistor_1_node);
  Pull_Resistor #(.pull(1)) pull_resistor_2 (.node(pull_resistor_2_node));
  Pull_Resistor #(.pull(1)) pull_resistor_3 (.node(pull_resistor_3_node));
  Pull_Resistor #(.pull(1)) pull_resistor_4 (.node(pull_resistor_4_node));
  // LVC161 lvc161_1: pin names not known; wires that end beside it: not_1_out, pull_resistor_2_node, counter_1_q[1], pull_resistor_3_node, pull_resistor_4_node, lvc161_1_p6, lvc161_1_p6
  Pull_Resistor pull_resistor_5 (.node(pull_resistor_5_node));
  Pull_Resistor pull_resistor_6 (.node(pull_resistor_6_node));
  // F521 f521_1: pin names not known; wires that end beside it: pull_resistor_6_node, {pull_resistor_5_node, lvc161_1_p6}, 8'ha, pull_resistor_1_node
  // Digital_Oscilloscope #(.nState(16)) digital_oscilloscope_1: pin names not known; wires that end beside it: clock_1_out, lvc161_1_p6[0], lvc161_1_p6[1], lvc161_1_p6[2], lvc161_1_p6[3]
endmodule
