// Logisim project DataEnable.circ as structural Verilog: 1 circuit, main circuit main
module main (
  input  ALWAYS_DATA,
  input  LED_ENABLE_B,
  output DATA_LED_ENABLE_B
);

  wire not_2_out, or_1_out, PHI2, PHI2_B;

  Clock clock_1 (.out(PHI2));
  not not_1 (PHI2_B, PHI2);
  or or_1 (or_1_out, ALWAYS_DATA, PHI2);
  not not_2 (not_2_out, or_1_out);
  or or_2 (DATA_LED_ENABLE_B, not_2_out, LED_ENABLE_B);
endmodule
