// Logisim project DeviceDecode.circ as structural Verilog: 1 circuit, main circuit main
module main (
  input  [23:0] in_1,
  input  in_2,
  input  in_3,
  input  in_4
);

  wire and_2_out, D32KB_B, D128KB_B, Device1_B, Device2_B, Device3_B, Device4_B, Device5_B, Device6_B,
       Device7_B, Device16_B, Device17_B, Device18_B, Device19_B, Devices_B, Main_B, NativeMode_B, nor_1_out,
       not_2_out, RAM_B, RAMCS_B, Registers_B, ROM_B, ROMCS_B;
  wire [7:4] n3_to_8_decoder_lvc138_1_p5, n3_to_8_decoder_lvc138_3_p5;

  // Probe on in_1
  nor nor_1 (nor_1_out, in_1[23], in_1[22], in_1[21]);
  not not_1 (NativeMode_B, in_4);
  and and_1 (Main_B, nor_1_out, in_2);
  // _3_to_8_Decoder__LVC138 3_to_8_decoder_lvc138_1: pin names not known; wires that end beside it: in_1[23], in_1[22], in_1[21:19], in_2, {n3_to_8_decoder_lvc138_1_p5, D128KB_B, D32KB_B, ROM_B, RAM_B}
  and and_2 (and_2_out, D32KB_B, D128KB_B);
  not not_2 (not_2_out, Registers_B);
  // _4_bit_Line_Driver__LVC125 4_bit_line_driver_lvc125_1: pin names not known; wires that end beside it: NativeMode_B, NativeMode_B, in_4, in_4, RAM_B, ROM_B, RAM_B, ROM_B, RAMCS_B, ROMCS_B, ROMCS_B, RAMCS_B
  or or_1 (Devices_B, and_2_out, not_2_out);
  // _3_to_8_Decoder__LVC138 3_to_8_decoder_lvc138_2: pin names not known; wires that end beside it: D32KB_B, in_1[18], in_1[17:15], in_3, {Device7_B, Device6_B, Device5_B, Device4_B, Device3_B, Device2_B, Device1_B, Registers_B}
  // _3_to_8_Decoder__LVC138 3_to_8_decoder_lvc138_3: pin names not known; wires that end beside it: D128KB_B, 1'b0, {1'b0, in_1[18:17]}, in_3, {n3_to_8_decoder_lvc138_3_p5, Device19_B, Device18_B, Device17_B, Device16_B}
  LED led_1 (.in(D32KB_B));
  LED led_2 (.in(D128KB_B));
  LED led_3 (.in(RAMCS_B));
  LED led_4 (.in(ROMCS_B));
  LED led_5 (.in(Registers_B));
  LED led_6 (.in(Devices_B));
  LED led_7 (.in(Main_B));

  // Other names for the same wires on the sheet: A19 = in_1[19]; A20 = in_1[20]; A21 = in_1[21]; A15 = in_1[15];
  //   A16 = in_1[16]; A17 = in_1[17]; A18 = in_1[18]; A22 = in_1[22]; A23 = in_1[23]; KernalMode = in_2;
  //   NativeMode = in_4; Reset = in_3
endmodule
