// Logisim project Memory_Copier.circ as structural Verilog: 3 circuits, main circuit Memory_Copier
module Memory_Copier (
);

  wire CLK, COUNT, LATCH_ADDRESS, LATCH_READ_B, n4_bit_up_counter_lvc163_1_p8, n4_bit_up_counter_lvc163_2_p8,
       n4_bit_up_counter_lvc163_3_p8, n4_bit_up_counter_lvc163_4_p8, n4_bit_up_counter_lvc163_5_p8,
       n4_bit_up_counter_lvc163_6_p8, n8_bit_comparator_f521_1_p4, n8_bit_comparator_f521_2_p4,
       n8_bit_latch_lvc573_1_p4, n8_bit_latch_lvc573_2_p4, not_1_out, not_2_out, not_7_out, not_8_out,
       not_9_out, or_1_out, pull_resistor_1_node, pull_resistor_2_node, pull_resistor_3_node,
       pull_resistor_4_node, pull_resistor_5_node, pull_resistor_6_node, pull_resistor_7_node,
       pull_resistor_9_node, pull_resistor_10_node, pull_resistor_11_node, pull_resistor_12_node,
       pull_resistor_13_node, pull_resistor_14_node, pull_resistor_15_node, pull_resistor_16_node,
       pull_resistor_17_node, READ_B, SKIP_WRITE_1, SKIP_WRITE_2, WRITE_B1, WRITE_B2;
  wire [3:0] n4_bit_up_counter_lvc163_1_p7, n4_bit_up_counter_lvc163_2_p7, n4_bit_up_counter_lvc163_3_p7,
       n4_bit_up_counter_lvc163_4_p7, n4_bit_up_counter_lvc163_5_p7, n4_bit_up_counter_lvc163_6_p7,
       n4_bit_up_counter_lvc163_7_p7, n4_bit_up_counter_lvc163_8_p7;
  wire [5:0] channel_selector_1_selector;
  wire [7:0] n4_bit_multiplexer_lvc257_1_p4;
  wire [7:4] ram_1_data;
  wire [23:0] DESTINATION_ADDRESS;

  not not_1 (not_1_out, LATCH_ADDRESS);
  Pull_Resistor #(.pull(1)) pull_resistor_1 (.node(pull_resistor_1_node));
  or or_1 (or_1_out, WRITE_B1, WRITE_B2);
  Pull_Resistor #(.pull(1)) pull_resistor_2 (.node(pull_resistor_2_node));
  Pull_Resistor pull_resistor_3 (.node(pull_resistor_3_node));
  Single_Pulse single_pulse_1 (.RESET(COUNT), .START(LATCH_ADDRESS));
  not not_2 (not_2_out, LATCH_ADDRESS);
  Pull_Resistor #(.pull(1)) pull_resistor_4 (.node(pull_resistor_4_node));
  Pull_Resistor #(.pull(1)) pull_resistor_5 (.node(pull_resistor_5_node));
  // _4_bit_Up_Counter__LVC163 4_bit_up_counter_lvc163_1: pin names not known; wires that end beside it: pull_resistor_2_node, not_1_out, 4'b0000, CLK, pull_resistor_1_node, COUNT, n4_bit_up_counter_lvc163_1_p7, n4_bit_up_counter_lvc163_1_p8
  // Probe on DESTINATION_ADDRESS
  RAM #(.addrWidth(24), .databus("bidir"), .enables("line"), .trigger("high"), .\type ("nonvolatile")) ram_1 (
    .addr(DESTINATION_ADDRESS), .data({ram_1_data, n4_bit_multiplexer_lvc257_1_p4[3:0]}));  // open: we, oe, clk
  // NOT_Gate not_3 has open pins: in=READ_B, out=open
  // NOT_Gate not_4 has open pins: in=or_1_out, out=open
  // NOT_Gate not_5 has open pins: in=pull_resistor_3_node, out=open
  Channel_Selector channel_selector_1 (
    .START(COUNT),
    .SELECTOR({WRITE_B2, WRITE_B1, channel_selector_1_selector[5:2], LATCH_READ_B, channel_selector_1_selector[0]}));
  // _4_bit_Up_Counter__LVC163 4_bit_up_counter_lvc163_2: pin names not known; wires that end beside it: pull_resistor_4_node, not_2_out, 4'b0111, CLK, pull_resistor_5_node, COUNT, n4_bit_up_counter_lvc163_2_p7, n4_bit_up_counter_lvc163_2_p8
  Pull_Resistor #(.pull(1)) pull_resistor_6 (.node(pull_resistor_6_node));
  // _4_bit_Up_Counter__LVC163 4_bit_up_counter_lvc163_3: pin names not known; wires that end beside it: pull_resistor_6_node, not_1_out, 4'b0000, CLK, n4_bit_up_counter_lvc163_1_p8, COUNT, n4_bit_up_counter_lvc163_3_p7, n4_bit_up_counter_lvc163_3_p8
  // Probe on {ram_1_data, n4_bit_multiplexer_lvc257_1_p4[3:0]}
  and and_1 (READ_B, channel_selector_1_selector[0], LATCH_READ_B);
  not not_6 (CLK, channel_selector_1_selector[2]);
  Pull_Resistor #(.pull(1)) pull_resistor_7 (.node(pull_resistor_7_node));
  // _4_bit_Up_Counter__LVC163 4_bit_up_counter_lvc163_4: pin names not known; wires that end beside it: pull_resistor_7_node, not_2_out, 4'b1010, CLK, n4_bit_up_counter_lvc163_2_p8, COUNT, n4_bit_up_counter_lvc163_4_p7, n4_bit_up_counter_lvc163_4_p8
  Pull_Resistor pull_resistor_8 ();  // open: node
  Pull_Resistor #(.pull(1)) pull_resistor_9 (.node(pull_resistor_9_node));
  // _4_bit_Multiplexer__LVC257 4_bit_multiplexer_lvc257_1: pin names not known; wires that end beside it: 1'b0, ram_1_data, 4'b0000, n4_bit_multiplexer_lvc257_1_p4[7:4]
  Pull_Resistor #(.pull(1)) pull_resistor_10 (.node(pull_resistor_10_node));
  // _4_bit_Up_Counter__LVC163 4_bit_up_counter_lvc163_5: pin names not known; wires that end beside it: pull_resistor_9_node, not_1_out, 4'b0000, CLK, n4_bit_up_counter_lvc163_3_p8, COUNT, n4_bit_up_counter_lvc163_5_p7, n4_bit_up_counter_lvc163_5_p8
  // _4_bit_Up_Counter__LVC163 4_bit_up_counter_lvc163_6: pin names not known; wires that end beside it: pull_resistor_10_node, not_2_out, 4'b0011, CLK, n4_bit_up_counter_lvc163_4_p8, COUNT, n4_bit_up_counter_lvc163_6_p7, n4_bit_up_counter_lvc163_6_p8
  Pull_Resistor #(.pull(1)) pull_resistor_11 (.node(pull_resistor_11_node));
  Pull_Resistor pull_resistor_12 (.node(pull_resistor_12_node));
  not not_7 (not_7_out, LATCH_READ_B);
  Pull_Resistor pull_resistor_13 (.node(pull_resistor_13_node));
  not not_8 (not_8_out, LATCH_READ_B);
  Pull_Resistor #(.pull(1)) pull_resistor_14 (.node(pull_resistor_14_node));
  // _4_bit_Up_Counter__LVC163 4_bit_up_counter_lvc163_7: pin names not known; wires that end beside it: pull_resistor_11_node, not_1_out, 4'b0110, CLK, n4_bit_up_counter_lvc163_5_p8, COUNT, n4_bit_up_counter_lvc163_7_p7
  // _8_bit_Latch__LVC573 8_bit_latch_lvc573_1: pin names not known; wires that end beside it: pull_resistor_12_node, n4_bit_multiplexer_lvc257_1_p4, not_7_out, n8_bit_latch_lvc573_1_p4
  // _8_bit_Latch__LVC573 8_bit_latch_lvc573_2: pin names not known; wires that end beside it: pull_resistor_13_node, {4'b0000, n4_bit_multiplexer_lvc257_1_p4[3:0]}, not_8_out, n8_bit_latch_lvc573_2_p4
  // _8_bit_Latch__LVC573 8_bit_latch_lvc573_3: pin names not known; wires that end beside it: READ_B, 8'h1, LATCH_ADDRESS, DESTINATION_ADDRESS[23:16]
  // _8_bit_Latch__LVC573 8_bit_latch_lvc573_4: pin names not known; wires that end beside it: WRITE_B1, {8{1'b0}}, LATCH_ADDRESS, DESTINATION_ADDRESS[23:16]
  // _4_bit_Up_Counter__LVC163 4_bit_up_counter_lvc163_8: pin names not known; wires that end beside it: pull_resistor_14_node, not_2_out, 4'b1111, CLK, n4_bit_up_counter_lvc163_6_p8, COUNT, n4_bit_up_counter_lvc163_8_p7
  not not_9 (not_9_out, LATCH_READ_B);
  Pull_Resistor pull_resistor_15 (.node(pull_resistor_15_node));
  Pull_Resistor pull_resistor_16 (.node(pull_resistor_16_node));
  Pull_Resistor pull_resistor_17 (.node(pull_resistor_17_node));
  // _16_bit_Bus_Transceiver__LVC164245 16_bit_bus_transceiver_lvc164245_1: pin names not known; wires that end beside it: WRITE_B2, WRITE_B2, {n4_bit_up_counter_lvc163_7_p7, n4_bit_up_counter_lvc163_5_p7}, not_9_out, {n4_bit_up_counter_lvc163_3_p7, n4_bit_up_counter_lvc163_1_p7}, not_9_out, DESTINATION_ADDRESS[15:8], DESTINATION_ADDRESS[7:0]
  // _16_bit_Bus_Transceiver__LVC164245 16_bit_bus_transceiver_lvc164245_2: pin names not known; wires that end beside it: WRITE_B1, WRITE_B1, {n4_bit_up_counter_lvc163_7_p7, n4_bit_up_counter_lvc163_5_p7}, pull_resistor_15_node, {n4_bit_up_counter_lvc163_3_p7, n4_bit_up_counter_lvc163_1_p7}, pull_resistor_15_node, DESTINATION_ADDRESS[15:8], DESTINATION_ADDRESS[7:0]
  // _8_bit_Comparator__F521 8_bit_comparator_f521_1: pin names not known; wires that end beside it: pull_resistor_16_node, n8_bit_latch_lvc573_1_p4, {8{1'b0}}, n8_bit_comparator_f521_1_p4
  // _8_bit_Comparator__F521 8_bit_comparator_f521_2: pin names not known; wires that end beside it: pull_resistor_17_node, n8_bit_latch_lvc573_2_p4, {8{1'b0}}, n8_bit_comparator_f521_2_p4
  // _16_bit_Line_Driver__LVC16244 16_bit_line_driver_lvc16244_1: pin names not known; wires that end beside it: READ_B, READ_B, READ_B, READ_B
  and and_2 (SKIP_WRITE_1, ~n8_bit_comparator_f521_1_p4, 1'b0);  // AND_Gate
  and and_3 (SKIP_WRITE_2, ~n8_bit_comparator_f521_2_p4, 1'b0);  // AND_Gate

  // Other names for the same wires on the sheet: LATCH_WRITE_ADDRESS_B = LATCH_READ_B;
  //   SOURCE_ADDRESS[23:0] = DESTINATION_ADDRESS; DESTINATION_BANK[7:0] = DESTINATION_ADDRESS[23:16];
  //   SOURCE_BANK[7:0] = DESTINATION_ADDRESS[23:16]
endmodule

module Single_Pulse (
  output RESET,
  output START
);

  wire clock_1_out, clock_2_out, d_ff_1_q, d_ff_1_qn, d_ff_2_q, not_1_out;

  Clock clock_1 (.out(clock_1_out));
  // EconoReset__DS1813 econoreset_ds1813_1: pin names not known; wires that end beside it: clock_1_out, RESET, RESET
  Clock clock_2 (.out(clock_2_out));
  not not_1 (not_1_out, clock_2_out);
  D_Flip_Flop d_ff_1 (.clk(clock_2_out), .D(RESET), .Q(d_ff_1_q), .Qn(d_ff_1_qn));  // open: preset, reset
  D_Flip_Flop d_ff_2 (.clk(not_1_out), .D(d_ff_1_qn), .Q(d_ff_2_q));  // open: Qn, preset, reset
  and and_1 (START, d_ff_1_q, d_ff_2_q);
  // Digital_Oscilloscope digital_oscilloscope_1: pin names not known; wires that end beside it: clock_2_out, START
endmodule

module Channel_Selector (
  input  START,
  output [7:0] SELECTOR
);

  wire clock_1_out, pull_resistor_1_node, pull_resistor_2_node, pull_resistor_3_node;
  wire [3:0] n4_bit_up_counter_lvc163_1_p6;

  Clock clock_1 (.out(clock_1_out));
  Pull_Resistor #(.pull(1)) pull_resistor_1 (.node(pull_resistor_1_node));
  // _4_bit_Up_Counter__LVC163 4_bit_up_counter_lvc163_1: pin names not known; wires that end beside it: START, pull_resistor_1_node, clock_1_out, pull_resistor_1_node, START, n4_bit_up_counter_lvc163_1_p6
  Pull_Resistor pull_resistor_2 (.node(pull_resistor_2_node));
  Pull_Resistor #(.pull(1)) pull_resistor_3 (.node(pull_resistor_3_node));
  // _3_to_8_Decoder__LVC138 3_to_8_decoder_lvc138_1: pin names not known; wires that end beside it: pull_resistor_2_node, pull_resistor_2_node, n4_bit_up_counter_lvc163_1_p6[2:0], pull_resistor_3_node, SELECTOR
endmodule
