// Logisim project Memory_Latch.circ as structural Verilog: 1 circuit, main circuit main
module main (
);

  wire clock_1_out, lvc4245_1_p2, lvc4245_1_p6, not_1_out;
  wire [2:0] counter_1_q;

  Clock clock_1 (.out(clock_1_out));
  Counter #(.max('h7), .width(3)) counter_1 (
    .Q(counter_1_q), .clk(clock_1_out));  // open: load, D, count, carry, up, clr
  Random random_1 ();  // open: clk, next, out, clr
  // LVC4245 lvc4245_1: pin names not known; wires that end beside it: clock_1_out, lvc4245_1_p2, counter_1_q[2], lvc4245_1_p2, counter_1_q[2], lvc4245_1_p6
  not not_1 (not_1_out, counter_1_q[2]);
  // LVC573 lvc573_1: pin names not known; wires that end beside it: not_1_out, lvc4245_1_p6, not_1_out, lvc4245_1_p6
  // Probe on lvc4245_1_p6
endmodule
