// Logisim project NotNANDvsOR.circ as structural Verilog: 1 circuit, main circuit main
module main (
  input  in_1,
  input  in_2,
  input  in_3
);

  wire or_1_out;

  or or_1 (or_1_out, in_1, in_2, in_3);
  nand nand_1 (or_1_out, ~in_1, ~in_2, ~in_3);  // NAND_Gate
  LED led_1 (.in(or_1_out));
endmodule
