// Logisim project Random Memory.circ as structural Verilog: 1 circuit, main circuit Memory Generator
module Memory_Generator (
);

  wire clock_1_out, pull_resistor_1_node;
  wire [7:0] ram_1_data;
  wire [16:0] counter_1_q;

  Counter #(.width(17), .max('h1ffff)) counter_1 (
    .Q(counter_1_q), .clk(clock_1_out));  // open: load, D, count, carry, clr
  RAM #(.addrWidth(17), .bus("asynch")) ram_1 (
    .addr(counter_1_q), .data(ram_1_data), .ld(pull_resistor_1_node));  // open: sel, clr
  Pull_Resistor pull_resistor_1 (.node(pull_resistor_1_node));
  Random random_1 (.clk(clock_1_out), .out(ram_1_data));  // open: next, clr
  Clock clock_1 (.out(clock_1_out));
endmodule
