// Logisim project Simple_65816.circ as structural Verilog: 2 circuits, main circuit Software_Interrupts
module Software_Interrupts (
);

  wire and_1_out, and_2_out, clock_1_out, d_ff_1_q, d_ff_2_q, IRQ_B, microprocessor_w65c816_1_p7,
       microprocessor_w65c816_1_p8, microprocessor_w65c816_1_p10, microprocessor_w65c816_1_p11,
       microprocessor_w65c816_1_p12, n8_bit_comparator_f521_1_p4, n8_bit_comparator_f521_2_p4,
       n8_bit_latch_lvc573_2_p3, nand_1_out, nand_2_out, NMI_B, not_1_out, not_2_out, not_3_out, not_4_out,
       pull_resistor_1_node, pull_resistor_3_node, pull_resistor_5_node, pull_resistor_6_node, RDY, RESET,
       VPB, xor_1_out;
  wire [7:0] D;
  wire [23:0] microprocessor_w65c816_1_p6;

  Pull_Resistor #(.pull(1)) pull_resistor_1 (.node(pull_resistor_1_node));
  Clock clock_1 (.out(clock_1_out));
  // Microprocessor__W65C816 microprocessor_w65c816_1: pin names not known; wires that end beside it: pull_resistor_1_node, IRQ_B, NMI_B, RESET, clock_1_out, microprocessor_w65c816_1_p6[15:0], microprocessor_w65c816_1_p7, microprocessor_w65c816_1_p8, RDY, microprocessor_w65c816_1_p10, microprocessor_w65c816_1_p11, microprocessor_w65c816_1_p12, VPB
  // Probe on microprocessor_w65c816_1_p6[15:0]
  // Probe on microprocessor_w65c816_1_p7
  nand nand_1 (nand_1_out, microprocessor_w65c816_1_p10, microprocessor_w65c816_1_p11);
  Pull_Resistor #(.pull(1)) pull_resistor_2 (.node(microprocessor_w65c816_1_p12));
  Pull_Resistor pull_resistor_3 (.node(pull_resistor_3_node));
  not not_1 (not_1_out, clock_1_out);
  // _8_bit_Latch__LVC573 8_bit_latch_lvc573_1: pin names not known; wires that end beside it: pull_resistor_3_node, microprocessor_w65c816_1_p7, not_1_out, microprocessor_w65c816_1_p6[23:16]
  // _8_bit_Bus_Transceiver__LVC4245 8_bit_bus_transceiver_lvc4245_1: pin names not known; wires that end beside it: not_1_out, microprocessor_w65c816_1_p7, microprocessor_w65c816_1_p8, D
  not not_2 (not_2_out, nand_1_out);
  // Probe on microprocessor_w65c816_1_p6[23:16]
  D_Flip_Flop d_ff_1 (.clk(not_1_out), .D(microprocessor_w65c816_1_p6[0]), .Q(d_ff_1_q));  // open: Qn, preset, reset
  not not_3 (not_3_out, d_ff_2_q);
  D_Flip_Flop d_ff_2 (.clk(not_1_out), .D(nand_1_out), .Q(d_ff_2_q));  // open: Qn, preset, reset
  Pull_Resistor pull_resistor_4 ();  // open: node
  and and_1 (and_1_out, not_2_out, clock_1_out);
  not not_4 (not_4_out, microprocessor_w65c816_1_p8);
  xor xor_1 (xor_1_out, microprocessor_w65c816_1_p6[0], d_ff_1_q);
  // _8_bit_Latch__LVC573 8_bit_latch_lvc573_2: pin names not known; wires that end beside it: D, and_1_out, n8_bit_latch_lvc573_2_p3
  // Probe on microprocessor_w65c816_1_p6[16:0]
  RAM #(.addrWidth(17), .databus("bidir"), .enables("line"), .trigger("high"), .\type ("nonvolatile")) ram_1 (
    .addr(microprocessor_w65c816_1_p6[16:0]), .data(D));  // open: we, oe, clk
  // NOT_Gate not_5 has open pins: in=not_4_out, out=open
  // NOT_Gate not_6 has open pins: in=microprocessor_w65c816_1_p8, out=open
  // NOT_Gate not_7 has open pins: in=not_1_out, out=open
  Pull_Resistor pull_resistor_5 (.node(pull_resistor_5_node));
  Pull_Resistor pull_resistor_6 (.node(pull_resistor_6_node));
  // _8_bit_Comparator__F521 8_bit_comparator_f521_1: pin names not known; wires that end beside it: pull_resistor_5_node, n8_bit_latch_lvc573_2_p3, {8{1'b0}}, n8_bit_comparator_f521_1_p4
  // _8_bit_Comparator__F521 8_bit_comparator_f521_2: pin names not known; wires that end beside it: pull_resistor_6_node, n8_bit_latch_lvc573_2_p3, 8'h2, n8_bit_comparator_f521_2_p4
  // Probe on D
  nand nand_2 (nand_2_out, n8_bit_comparator_f521_1_p4, n8_bit_comparator_f521_2_p4);
  and and_2 (and_2_out, xor_1_out, not_3_out, nand_2_out);

  // Notes on the sheet:
  //   !PHI2
  //   !(VDA & VPA)
  //   PHI2
  //   Data Bus
  //   Address A0
  //   Holds the previous value of A0
  //   Holds 0 on the second cycleof a new instruction
  //   BRK
  //   COP
  //   A0 incremented (kinda)
  //   Second instruction cycle
  //   BRK or COP instruction exectuting second cycle
endmodule

module Hardware_Interrupts (
  input  ABORT,
  input  IRQ,
  input  NMI,
  input  RESET
);

  wire clock_1_out, clock_2_out, clock_3_out, d_ff_1_q, d_ff_2_q, econoreset_ds1813_1_p3,
       microprocessor_w65c816_1_p7, microprocessor_w65c816_1_p8, microprocessor_w65c816_1_p10,
       microprocessor_w65c816_1_p11, microprocessor_w65c816_1_p12, nand_1_out, nor_1_out, not_1_out,
       not_2_out, not_3_out, not_4_out, not_5_out, not_6_out, pull_resistor_2_node, RDY, VPB, xor_1_out;
  wire [7:0] D, microprocessor_w65c816_1_p6, microprocessor_w65c816_1_p6_2, n8_bit_latch_lvc573_1_p4;

  Clock clock_1 (.out(clock_1_out));
  not not_1 (not_1_out, ABORT);
  not not_2 (not_2_out, IRQ);
  not not_3 (not_3_out, NMI);
  not not_4 (not_4_out, RESET);
  Clock clock_2 (.out(clock_2_out));
  // EconoReset__DS1813 econoreset_ds1813_1: pin names not known; wires that end beside it: not_4_out, clock_2_out, econoreset_ds1813_1_p3
  // Microprocessor__W65C816 microprocessor_w65c816_1: pin names not known; wires that end beside it: not_1_out, not_2_out, not_3_out, econoreset_ds1813_1_p3, clock_1_out, {microprocessor_w65c816_1_p6_2, microprocessor_w65c816_1_p6}, microprocessor_w65c816_1_p7, microprocessor_w65c816_1_p8, RDY, microprocessor_w65c816_1_p10, microprocessor_w65c816_1_p11, microprocessor_w65c816_1_p12, VPB
  Pull_Resistor #(.pull(1)) pull_resistor_1 (.node(microprocessor_w65c816_1_p12));
  // Probe on {microprocessor_w65c816_1_p6_2, microprocessor_w65c816_1_p6}
  // Probe on microprocessor_w65c816_1_p7
  nand nand_1 (nand_1_out, microprocessor_w65c816_1_p10, microprocessor_w65c816_1_p11);
  not not_5 (not_5_out, clock_1_out);
  Pull_Resistor pull_resistor_2 (.node(pull_resistor_2_node));
  // _8_bit_Latch__LVC573 8_bit_latch_lvc573_1: pin names not known; wires that end beside it: pull_resistor_2_node, microprocessor_w65c816_1_p7, not_5_out, n8_bit_latch_lvc573_1_p4
  // _8_bit_Bus_Transceiver__LVC4245 8_bit_bus_transceiver_lvc4245_1: pin names not known; wires that end beside it: not_5_out, microprocessor_w65c816_1_p7, microprocessor_w65c816_1_p8, D
  // Probe on n8_bit_latch_lvc573_1_p4
  D_Flip_Flop d_ff_1 (.clk(not_5_out), .D(microprocessor_w65c816_1_p6[0]), .Q(d_ff_1_q));  // open: Qn, preset, reset
  D_Flip_Flop d_ff_2 (.clk(not_5_out), .D(nand_1_out), .Q(d_ff_2_q));  // open: Qn, preset, reset
  not not_6 (not_6_out, microprocessor_w65c816_1_p8);
  xor xor_1 (xor_1_out, microprocessor_w65c816_1_p6[0], d_ff_1_q);
  // Probe on {n8_bit_latch_lvc573_1_p4[0], microprocessor_w65c816_1_p6_2, microprocessor_w65c816_1_p6}
  RAM #(.addrWidth(17), .databus("bidir"), .enables("line"), .trigger("high"), .\type ("nonvolatile")) ram_1 (
    .addr({n8_bit_latch_lvc573_1_p4[0], microprocessor_w65c816_1_p6_2, microprocessor_w65c816_1_p6}), .data(D));  // open: we, oe, clk
  // NOT_Gate not_7 has open pins: in=not_6_out, out=open
  // NOT_Gate not_8 has open pins: in=microprocessor_w65c816_1_p8, out=open
  // NOT_Gate not_9 has open pins: in=not_5_out, out=open
  nor nor_1 (nor_1_out, xor_1_out, d_ff_2_q);
  Clock clock_3 (.out(clock_3_out));
  // Digital_Oscilloscope digital_oscilloscope_1: pin names not known; wires that end beside it: clock_3_out, nor_1_out
  // Probe on D

  // Notes on the sheet:
  //   !PHI2
  //   Address A0
  //   Holds the previous value of A0
  //   Holds 0 on the second cycleof a new instruction
endmodule
