// Logisim project TimerSwitch.circ as structural Verilog: 1 circuit, main circuit main
module main (
);

  wire and_1_out, clock_1_out, clock_2_out, d_type_flip_flop_lvc74_1_p2, econoreset_ds1813_1_p2,
       n4_bit_up_counter_lvc163_1_p4, n4_bit_up_counter_lvc163_2_p5, n4_bit_up_counter_lvc163_2_p7,
       n4_bit_up_counter_lvc163_3_p7, not_2_out;
  wire [3:0] n4_bit_up_counter_lvc163_2_p6, n4_bit_up_counter_lvc163_3_p6;
  wire [7:0] not_1_out;

  Pull_Resistor #(.pull(1)) pull_resistor_1 ();  // open: node
  Clock clock_1 (.out(clock_1_out));
  Clock clock_2 (.out(clock_2_out));
  // EconoReset__DS1813 econoreset_ds1813_1: pin names not known; wires that end beside it: clock_1_out, econoreset_ds1813_1_p2
  assign not_1_out = ~8'h3;  // NOT_Gate not_1, 8 bits wide
  and and_1 (and_1_out, econoreset_ds1813_1_p2, not_2_out);
  not not_2 (not_2_out, n4_bit_up_counter_lvc163_1_p4);
  Pull_Resistor #(.pull(1)) pull_resistor_2 ();  // open: node
  Pull_Resistor #(.pull(1)) pull_resistor_3 ();  // open: node
  Pull_Resistor #(.pull(1)) pull_resistor_4 ();  // open: node
  // _4_bit_Up_Counter__LVC163 4_bit_up_counter_lvc163_1: pin names not known; wires that end beside it: and_1_out, 4'b0110, clock_2_out, n4_bit_up_counter_lvc163_1_p4
  Pull_Resistor #(.pull(1)) pull_resistor_5 ();  // open: node
  // _4_bit_Up_Counter__LVC163 4_bit_up_counter_lvc163_2: pin names not known; wires that end beside it: econoreset_ds1813_1_p2, not_1_out[3:0], clock_2_out, n4_bit_up_counter_lvc163_1_p4, n4_bit_up_counter_lvc163_2_p5, n4_bit_up_counter_lvc163_2_p6, n4_bit_up_counter_lvc163_2_p7
  Pull_Resistor pull_resistor_6 ();  // open: node
  Pull_Resistor pull_resistor_7 ();  // open: node
  Pull_Resistor pull_resistor_8 ();  // open: node
  Pull_Resistor pull_resistor_9 ();  // open: node
  Pull_Resistor pull_resistor_10 ();  // open: node
  Pull_Resistor #(.pull(1)) pull_resistor_11 ();  // open: node
  // D_type_Flip_Flop__LVC74 d_type_flip_flop_lvc74_1: pin names not known; wires that end beside it: econoreset_ds1813_1_p2, d_type_flip_flop_lvc74_1_p2, n4_bit_up_counter_lvc163_2_p5
  Pull_Resistor #(.pull(1)) pull_resistor_12 ();  // open: node
  // _4_bit_Up_Counter__LVC163 4_bit_up_counter_lvc163_3: pin names not known; wires that end beside it: econoreset_ds1813_1_p2, not_1_out[7:4], clock_2_out, n4_bit_up_counter_lvc163_2_p7, n4_bit_up_counter_lvc163_2_p5, n4_bit_up_counter_lvc163_3_p6, n4_bit_up_counter_lvc163_3_p7
  not not_3 (d_type_flip_flop_lvc74_1_p2, n4_bit_up_counter_lvc163_3_p7);
  // Probe on {n4_bit_up_counter_lvc163_3_p6, n4_bit_up_counter_lvc163_2_p6}
endmodule
