// Logisim project demo.circ as structural Verilog: 1 circuit, main circuit main
module main (
);

  wire and_1_out, and_2_out, and_3_out, and_4_out, and_5_out, and_6_out, buffer_2_out, buffer_3_out,
       buffer_4_out, buffer_5_out, buffer_6_out, buffer_7_out, buffer_8_out, buffer_9_out, buffer_10_out,
       buffer_11_out, comparator_1_eq, demultiplexer_1_out0, demultiplexer_1_out1, demultiplexer_1_out2,
       demultiplexer_1_out3, keyboard_1_avail, NMI_out, not_1_out, not_2_out, not_3_out, not_4_out,
       not_5_out, or_1_out, or_2_out, or_3_out, or_4_out, PHI2, pull_resistor_1_node, Reset_out,
       w65c02s_simple_1_p5;
  wire [1:0] w65c02s_simple_1_p7_2;
  wire [6:0] keyboard_1_data, w65c02s_simple_1_p6;
  wire [7:0] controlled_buffer_2_out, ram_1_dout, rom_1_data;
  wire [7:7] w65c02s_simple_1_p6_2;
  wire [13:0] w65c02s_simple_1_p7;
  wire [23:0] counter_1_q;

  Clock clock_1 (.out(PHI2));
  Button NMI (.out(NMI_out));
  Button Reset (.out(Reset_out));
  Pull_Resistor #(.pull(1)) pull_resistor_1 (.node(pull_resistor_1_node));
  buf buffer_1 (pull_resistor_1_node, buffer_2_out);
  buf buffer_2 (buffer_2_out, buffer_3_out);
  buf buffer_3 (buffer_3_out, buffer_4_out);
  buf buffer_4 (buffer_4_out, buffer_5_out);
  buf buffer_5 (buffer_5_out, buffer_6_out);
  buf buffer_6 (buffer_6_out, buffer_11_out);
  TTY #(.rows(16), .trigger("falling")) tty_1 (.data(w65c02s_simple_1_p6), .clk(PHI2), .we(and_4_out), .clr(or_1_out));
  or or_1 (or_1_out, or_2_out, and_2_out);
  // Probe on counter_1_q
  Counter #(.max('hffffff), .width(24)) counter_1 (
    .Q(counter_1_q), .clk(PHI2));  // open: load, D, count, carry, up, clr
  or or_2 (or_2_out, Reset_out, pull_resistor_1_node);
  buf buffer_7 (buffer_7_out, 1'b0);
  buf buffer_8 (buffer_8_out, buffer_7_out);
  buf buffer_9 (buffer_9_out, buffer_8_out);
  buf buffer_10 (buffer_10_out, buffer_9_out);
  buf buffer_11 (buffer_11_out, buffer_10_out);
  not not_1 (not_1_out, keyboard_1_avail);
  not not_2 (not_2_out, NMI_out);
  not not_3 (not_3_out, or_2_out);
  Keyboard #(.trigger("falling")) keyboard_1 (
    .clk(PHI2), .re(and_3_out), .clr(or_3_out), .avail(keyboard_1_avail), .data(keyboard_1_data));
  // W65C02S__Simple w65c02s_simple_1: pin names not known; wires that end beside it: PHI2, not_1_out, not_2_out, not_3_out, w65c02s_simple_1_p5, {w65c02s_simple_1_p6_2[7], w65c02s_simple_1_p6}, {w65c02s_simple_1_p7_2, w65c02s_simple_1_p7}
  or or_3 (or_3_out, or_2_out, and_1_out);
  and and_1 (and_1_out, ~w65c02s_simple_1_p5, demultiplexer_1_out1, comparator_1_eq);  // AND_Gate
  and and_2 (and_2_out, ~w65c02s_simple_1_p5, demultiplexer_1_out1, w65c02s_simple_1_p6_2[7]);  // AND_Gate
  and and_3 (and_3_out, w65c02s_simple_1_p5, demultiplexer_1_out1);
  Comparator comparator_1 (
    .a({8{1'b0}}), .b({w65c02s_simple_1_p6_2[7], w65c02s_simple_1_p6}), .eq(comparator_1_eq));  // open: gt, lt
  and and_4 (and_4_out, ~w65c02s_simple_1_p5, demultiplexer_1_out1);  // AND_Gate
  not not_4 (not_4_out, w65c02s_simple_1_p5);
  Demultiplexer #(.enable("false"), .select(2)) demultiplexer_1 (
    .out0(demultiplexer_1_out0), .out1(demultiplexer_1_out1), .out2(demultiplexer_1_out2),
    .out3(demultiplexer_1_out3), .in(1'b1), .sel(w65c02s_simple_1_p7_2));
  assign {w65c02s_simple_1_p6_2[7], w65c02s_simple_1_p6} = and_3_out ? {1'b0, keyboard_1_data} : 8'bz;  // Controlled_Buffer controlled_buffer_1
  not not_5 (not_5_out, PHI2);
  assign controlled_buffer_2_out = and_5_out ? {w65c02s_simple_1_p6_2[7], w65c02s_simple_1_p6} : 8'bz;  // Controlled_Buffer controlled_buffer_2
  and and_5 (and_5_out, not_4_out, demultiplexer_1_out0);
  or or_4 (or_4_out, demultiplexer_1_out2, demultiplexer_1_out3);
  RAM #(.addrWidth(14), .enables("line")) ram_1 (
    .addr(w65c02s_simple_1_p7), .we(and_5_out), .clk(not_5_out), .din(controlled_buffer_2_out),
    .dout(ram_1_dout));
  ROM #(.addrWidth(15)) rom_1 (.addr({w65c02s_simple_1_p7_2[0], w65c02s_simple_1_p7}), .data(rom_1_data));
  // Probe on {w65c02s_simple_1_p7_2, w65c02s_simple_1_p7}
  // Probe on {w65c02s_simple_1_p6_2[7], w65c02s_simple_1_p6}
  LED Read (.in(w65c02s_simple_1_p5));
  LED Write (.in(w65c02s_simple_1_p5));
  // Digital_Oscilloscope #(.frontlines("both")) digital_oscilloscope_1: pin names not known; wires that end beside it: PHI2, w65c02s_simple_1_p6[0], w65c02s_simple_1_p6[1], w65c02s_simple_1_p6[2], w65c02s_simple_1_p6[3], w65c02s_simple_1_p6[4], w65c02s_simple_1_p6[5], w65c02s_simple_1_p6[6], w65c02s_simple_1_p6_2[7]
  and and_6 (and_6_out, w65c02s_simple_1_p5, demultiplexer_1_out0);
  assign {w65c02s_simple_1_p6_2[7], w65c02s_simple_1_p6} = and_6_out ? ram_1_dout : 8'bz;  // Controlled_Buffer controlled_buffer_3
  assign {w65c02s_simple_1_p6_2[7], w65c02s_simple_1_p6} = or_4_out ? rom_1_data : 8'bz;  // Controlled_Buffer controlled_buffer_4

  // Notes on the sheet:
  //   (automatic
  //   reset
  //   sequencer)
  //   Keyboard (type here)
  //   contents of rom_1 (hex, n*v repeats v):
  //   40 5a a0 0 b1 0 f0 6 8d 0 40 c8 80 f6 7a 60 a2 ff 9a e8 80 e a2 ff 9a 8e 0 40 e8 a0 0 a9 0 9c 0 40
  //   a9 5 85 2 a9 3 85 3 a9 a 85 4 48 a9 b4 85 0 a9 81 85 1 20 1 80 68 20 48 80 20 d3 80 20 1e 81 80 f5
  //   48 a9 d0 85 0 a9 81 85 1 20 1 80 68 a5 2 f0 5 9 30 8d 0 40 48 a9 d6 85 0 a9 81 85 1 20 1 80 68 a5 3
  //   f0 1a c9 1 f0 7 9 30 8d 0 40 80 19 48 a9 df 85 0 a9 81 85 1 20 1 80 68 80 17 a9 6e 8d 0 40 a9 6f 8d
  //   0 40 48 a9 eb 85 0 a9 81 85 1 20 1 80 68 48 a9 f5 85 0 a9 81 85 1 20 1 80 68 a5 4 f0 14 c9 a b0 7 9
  //   30 8d 0 40 80 9 a9 31 8d 0 40 3a 8d 0 40 48 a9 fd 85 0 a9 81 85 1 20 1 80 68 60 a5 2 d0 33 a5 4 d0 f
  //   48 a9 5 85 0 a9 82 85 1 20 1 80 68 80 d 48 a9 47 85 0 a9 82 85 1 20 1 80 68 48 a9 54 85 0 a9 82 85 1
  //   20 1 80 68 20 a8 81 4c 10 80 a5 4 f0 1 60 48 a9 7a 85 0 a9 82 85 1 20 1 80 68 80 e6 48 a9 c2 85 0 a9
  //   82 85 1 20 1 80 68 cb ad 0 40 c9 61 f0 17 c9 70 f0 24 c9 72 f0 2 80 ee a9 72 8d 0 40 a9 a 8d 0 40 4c
  //   10 80 48 a9 47 85 0 a9 83 85 1 20 1 80 68 c6 4 80 3d c6 3 30 29 48 a9 93 85 0 a9 83 85 1 20 1 80 68
  //   a5 2 18 69 3 c9 6 90 f 48 a9 2f 85 0 a9 83 85 1 20 1 80 68 a9 5 85 2 80 10 48 a9 6a 85 0 a9 83 85 1
  //   20 1 80 68 64 3 60 48 a9 4 85 0 a9 83 85 1 20 1 80 68 c6 2 60 9c 0 40 cb ad 0 40 c9 a d0 f8 60 a
  //   7*20 57 65 6c 63 6f 6d 65 20 74 6f 20 46 69 67 68 74 21 a a 0 59 6f 75 3a 20 0 30 2f 35 30 48 50 2c
  //   20 0 6f 6e 65 20 70 6f 74 69 6f 6e a 0 20 70 6f 74 69 6f 6e 73 a 0 45 6e 65 6d 79 3a 20 0 30 2f 31
  //   30 30 a a 0 59 6f 75 20 73 6c 65 77 20 79 6f 75 72 20 66 6f 65 2c 20 62 75 74 20 77 65 72 65 a 66 61
  //   74 61 6c 6c 79 20 77 6f 75 6e 64 65 64 20 62 79 20 68 69 73 20 66 69 6e 61 6c a 62 6c 6f 77 2e 2e 2e
  //   a 0 59 6f 75 20 64 69 65 64 2e 2e 2e a 0 47 61 6d 65 20 6f 76 65 72 2e 20 50 72 65 73 73 20 65 6e 74
  //   65 72 20 74 6f 20 74 72 79 a 61 67 61 69 6e 2e a 0 59 6f 75 72 20 66 6f 65 20 69 73 20 76 61 6e 71
  //   75 69 73 68 65 64 21 20 59 6f 75 20 61 72 65 a 76 69 63 74 6f 72 69 6f 75 73 21 a 50 72 65 73 73 20
  //   65 6e 74 65 72 20 74 6f 20 70 6c 61 79 20 61 67 61 69 6e 2e a 0 57 68 61 74 20 77 69 6c 6c 20 79 6f
  //   75 20 64 6f 3f a 61 20 3d 20 61 74 74 61 63 6b 2c 20 70 20 3d 20 64 72 69 6e 6b 20 70 6f 74 69 6f 6e
  //   2c a 72 20 3d 20 73 74 61 72 74 20 6f 76 65 72 a 3e 20 0 54 68 65 20 65 6e 65 6d 79 20 61 74 74 61
  //   63 6b 73 20 79 6f 75 2c 20 64 65 61 6c 69 6e 67 a 31 30 20 64 61 6d 61 67 65 2e a 0 53 6f 6d 65 20
  //   6f 66 20 69 74 20 77 61 73 20 77 61 73 74 65 64 21 a 0 61 a a 59 6f 75 20 61 74 74 61 63 6b 2c 20 64
  //   65 61 6c 69 6e 67 20 31 30 20 64 61 6d 61 67 65 2e a 0 70 a a 59 6f 75 20 64 6f 6e 27 74 20 68 61 76
  //   65 20 61 6e 79 20 70 6f 74 69 6f 6e 73 20 74 6f a 64 72 69 6e 6b 2e a 0 70 a a 59 6f 75 20 64 72 69
  //   6e 6b 20 61 20 70 6f 74 69 6f 6e 2c 20 68 65 61 6c 69 6e 67 a 33 30 20 48 50 2e a 31810*0 80 16 80 0
  //   80
  //   Address
  //   Data
endmodule
