// Logisim project Test.circ as structural Verilog: 1 circuit, main circuit main
module main (
);

  wire and_1_out, and_2_out, clock_1_out, clock_2_out, clock_3_out, clock_4_out, clock_5_out, clock_6_out,
       clock_7_out, clock_8_out, clock_9_out, clock_10_out, clock_11_out, clock_12_out, clock_13_out,
       clock_14_out, clock_15_out, clock_16_out, clock_17_out, clock_18_out, clock_19_out, clock_20_out,
       clock_21_out, clock_22_out, clock_23_out, clock_24_out, clock_25_out, clock_26_out, clock_27_out,
       clock_28_out, clock_29_out, clock_30_out, clock_31_out, clock_32_out, clock_34_out, clock_35_out,
       clock_36_out, clock_37_out, clock_39_out, clock_40_out, comparator_2_eq, comparator_3_eq,
       comparator_4_eq, comparator_5_eq, comparator_6_gt, comparator_7_eq, comparator_8_eq, comparator_8_gt,
       comparator_9_gt, comparator_10_gt, comparator_11_eq, comparator_12_eq, comparator_13_eq,
       comparator_14_lt, comparator_15_lt, comparator_16_eq, comparator_17_eq, counter_13_carry,
       counter_15_carry, counter_17_carry, d_type_flip_flop_lvc74_1_p1, d_type_flip_flop_lvc74_1_p9,
       d_type_flip_flop_lvc74_1_p10, decoder_1_out0, decoder_1_out1, decoder_1_out2, decoder_1_out3,
       decoder_2_out0, decoder_2_out1, decoder_2_out2, decoder_2_out3, decoder_2_out4, decoder_2_out5,
       decoder_2_out6, decoder_2_out7, decoder_3_out0, decoder_3_out1, decoder_3_out2, decoder_3_out3,
       decoder_4_out0, decoder_4_out1, decoder_4_out2, decoder_4_out3, decoder_5_out0, decoder_5_out1,
       decoder_5_out2, decoder_5_out3, decoder_5_out4, decoder_5_out5, decoder_5_out6, decoder_5_out7,
       decoder_5_out8, econoreset_ds1813_1_p3, n4_bit_full_adder_f283_1_p4, n4_bit_full_adder_f283_1_p5,
       n4_bit_line_driver_lvc125_1_p11, n4_bit_line_driver_lvc125_1_p12, n4_bit_line_driver_lvc125_1_p13,
       n4_bit_line_driver_lvc125_1_p14, n4_bit_line_driver_lvc126_1_p11, n4_bit_line_driver_lvc126_1_p12,
       n4_bit_line_driver_lvc126_1_p13, n4_bit_line_driver_lvc126_1_p14, n4_bit_multiplexer_lvc157_1_p5,
       n4_bit_multiplexer_lvc257_1_p5, n4_bit_up_counter_lvc161_1_p7, n4_bit_up_counter_lvc163_1_p8,
       n4_bit_up_counter_lvc163_1_p9, n4_bit_up_down_counter_hct193_1_p2, n4_bit_up_down_counter_hct193_1_p8,
       n4_bit_up_down_counter_hct193_1_p9, n4_bit_up_down_counter_hct193_1_p10,
       n4_bit_up_down_counter_hct193_2_p6, n4_bit_up_down_counter_hct193_2_p7,
       n4_bit_up_down_counter_hct193_2_p8, n4_to_1_multiplexer_qs3253_1_p6, n4_to_1_multiplexer_qs3253_1_p7,
       n8_bit_bi_latch_lvc543_1_p1, n8_bit_bi_latch_lvc543_1_p6, n8_bit_bi_latch_lvc543_1_p7,
       n8_bit_bi_latch_lvc543_2_p1, n8_bit_bi_latch_lvc543_2_p5, n8_bit_comparator_f521_1_p4,
       n8_bit_latch_lvc273_1_p1, n8_bit_latch_lvc273_1_p5, n8_bit_latch_lvc373_1_p2,
       n8_bit_latch_lvc373_1_p4, n8_bit_latch_lvc573_1_p2, n8_bit_latch_lvc573_1_p4,
       n8_bit_latch_lvc574_1_p2, n8_bit_latch_lvc574_1_p4, n8_bit_line_driver_lvc541_1_p1,
       n8_bit_line_driver_lvc541_1_p5, n8_bit_parallel_in_shift_lv165_1_p2,
       n8_bit_parallel_in_shift_lv165_1_p8, n8_bit_parallel_in_shift_lv165_1_p9,
       n8_bit_parallel_in_shift_lv165_1_p10, n8_bit_serial_in_shift_lvc595_1_p6,
       n8_bit_serial_in_shift_lvc595_1_p7, n8_bit_up_counter_hc590_1_p6, n8_bit_up_counter_hc590_1_p7,
       n8_to_1_multiplexer_b3251_1_p4, n8_to_1_multiplexer_f251_1_p4, n8_to_1_multiplexer_f251_1_p5,
       n8_to_3_encoder_ls148_1_p3, n8_to_3_encoder_ls148_1_p4, n8_to_3_encoder_ls148_1_p5,
       n10_to_4_encoder_hc147_1_p2, n12_bit_up_counter_hc4040_1_p3, n16_bit_latch_lvc16373_1_p3,
       n16_bit_latch_lvc16373_1_p7, n16_bit_latch_lvc16373_1_p8, n16_bit_latch_lvc162373_1_p3,
       n16_bit_latch_lvc162373_1_p7, n16_bit_latch_lvc162373_1_p8, n16_bit_line_driver_lvc16244_1_p11,
       n16_bit_line_driver_lvc16244_1_p12, n16_bit_line_driver_lvc16244_1_p13,
       n16_bit_line_driver_lvc16244_1_p14, n512_byte_fifo_idt7201_1_p2, n512_byte_fifo_idt7201_1_p8,
       n512_byte_fifo_idt7201_1_p9, n512_byte_fifo_idt7201_1_p10, n512_byte_fifo_idt7201_1_p11, not_1_out,
       not_2_out, not_3_out, not_4_out, not_5_out, not_6_out, not_15_out, not_16_out, not_17_out, not_18_out,
       not_19_out, not_20_out, not_21_out, not_22_out, not_23_out, not_24_out, not_25_out, not_26_out,
       not_27_out, not_28_out, not_29_out, not_30_out, not_31_out, not_32_out, not_33_out, not_43_out,
       not_44_out, not_45_out, not_46_out, not_47_out, or_1_out, pull_resistor_1_node, pull_resistor_2_node,
       pull_resistor_3_node, pull_resistor_5_node, pull_resistor_6_node, pull_resistor_8_node,
       pull_resistor_9_node, pull_resistor_10_node, pull_resistor_11_node, pull_resistor_12_node,
       pull_resistor_13_node, pull_resistor_14_node, pull_resistor_15_node, pull_resistor_16_node,
       pull_resistor_17_node, pull_resistor_18_node, pull_resistor_19_node, pull_resistor_20_node,
       pull_resistor_21_node, pull_resistor_22_node, pull_resistor_23_node, random_21_p1, random_24_p1,
       random_26_p2, shift_register_2_out, undriven;
  wire [1:0] controlled_buffer_9_out, controlled_buffer_10_out, counter_7_q, counter_14_q, counter_21_q,
       counter_24_q, counter_30_q, counter_31_q, n2_bit_translator_lsf0102_1_p1,
       n2_bit_translator_lsf0102_1_p4;
  wire [2:0] counter_9_q, counter_10_q, counter_13_q, counter_29_q, counter_37_q;
  wire [3:0] controlled_buffer_7_out, controlled_buffer_8_out, counter_1_q, counter_2_q, counter_3_q,
       counter_4_q, counter_5_q, counter_6_q, counter_11_q, counter_16_q, counter_18_q, counter_19_q,
       counter_20_q, counter_22_q, counter_23_q, counter_26_q, counter_27_q, counter_28_q, counter_33_q,
       counter_36_q, counter_38_q, n4_bit_line_driver_lvc125_1_p2, n4_bit_line_driver_lvc126_1_p2,
       n4_bit_translator_lsf0204_1_p1, n4_bit_translator_lsf0204_1_p4, n4_bit_up_counter_lvc161_1_p6;
  wire [4:0] counter_12_q, counter_17_q, pull_resistor_7_node;
  wire [5:0] counter_32_q, counter_34_q, counter_35_q;
  wire [7:0] controlled_buffer_1_out, controlled_buffer_2_out, controlled_buffer_3_out,
       controlled_buffer_4_out, controlled_buffer_5_out, controlled_buffer_6_out,
       n8_bit_bus_transceiver_lvc4245_1_p1, n8_bit_bus_transceiver_lvc4245_1_p5,
       n8_bit_down_counter_hct40103_1_p6, n8_bit_parallel_in_shift_lv165_1_p11,
       n16_bit_bus_transceiver_lvc164245_1_p1, n16_bit_bus_transceiver_lvc164245_1_p8, not_7_out,
       random_26_p1, shift_register_1_q0;
  wire [8:0] counter_25_q, not_34_out;
  wire [9:0] counter_8_q;
  wire [15:0] n16_bit_line_driver_lvc16244_1_p2;

  Random random_1 ();  // open: clk, next, out, clr
  Clock clock_1 (.out(clock_1_out));
  Random random_2 ();  // open: clk, next, out, clr
  Clock clock_2 (.out(clock_2_out));
  Clock clock_3 (.out(clock_3_out));
  Clock clock_4 (.out(clock_4_out));
  Clock clock_5 (.out(clock_5_out));
  Clock clock_6 (.out(clock_6_out));
  Clock clock_7 (.out(clock_7_out));
  Clock clock_8 (.out(clock_8_out));
  Counter #(.width(4), .max('hf)) counter_1 (
    .Q(counter_1_q), .clk(clock_1_out));  // open: load, D, count, carry, up, clr
  Counter #(.width(4), .max('hf)) counter_2 (
    .Q(counter_2_q), .clk(clock_2_out));  // open: load, D, count, carry, up, clr
  Counter #(.max('hf), .width(4)) counter_3 (
    .Q(counter_3_q), .clk(clock_3_out));  // open: load, D, count, carry, up, clr
  Random random_3 (.clr(clock_3_out));  // open: clk, next, out
  Counter #(.max('hf), .width(4)) counter_4 (
    .Q(counter_4_q), .clk(clock_4_out));  // open: load, D, count, carry, up, clr
  Random random_4 (.clr(clock_4_out));  // open: clk, next, out
  Counter #(.width(4), .max('hf)) counter_5 (
    .Q(counter_5_q), .clk(clock_5_out));  // open: load, D, count, carry, up, clr
  // Random random_5: pin names not known; wires that end beside it: clock_5_out
  Counter #(.width(4), .max('hf)) counter_6 (
    .Q(counter_6_q), .clk(clock_6_out));  // open: load, D, count, carry, up, clr
  // Random #(.seed(2)) random_6: pin names not known; wires that end beside it: clock_6_out
  Decoder #(.select(2)) decoder_1 (
    .out0(decoder_1_out0), .out1(decoder_1_out1), .out2(decoder_1_out2), .out3(decoder_1_out3),
    .sel(counter_7_q));  // open: en
  Counter #(.max('h3), .width(2)) counter_7 (
    .Q(counter_7_q), .clk(clock_7_out));  // open: load, D, count, carry, up, clr
  Random #(.width(4)) random_7 (.clk(clock_7_out), .next(clock_7_out));  // open: out, clr
  Counter #(.max('h3ff), .width(10)) counter_8 (
    .Q(counter_8_q), .clk(clock_8_out));  // open: load, D, count, carry, up, clr
  Random #(.width(9)) random_8 (.clk(clock_8_out), .next(clock_8_out));  // open: out, clr
  Pull_Resistor #(.pull(1)) pull_resistor_1 (.node(pull_resistor_1_node));
  // Probe on controlled_buffer_1_out
  assign controlled_buffer_1_out = counter_5_q[3] ? n8_bit_bus_transceiver_lvc4245_1_p1 : 8'bz;  // Controlled_Buffer controlled_buffer_1
  // Probe on controlled_buffer_2_out
  assign controlled_buffer_2_out = counter_6_q[3] ? n16_bit_bus_transceiver_lvc164245_1_p1 : 8'bz;  // Controlled_Buffer controlled_buffer_2
  // Probe on controlled_buffer_3_out
  assign controlled_buffer_3_out = counter_6_q[2] ? n16_bit_bus_transceiver_lvc164245_1_p1 : 8'bz;  // Controlled_Buffer controlled_buffer_3
  Comparator #(.width(10), .mode("unsigned")) comparator_1 (.b(counter_8_q));  // open: a, gt, eq, lt
  // Probe on n8_bit_bi_latch_lvc543_2_p5
  not not_1 (not_1_out, counter_5_q[3]);
  not not_2 (not_2_out, counter_6_q[3]);
  not not_3 (not_3_out, counter_6_q[2]);
  Pull_Resistor #(.pull(1)) pull_resistor_2 (.node(pull_resistor_2_node));
  Pull_Resistor pull_resistor_3 (.node(pull_resistor_3_node));
  // _16_bit_Latch__LVC16373 16_bit_latch_lvc16373_1: pin names not known; wires that end beside it: counter_1_q[0], counter_1_q[1], n16_bit_latch_lvc16373_1_p3, counter_1_q[2], n16_bit_latch_lvc16373_1_p3, counter_1_q[3], n16_bit_latch_lvc16373_1_p7, n16_bit_latch_lvc16373_1_p8
  // _8_bit_Latch__LVC373 8_bit_latch_lvc373_1: pin names not known; wires that end beside it: counter_2_q[0], n8_bit_latch_lvc373_1_p2, counter_2_q[2], n8_bit_latch_lvc373_1_p4
  // _8_bit_Bi_latch__LVC543 8_bit_bi_latch_lvc543_1: pin names not known; wires that end beside it: n8_bit_bi_latch_lvc543_1_p1, counter_3_q[1], counter_3_q[2], counter_3_q[3], n8_bit_bi_latch_lvc543_1_p1, n8_bit_bi_latch_lvc543_1_p6, n8_bit_bi_latch_lvc543_1_p7, n8_bit_bi_latch_lvc543_1_p7
  // _8_bit_Bi_latch__LVC543 8_bit_bi_latch_lvc543_2: pin names not known; wires that end beside it: n8_bit_bi_latch_lvc543_2_p1, pull_resistor_1_node, pull_resistor_1_node, pull_resistor_1_node, n8_bit_bi_latch_lvc543_2_p5, n8_bit_bi_latch_lvc543_2_p1, counter_4_q[1], counter_4_q[2], counter_4_q[3]
  // _8_bit_Bus_Transceiver__LVC4245 8_bit_bus_transceiver_lvc4245_1: pin names not known; wires that end beside it: n8_bit_bus_transceiver_lvc4245_1_p1, counter_5_q[0], controlled_buffer_1_out, not_1_out, n8_bit_bus_transceiver_lvc4245_1_p5
  // _16_bit_Bus_Transceiver__LVC164245 16_bit_bus_transceiver_lvc164245_1: pin names not known; wires that end beside it: n16_bit_bus_transceiver_lvc164245_1_p1, counter_6_q[0], counter_6_q[1], controlled_buffer_2_out, not_2_out, controlled_buffer_3_out, not_3_out, n16_bit_bus_transceiver_lvc164245_1_p8
  // _4_bit_Line_Driver__LVC125 4_bit_line_driver_lvc125_1: pin names not known; wires that end beside it: clock_7_out, n4_bit_line_driver_lvc125_1_p2, decoder_1_out0, decoder_1_out1, decoder_1_out2, decoder_1_out3, n4_bit_line_driver_lvc125_1_p2[0], n4_bit_line_driver_lvc125_1_p2[1], n4_bit_line_driver_lvc125_1_p2[2], n4_bit_line_driver_lvc125_1_p2[3], n4_bit_line_driver_lvc125_1_p11, n4_bit_line_driver_lvc125_1_p12, n4_bit_line_driver_lvc125_1_p13, n4_bit_line_driver_lvc125_1_p14
  // _512_Byte_FIFO__IDT7201 512_byte_fifo_idt7201_1: pin names not known; wires that end beside it: clock_8_out, n512_byte_fifo_idt7201_1_p2, counter_8_q[0], counter_8_q[1], pull_resistor_2_node, pull_resistor_3_node, n512_byte_fifo_idt7201_1_p2, n512_byte_fifo_idt7201_1_p8, n512_byte_fifo_idt7201_1_p9, n512_byte_fifo_idt7201_1_p10, n512_byte_fifo_idt7201_1_p11
  // Probe on n16_bit_latch_lvc16373_1_p7
  // Probe on n16_bit_latch_lvc16373_1_p8
  // Probe on n8_bit_latch_lvc373_1_p4
  // Probe on n8_bit_bi_latch_lvc543_1_p6
  Pull_Resistor #(.pull(1)) pull_resistor_4 (.node(n8_bit_bi_latch_lvc543_1_p7));
  // Probe on controlled_buffer_4_out
  assign controlled_buffer_4_out = not_4_out ? n8_bit_bus_transceiver_lvc4245_1_p5 : 8'bz;  // Controlled_Buffer controlled_buffer_4
  not not_4 (not_4_out, counter_5_q[3]);
  // Probe on controlled_buffer_5_out
  assign controlled_buffer_5_out = not_6_out ? n16_bit_bus_transceiver_lvc164245_1_p8 : 8'bz;  // Controlled_Buffer controlled_buffer_5
  // Probe on controlled_buffer_6_out
  assign controlled_buffer_6_out = not_5_out ? n16_bit_bus_transceiver_lvc164245_1_p8 : 8'bz;  // Controlled_Buffer controlled_buffer_6
  not not_5 (not_5_out, counter_6_q[2]);
  // Probe on n4_bit_line_driver_lvc125_1_p11
  // Probe on n4_bit_line_driver_lvc125_1_p12
  // Probe on n4_bit_line_driver_lvc125_1_p13
  // Probe on n4_bit_line_driver_lvc125_1_p14
  // Random #(.seed(1)) random_9: pin names not known; wires that end beside it: controlled_buffer_4_out, clock_5_out
  // Random #(.seed(3)) random_10: pin names not known; wires that end beside it: controlled_buffer_5_out, controlled_buffer_6_out, clock_6_out
  not not_6 (not_6_out, counter_6_q[3]);
  // Probe on n512_byte_fifo_idt7201_1_p9
  // Probe on n512_byte_fifo_idt7201_1_p10
  // Probe on n512_byte_fifo_idt7201_1_p11
  // Probe on n512_byte_fifo_idt7201_1_p8
  Counter #(.width(3), .max('h7)) counter_9 (
    .Q(counter_9_q), .clk(clock_9_out));  // open: load, D, count, carry, up, clr
  Clock clock_9 (.out(clock_9_out));
  Counter #(.width(3), .max('h7)) counter_10 (
    .Q(counter_10_q), .clk(clock_10_out));  // open: load, D, count, carry, up, clr
  Clock clock_10 (.out(clock_10_out));
  Counter #(.width(4), .max('hf)) counter_11 (
    .Q(counter_11_q), .clk(clock_11_out));  // open: load, D, count, carry, up, clr
  Clock clock_11 (.out(clock_11_out));
  Counter #(.width(5), .max('h1f)) counter_12 (
    .Q(counter_12_q), .clk(clock_12_out));  // open: load, D, count, carry, up, clr
  Clock clock_12 (.out(clock_12_out));
  Counter #(.width(3), .max('h7)) counter_13 (
    .Q(counter_13_q), .carry(counter_13_carry), .clk(clock_13_out));  // open: load, D, count, up, clr
  Clock clock_13 (.out(clock_13_out));
  Clock clock_14 (.out(clock_14_out));
  Clock clock_15 (.out(clock_15_out));
  Counter #(.width(2), .max('h3)) counter_14 (
    .Q(counter_14_q), .clk(clock_16_out), .clr(undriven));  // open: load, D, count, carry, up
  Clock clock_16 (.out(clock_16_out));
  Counter #(.width(4), .max('hf)) counter_15 (
    .carry(counter_15_carry), .clk(clock_17_out));  // open: load, D, count, Q, up, clr
  Clock clock_17 (.out(clock_17_out));
  Pull_Resistor pull_resistor_5 (.node(pull_resistor_5_node));
  Pull_Resistor pull_resistor_6 (.node(pull_resistor_6_node));
  not not_7 (not_7_out[0], decoder_2_out0);
  not not_8 (not_7_out[1], decoder_2_out1);
  not not_9 (not_7_out[2], decoder_2_out2);
  not not_10 (not_7_out[3], decoder_2_out3);
  not not_11 (not_7_out[4], decoder_2_out4);
  not not_12 (not_7_out[5], decoder_2_out5);
  not not_13 (not_7_out[6], decoder_2_out6);
  not not_14 (not_7_out[7], decoder_2_out7);
  Decoder #(.select(3)) decoder_2 (
    .out0(decoder_2_out0), .out1(decoder_2_out1), .out2(decoder_2_out2), .out3(decoder_2_out3),
    .out4(decoder_2_out4), .out5(decoder_2_out5), .out6(decoder_2_out6), .out7(decoder_2_out7),
    .sel(counter_11_q[2:0]));  // open: en
  Comparator #(.width(5)) comparator_2 (.a(counter_12_q), .b(5'b11100), .eq(comparator_2_eq));  // open: gt, lt
  Comparator #(.width(5)) comparator_3 (.a(counter_12_q), .b(5'b00100), .eq(comparator_3_eq));  // open: gt, lt
  Pull_Resistor pull_resistor_7 (.node(pull_resistor_7_node));
  Comparator #(.width(4)) comparator_4 (
    .a(4'b1011), .b(n4_bit_up_counter_lvc161_1_p6), .eq(comparator_4_eq));  // open: gt, lt
  Counter #(.width(4), .max('hf)) counter_16 (
    .Q(counter_16_q), .clk(counter_17_carry));  // open: load, D, count, carry, up, clr
  Counter #(.max('h1f), .width(5)) counter_17 (
    .Q(counter_17_q), .carry(counter_17_carry), .clk(clock_15_out));  // open: load, D, count, up, clr
  Decoder #(.select(2)) decoder_3 (
    .out0(decoder_3_out0), .out1(decoder_3_out1), .out2(decoder_3_out2), .out3(decoder_3_out3),
    .sel(counter_14_q));  // open: en
  Random #(.width(16)) random_11 (.clk(undriven));  // open: next, out, clr
  not not_15 (not_15_out, counter_15_carry);
  Pull_Resistor #(.pull(1)) pull_resistor_8 (.node(pull_resistor_8_node));
  Pull_Resistor #(.pull(1)) pull_resistor_9 (.node(pull_resistor_9_node));
  not not_16 (not_16_out, comparator_2_eq);
  not not_17 (not_17_out, comparator_3_eq);
  Pull_Resistor #(.pull(1)) pull_resistor_10 (.node(pull_resistor_10_node));
  not not_18 (not_18_out, comparator_4_eq);
  Pull_Resistor #(.pull(1)) pull_resistor_11 (.node(pull_resistor_11_node));
  Clock clock_18 (.out(clock_18_out));
  // _3_to_8_Decoder__LVC138 3_to_8_decoder_lvc138_1: pin names not known; wires that end beside it: pull_resistor_5_node, pull_resistor_5_node, counter_9_q, pull_resistor_8_node
  // _3_to_8_Decoder__VHC238 3_to_8_decoder_vhc238_1: pin names not known; wires that end beside it: pull_resistor_6_node, pull_resistor_6_node, counter_10_q, pull_resistor_9_node
  // _8_to_3_Encoder__LS148 8_to_3_encoder_ls148_1: pin names not known; wires that end beside it: counter_11_q[3], not_7_out, n8_to_3_encoder_ls148_1_p3, n8_to_3_encoder_ls148_1_p4, n8_to_3_encoder_ls148_1_p5
  // _4_bit_Up_Counter__LVC163 4_bit_up_counter_lvc163_1: pin names not known; wires that end beside it: pull_resistor_10_node, not_16_out, not_17_out, 4'b1010, clock_12_out, pull_resistor_10_node, pull_resistor_10_node, n4_bit_up_counter_lvc163_1_p8, n4_bit_up_counter_lvc163_1_p9
  // _8_bit_Comparator__F521 8_bit_comparator_f521_1: pin names not known; wires that end beside it: counter_13_carry, {pull_resistor_7_node, counter_13_q}, 8'h3, n8_bit_comparator_f521_1_p4
  // _4_bit_Up_Counter__LVC161 4_bit_up_counter_lvc161_1: pin names not known; wires that end beside it: not_18_out, pull_resistor_11_node, clock_14_out, pull_resistor_11_node, pull_resistor_11_node, n4_bit_up_counter_lvc161_1_p6, n4_bit_up_counter_lvc161_1_p7
  // _4_bit_Full_Adder__F283 4_bit_full_adder_f283_1: pin names not known; wires that end beside it: counter_16_q, counter_17_q[3:0], counter_17_q[4], n4_bit_full_adder_f283_1_p4, n4_bit_full_adder_f283_1_p5
  // _16_bit_Line_Driver__LVC16244 16_bit_line_driver_lvc16244_1: pin names not known; wires that end beside it: clock_16_out, n16_bit_line_driver_lvc16244_1_p2, decoder_3_out0, decoder_3_out1, decoder_3_out2, decoder_3_out3, n16_bit_line_driver_lvc16244_1_p2[3:0], n16_bit_line_driver_lvc16244_1_p2[7:4], n16_bit_line_driver_lvc16244_1_p2[11:8], n16_bit_line_driver_lvc16244_1_p2[15:12], n16_bit_line_driver_lvc16244_1_p11, n16_bit_line_driver_lvc16244_1_p12, n16_bit_line_driver_lvc16244_1_p13, n16_bit_line_driver_lvc16244_1_p14
  // EconoReset__DS1813 econoreset_ds1813_1: pin names not known; wires that end beside it: not_15_out, clock_18_out, econoreset_ds1813_1_p3
  // Probe on nothing
  // Probe on nothing
  // Probe on n8_to_3_encoder_ls148_1_p4
  // Probe on n8_to_3_encoder_ls148_1_p5
  // Probe on n8_to_3_encoder_ls148_1_p3
  // Probe on n4_bit_up_counter_lvc163_1_p8
  // Probe on n4_bit_up_counter_lvc163_1_p9
  // Probe on n8_bit_comparator_f521_1_p4
  // Probe on n4_bit_up_counter_lvc161_1_p6
  // Probe on n4_bit_up_counter_lvc161_1_p7
  // Probe on n4_bit_full_adder_f283_1_p4
  // Probe on n4_bit_full_adder_f283_1_p5
  // Probe on n16_bit_line_driver_lvc16244_1_p11
  // Probe on n16_bit_line_driver_lvc16244_1_p12
  // Probe on n16_bit_line_driver_lvc16244_1_p13
  // Probe on n16_bit_line_driver_lvc16244_1_p14
  // Probe on econoreset_ds1813_1_p3
  Random random_12 ();  // open: clk, next, out, clr
  Clock clock_19 (.out(clock_19_out));
  Random random_13 ();  // open: clk, next, out, clr
  Clock clock_20 (.out(clock_20_out));
  Clock clock_21 (.out(clock_21_out));
  Clock clock_22 (.out(clock_22_out));
  Clock clock_23 (.out(clock_23_out));
  Clock clock_24 (.out(clock_24_out));
  Random random_14 ();  // open: clk, next, out, clr
  Clock clock_25 (.out(clock_25_out));
  Counter #(.width(4), .max('hf)) counter_18 (
    .Q(counter_18_q), .clk(clock_19_out));  // open: load, D, count, carry, up, clr
  Counter #(.width(4), .max('hf)) counter_19 (
    .Q(counter_19_q), .clk(clock_20_out));  // open: load, D, count, carry, up, clr
  Counter #(.width(4), .max('hf)) counter_20 (
    .Q(counter_20_q), .clk(clock_21_out));  // open: load, D, count, carry, up, clr
  // Random #(.width(4)) random_15: pin names not known; wires that end beside it: clock_21_out
  Decoder #(.select(2)) decoder_4 (
    .out0(decoder_4_out0), .out1(decoder_4_out1), .out2(decoder_4_out2), .out3(decoder_4_out3),
    .sel(counter_21_q));  // open: en
  Counter #(.max('h3), .width(2)) counter_21 (
    .Q(counter_21_q), .clk(clock_22_out));  // open: load, D, count, carry, up, clr
  Random #(.width(4)) random_16 (.clk(clock_22_out), .next(clock_22_out));  // open: out, clr
  Comparator #(.width(4)) comparator_5 (.a(4'b0000), .b(counter_22_q), .eq(comparator_5_eq));  // open: gt, lt
  Counter #(.max('hf), .width(4)) counter_22 (
    .Q(counter_22_q), .clk(clock_24_out));  // open: load, D, count, carry, up, clr
  Comparator #(.width(4), .mode("unsigned")) comparator_6 (
    .a(counter_22_q), .b(4'b0001), .gt(comparator_6_gt));  // open: eq, lt
  Random random_17 ();  // open: clk, next, out, clr
  Counter #(.width(4), .max('hf)) counter_23 (
    .Q(counter_23_q), .clk(clock_25_out));  // open: load, D, count, carry, up, clr
  // Probe on controlled_buffer_7_out
  assign controlled_buffer_7_out = counter_20_q[3] ? n4_bit_translator_lsf0204_1_p1 : 4'bz;  // Controlled_Buffer controlled_buffer_7
  Counter #(.max('h3), .width(2)) counter_24 (
    .Q(counter_24_q), .clk(clock_23_out));  // open: load, D, count, carry, up, clr
  // Random random_18: pin names not known; wires that end beside it: clock_23_out
  not not_19 (not_19_out, decoder_4_out0);
  not not_20 (not_20_out, decoder_4_out1);
  not not_21 (not_21_out, decoder_4_out2);
  not not_22 (not_22_out, decoder_4_out3);
  Pull_Resistor pull_resistor_12 (.node(pull_resistor_12_node));
  Pull_Resistor #(.pull(1)) pull_resistor_13 (.node(pull_resistor_13_node));
  not not_23 (not_23_out, comparator_5_eq);
  not not_24 (not_24_out, comparator_6_gt);
  Pull_Resistor pull_resistor_14 (.node(pull_resistor_14_node));
  // _16_bit_Latch__LVC162373 16_bit_latch_lvc162373_1: pin names not known; wires that end beside it: counter_18_q[0], counter_18_q[1], n16_bit_latch_lvc162373_1_p3, counter_18_q[2], n16_bit_latch_lvc162373_1_p3, counter_18_q[3], n16_bit_latch_lvc162373_1_p7, n16_bit_latch_lvc162373_1_p8
  // _8_bit_Latch__LVC573 8_bit_latch_lvc573_1: pin names not known; wires that end beside it: counter_19_q[0], n8_bit_latch_lvc573_1_p2, counter_19_q[2], n8_bit_latch_lvc573_1_p4
  // _4_bit_Translator__LSF0204 4_bit_translator_lsf0204_1: pin names not known; wires that end beside it: n4_bit_translator_lsf0204_1_p1, counter_20_q[2], controlled_buffer_7_out, n4_bit_translator_lsf0204_1_p4
  // _4_bit_Line_Driver__LVC126 4_bit_line_driver_lvc126_1: pin names not known; wires that end beside it: clock_22_out, n4_bit_line_driver_lvc126_1_p2, not_19_out, not_20_out, not_21_out, not_22_out, n4_bit_line_driver_lvc126_1_p2[0], n4_bit_line_driver_lvc126_1_p2[1], n4_bit_line_driver_lvc126_1_p2[2], n4_bit_line_driver_lvc126_1_p2[3], n4_bit_line_driver_lvc126_1_p11, n4_bit_line_driver_lvc126_1_p12, n4_bit_line_driver_lvc126_1_p13, n4_bit_line_driver_lvc126_1_p14
  // _8_bit_Line_Driver__LVC541 8_bit_line_driver_lvc541_1: pin names not known; wires that end beside it: n8_bit_line_driver_lvc541_1_p1, counter_24_q[0], counter_24_q[1], n8_bit_line_driver_lvc541_1_p1, n8_bit_line_driver_lvc541_1_p5
  Shift_Register shift_register_1 (
    .shift(pull_resistor_13_node), .in(n8_bit_parallel_in_shift_lv165_1_p8), .clk(clock_24_out),
    .out(shift_register_1_q0[7]), .load(pull_resistor_12_node), .clr(comparator_5_eq),
    .d0(pull_resistor_12_node), .q0(shift_register_1_q0[0]), .d1(pull_resistor_12_node),
    .q1(shift_register_1_q0[1]), .d2(pull_resistor_12_node), .q2(shift_register_1_q0[2]),
    .d3(pull_resistor_12_node), .q3(shift_register_1_q0[3]), .d4(pull_resistor_12_node),
    .q4(shift_register_1_q0[4]), .d5(pull_resistor_12_node), .q5(shift_register_1_q0[5]),
    .d6(pull_resistor_12_node), .q6(shift_register_1_q0[6]), .d7(pull_resistor_12_node));  // open: q7
  // _8_bit_parallel_in_shift__LV165 8_bit_parallel_in_shift_lv165_1: pin names not known; wires that end beside it: comparator_5_eq, n8_bit_parallel_in_shift_lv165_1_p2, not_24_out, not_23_out, clock_24_out, n8_bit_parallel_in_shift_lv165_1_p2, pull_resistor_14_node, n8_bit_parallel_in_shift_lv165_1_p8, n8_bit_parallel_in_shift_lv165_1_p9, n8_bit_parallel_in_shift_lv165_1_p10, n8_bit_parallel_in_shift_lv165_1_p11
  // _8_bit_Latch__LVC574 8_bit_latch_lvc574_1: pin names not known; wires that end beside it: counter_23_q[3], n8_bit_latch_lvc574_1_p2, counter_23_q[1], n8_bit_latch_lvc574_1_p4
  // Probe on n16_bit_latch_lvc162373_1_p7
  // Probe on n16_bit_latch_lvc162373_1_p8
  // Probe on n8_bit_latch_lvc573_1_p4
  // Probe on controlled_buffer_8_out
  assign controlled_buffer_8_out = not_25_out ? n4_bit_translator_lsf0204_1_p4 : 4'bz;  // Controlled_Buffer controlled_buffer_8
  not not_25 (not_25_out, counter_20_q[3]);
  // Probe on n4_bit_line_driver_lvc126_1_p11
  // Probe on n4_bit_line_driver_lvc126_1_p12
  // Probe on n4_bit_line_driver_lvc126_1_p13
  // Probe on n4_bit_line_driver_lvc126_1_p14
  // Probe on n8_bit_line_driver_lvc541_1_p5
  // Random #(.seed(1), .width(4)) random_19: pin names not known; wires that end beside it: controlled_buffer_8_out, clock_21_out
  // Probe on shift_register_1_q0
  // Probe on n8_bit_parallel_in_shift_lv165_1_p8
  // Probe on n8_bit_parallel_in_shift_lv165_1_p9
  // Probe on n8_bit_latch_lvc574_1_p4
  Counter #(.max('h1ff), .width(9)) counter_25 (
    .Q(counter_25_q), .clk(clock_26_out));  // open: load, D, count, carry, up, clr
  Clock clock_26 (.out(clock_26_out));
  Clock clock_27 (.out(clock_27_out));
  Clock clock_28 (.out(clock_28_out));
  Counter #(.width(4), .max('hf)) counter_26 (
    .Q(counter_26_q), .clk(clock_29_out));  // open: load, D, count, carry, up, clr
  Clock clock_29 (.out(clock_29_out));
  Clock clock_30 (.out(clock_30_out));
  Counter #(.max('h9), .width(4)) counter_27 (
    .Q(counter_27_q), .carry(n8_bit_parallel_in_shift_lv165_1_p10), .clk(clock_31_out));  // open: load, D, count, up, clr
  Clock clock_31 (.out(clock_31_out));
  Random random_20 ();  // open: clk, next, out, clr
  Clock clock_32 (.out(clock_32_out));
  Counter #(.max('hf), .width(4)) counter_28 (
    .Q(counter_28_q), .clk(random_21_p1));  // open: load, D, count, carry, up, clr
  // Random #(.width(2)) random_21: pin names not known; wires that end beside it: random_21_p1
  Clock clock_33 (.out(random_21_p1));
  Comparator #(.width(9)) comparator_7 (.a(counter_25_q), .b(9'h1fc), .eq(comparator_7_eq));  // open: gt, lt
  Counter #(.width(3), .max('h7)) counter_29 (
    .Q(counter_29_q), .clk(clock_28_out));  // open: load, D, count, carry, up, clr
  Counter #(.max('h3), .width(2)) counter_30 (
    .Q(counter_30_q), .clk(clock_30_out));  // open: load, D, count, carry, up, clr
  Comparator #(.mode("unsigned"), .width(4)) comparator_8 (
    .a(counter_27_q), .b(4'b1000), .gt(comparator_8_gt), .eq(comparator_8_eq));  // open: lt
  Shift_Register shift_register_2 (
    .shift(pull_resistor_15_node), .in(pull_resistor_16_node), .clk(clock_31_out),
    .out(shift_register_2_out), .load(n8_bit_parallel_in_shift_lv165_1_p10), .clr(pull_resistor_17_node),
    .d0(n8_bit_parallel_in_shift_lv165_1_p11[0]), .d1(n8_bit_parallel_in_shift_lv165_1_p11[1]),
    .d2(n8_bit_parallel_in_shift_lv165_1_p11[2]), .d3(n8_bit_parallel_in_shift_lv165_1_p11[3]),
    .d4(n8_bit_parallel_in_shift_lv165_1_p11[4]), .d5(n8_bit_parallel_in_shift_lv165_1_p11[5]),
    .d6(n8_bit_parallel_in_shift_lv165_1_p11[6]), .d7(n8_bit_parallel_in_shift_lv165_1_p11[7]));  // open: q0, q1, q2, q3, q4, q5, q6, q7
  Pull_Resistor #(.pull(1)) pull_resistor_15 (.node(pull_resistor_15_node));
  Pull_Resistor pull_resistor_16 (.node(pull_resistor_16_node));
  Pull_Resistor pull_resistor_17 (.node(pull_resistor_17_node));
  Counter #(.width(2), .max('h3)) counter_31 (
    .Q(counter_31_q), .clk(clock_32_out));  // open: load, D, count, carry, up, clr
  not not_26 (not_26_out, comparator_7_eq);
  Pull_Resistor #(.pull(1)) pull_resistor_18 (.node(pull_resistor_18_node));
  Pull_Resistor pull_resistor_19 (.node(pull_resistor_19_node));
  Pull_Resistor pull_resistor_20 (.node(pull_resistor_20_node));
  not not_27 (not_27_out, comparator_8_gt);
  // Probe on controlled_buffer_9_out
  assign controlled_buffer_9_out = counter_28_q[3] ? n2_bit_translator_lsf0102_1_p1 : 2'bz;  // Controlled_Buffer controlled_buffer_9
  // _8_bit_Up_Counter__HC590 8_bit_up_counter_hc590_1: pin names not known; wires that end beside it: not_26_out, pull_resistor_18_node, counter_25_q[1], clock_26_out, counter_25_q[0], n8_bit_up_counter_hc590_1_p6, n8_bit_up_counter_hc590_1_p7
  // _12_bit_Up_Counter__HC4040 12_bit_up_counter_hc4040_1: pin names not known; wires that end beside it: pull_resistor_19_node, clock_27_out, n12_bit_up_counter_hc4040_1_p3
  // _2_to_4_Decoder__LVC139 2_to_4_decoder_lvc139_1: pin names not known; wires that end beside it: counter_29_q[2], counter_29_q[2], counter_29_q[1:0], counter_29_q[1:0]
  // _8_to_1_Multiplexer__F251 8_to_1_multiplexer_f251_1: pin names not known; wires that end beside it: counter_26_q[0], counter_26_q[3:1], 8'ha5, n8_to_1_multiplexer_f251_1_p4, n8_to_1_multiplexer_f251_1_p5
  // _4_bit_Multiplexer__LVC257 4_bit_multiplexer_lvc257_1: pin names not known; wires that end beside it: counter_30_q[0], counter_30_q[1], 4'b1010, 4'b0101, n4_bit_multiplexer_lvc257_1_p5
  // _8_bit_serial_in_shift__LVC595 8_bit_serial_in_shift_lvc595_1: pin names not known; wires that end beside it: pull_resistor_20_node, not_27_out, shift_register_2_out, clock_31_out, comparator_8_eq, n8_bit_serial_in_shift_lvc595_1_p6, n8_bit_serial_in_shift_lvc595_1_p7
  // _4_bit_Multiplexer__LVC157 4_bit_multiplexer_lvc157_1: pin names not known; wires that end beside it: counter_31_q[0], counter_31_q[1], 4'b1111, 4'b1100, n4_bit_multiplexer_lvc157_1_p5
  // _2_bit_Translator__LSF0102 2_bit_translator_lsf0102_1: pin names not known; wires that end beside it: n2_bit_translator_lsf0102_1_p1, counter_28_q[2], controlled_buffer_9_out, n2_bit_translator_lsf0102_1_p4
  // Probe on n8_bit_up_counter_hc590_1_p6
  // Probe on n8_bit_up_counter_hc590_1_p7
  // Probe on n12_bit_up_counter_hc4040_1_p3
  // Probe on nothing
  // Probe on nothing
  // Probe on n8_to_1_multiplexer_f251_1_p4
  // Probe on n8_to_1_multiplexer_f251_1_p5
  // Probe on n4_bit_multiplexer_lvc257_1_p5
  // Probe on n8_bit_serial_in_shift_lvc595_1_p6
  // Probe on n8_bit_serial_in_shift_lvc595_1_p7
  // Probe on n4_bit_multiplexer_lvc157_1_p5
  // Probe on controlled_buffer_10_out
  assign controlled_buffer_10_out = not_28_out ? n2_bit_translator_lsf0102_1_p4 : 2'bz;  // Controlled_Buffer controlled_buffer_10
  not not_28 (not_28_out, counter_28_q[3]);
  // Random #(.width(2), .seed(1)) random_22: pin names not known; wires that end beside it: controlled_buffer_10_out, random_21_p1
  Clock clock_34 (.out(clock_34_out));
  Clock clock_35 (.out(clock_35_out));
  Clock clock_36 (.out(clock_36_out));
  Counter #(.max('h3f), .width(6)) counter_32 (
    .Q(counter_32_q), .clk(clock_34_out));  // open: load, D, count, carry, up, clr
  Counter #(.width(4), .max('hf)) counter_33 (
    .Q(counter_33_q), .clk(clock_35_out));  // open: load, D, count, carry, up, clr
  Counter #(.width(6), .max('h3f)) counter_34 (
    .Q(counter_34_q), .clk(clock_36_out));  // open: load, D, count, carry, up, clr
  Comparator #(.mode("unsigned"), .width(6)) comparator_9 (
    .a(counter_32_q), .b(6'b000011), .gt(comparator_9_gt));  // open: eq, lt
  Comparator #(.width(6), .mode("unsigned")) comparator_10 (
    .a(counter_32_q), .b(6'b011001), .gt(comparator_10_gt));  // open: eq, lt
  Comparator #(.width(6), .mode("unsigned")) comparator_11 (
    .a(counter_32_q), .b(6'b110010), .eq(comparator_11_eq));  // open: gt, lt
  not not_29 (not_29_out, counter_33_q[3]);
  Comparator #(.mode("unsigned"), .width(6)) comparator_12 (
    .a(6'b000011), .b(counter_34_q), .eq(comparator_12_eq));  // open: gt, lt
  Comparator #(.mode("unsigned"), .width(6)) comparator_13 (
    .a(counter_34_q), .b(6'b010111), .eq(comparator_13_eq));  // open: gt, lt
  Clock clock_37 (.out(clock_37_out));
  Comparator #(.width(6), .mode("unsigned")) comparator_14 (
    .a(counter_32_q), .b(6'b010111), .lt(comparator_14_lt));  // open: gt, eq
  Comparator #(.width(6), .mode("unsigned")) comparator_15 (
    .a(counter_32_q), .b(6'b101111), .lt(comparator_15_lt));  // open: gt, eq
  Comparator #(.width(6), .mode("unsigned")) comparator_16 (
    .a(counter_32_q), .b(6'b110110), .eq(comparator_16_eq));  // open: gt, lt
  Random random_23 ();  // open: clk, next, out, clr
  Comparator #(.mode("unsigned"), .width(6)) comparator_17 (
    .a(counter_34_q), .b(6'b011011), .eq(comparator_17_eq));  // open: gt, lt
  Counter #(.max('h3f), .width(6)) counter_35 (
    .Q(counter_35_q), .clk(random_24_p1));  // open: load, D, count, carry, up, clr
  // Random #(.width(1)) random_24: pin names not known; wires that end beside it: random_24_p1
  Clock clock_38 (.out(random_24_p1));
  Counter #(.max('ha), .width(4)) counter_36 (
    .Q(counter_36_q), .clk(clock_37_out));  // open: load, D, count, carry, up, clr
  Counter #(.width(3), .max('h7)) counter_37 (
    .Q(counter_37_q), .clk(clock_39_out));  // open: load, D, count, carry, up, clr
  Clock clock_39 (.out(clock_39_out));
  Counter #(.width(4), .max('hf)) counter_38 (
    .Q(counter_38_q), .clk(clock_40_out));  // open: load, D, count, carry, up, clr
  Clock clock_40 (.out(clock_40_out));
  and and_1 (and_1_out, comparator_14_lt, clock_34_out, comparator_9_gt);
  Random #(.width(4)) random_25 (.clk(clock_34_out));  // open: next, out, clr
  and and_2 (and_2_out, comparator_15_lt, clock_34_out, comparator_10_gt);
  not not_30 (not_30_out, comparator_11_eq);
  Pull_Resistor #(.pull(1)) pull_resistor_21 (.node(pull_resistor_21_node));
  Pull_Resistor #(.pull(1)) pull_resistor_22 (.node(pull_resistor_22_node));
  not not_31 (not_31_out, comparator_12_eq);
  not not_32 (not_32_out, comparator_13_eq);
  not not_33 (not_33_out, comparator_17_eq);
  not not_34 (not_34_out[0], decoder_5_out0);
  not not_35 (not_34_out[1], decoder_5_out1);
  not not_36 (not_34_out[2], decoder_5_out2);
  not not_37 (not_34_out[3], decoder_5_out3);
  not not_38 (not_34_out[4], decoder_5_out4);
  not not_39 (not_34_out[5], decoder_5_out5);
  not not_40 (not_34_out[6], decoder_5_out6);
  not not_41 (not_34_out[7], decoder_5_out7);
  not not_42 (not_34_out[8], decoder_5_out8);
  Decoder #(.select(4)) decoder_5 (
    .out0(decoder_5_out0), .out1(decoder_5_out1), .out2(decoder_5_out2), .out3(decoder_5_out3),
    .out4(decoder_5_out4), .out5(decoder_5_out5), .out6(decoder_5_out6), .out7(decoder_5_out7),
    .out8(decoder_5_out8), .sel(counter_36_q));  // open: out9, out10, out11, out12, out13, out14, out15, en
  not not_43 (not_43_out, and_1_out);
  not not_44 (not_44_out, and_2_out);
  not not_45 (not_45_out, counter_35_q[4]);
  not not_46 (not_46_out, counter_35_q[5]);
  Pull_Resistor #(.pull(1)) pull_resistor_23 (.node(pull_resistor_23_node));
  not not_47 (not_47_out, counter_37_q[2]);
  // _4_bit_Up_Down_Counter__HCT193 4_bit_up_down_counter_hct193_1: pin names not known; wires that end beside it: and_2_out, n4_bit_up_down_counter_hct193_1_p2, not_30_out, comparator_16_eq, n4_bit_up_down_counter_hct193_1_p2, not_43_out, not_44_out, n4_bit_up_down_counter_hct193_1_p8, n4_bit_up_down_counter_hct193_1_p9, n4_bit_up_down_counter_hct193_1_p10
  // _4_bit_Up_Down_Counter__HCT193 4_bit_up_down_counter_hct193_2: pin names not known; wires that end beside it: pull_resistor_21_node, comparator_16_eq, pull_resistor_22_node, n4_bit_up_down_counter_hct193_1_p9, n4_bit_up_down_counter_hct193_1_p10, n4_bit_up_down_counter_hct193_2_p6, n4_bit_up_down_counter_hct193_2_p7, n4_bit_up_down_counter_hct193_2_p8
  // _8_bit_Latch__LVC273 8_bit_latch_lvc273_1: pin names not known; wires that end beside it: n8_bit_latch_lvc273_1_p1, not_29_out, n8_bit_latch_lvc273_1_p1, counter_33_q[1], n8_bit_latch_lvc273_1_p5
  // _8_bit_Down_Counter__HCT40103 8_bit_down_counter_hct40103_1: pin names not known; wires that end beside it: not_31_out, not_32_out, not_33_out, counter_34_q[5], clock_36_out, n8_bit_down_counter_hct40103_1_p6
  // D_type_Flip_Flop__LVC74 d_type_flip_flop_lvc74_1: pin names not known; wires that end beside it: d_type_flip_flop_lvc74_1_p1, not_45_out, not_46_out, pull_resistor_23_node, pull_resistor_23_node, counter_35_q[0], d_type_flip_flop_lvc74_1_p1, random_24_p1, d_type_flip_flop_lvc74_1_p9, d_type_flip_flop_lvc74_1_p10, d_type_flip_flop_lvc74_1_p9, d_type_flip_flop_lvc74_1_p10
  // _10_to_4_Encoder__HC147 10_to_4_encoder_hc147_1: pin names not known; wires that end beside it: not_34_out, n10_to_4_encoder_hc147_1_p2
  // _4_to_1_Multiplexer__QS3253 4_to_1_multiplexer_qs3253_1: pin names not known; wires that end beside it: counter_37_q[2], not_47_out, counter_37_q[1:0], 4'b0001, 4'b1000, n4_to_1_multiplexer_qs3253_1_p6, n4_to_1_multiplexer_qs3253_1_p7
  // _8_to_1_Multiplexer__B3251 8_to_1_multiplexer_b3251_1: pin names not known; wires that end beside it: counter_38_q[3], counter_38_q[2:0], 8'h81, n8_to_1_multiplexer_b3251_1_p4
  // Random #(.seed(78)) random_26: pin names not known; wires that end beside it: random_26_p1, random_26_p2, counter_34_q[0]
  // Probe on n4_to_1_multiplexer_qs3253_1_p6
  // Probe on n4_to_1_multiplexer_qs3253_1_p7
  // Probe on n8_to_1_multiplexer_b3251_1_p4
  // Probe on n4_bit_up_down_counter_hct193_1_p8
  // Probe on n4_bit_up_down_counter_hct193_1_p9
  // Probe on n4_bit_up_down_counter_hct193_1_p10
  // Probe on n4_bit_up_down_counter_hct193_2_p6
  // Probe on n4_bit_up_down_counter_hct193_2_p7
  // Probe on n4_bit_up_down_counter_hct193_2_p8
  // Probe on n8_bit_latch_lvc273_1_p5
  // Probe on random_26_p1
  // Probe on random_26_p2
  assign random_26_p1 = or_1_out ? n8_bit_down_counter_hct40103_1_p6 : 8'bz;  // Controlled_Buffer controlled_buffer_11
  or or_1 (or_1_out, comparator_13_eq, comparator_17_eq);
  // Probe on n10_to_4_encoder_hc147_1_p2
endmodule
