// Logisim project demo.circ as structural Verilog: 1 circuit, main circuit main
module main (
);

  wire Abort_816_out, and_1_out, and_2_out, clock_1_out, clock_2_out, IRQ_02_out, IRQ_816_out, NMI_02_out,
       NMI_816_out, not_1_out, not_2_out, not_3_out, not_4_out, not_5_out, not_6_out, not_7_out, not_8_out,
       not_9_out, not_10_out, pull_resistor_3_node, pull_resistor_4_node, Reset_02_out, Reset_816_out,
       w65c02s_1_p1, w65c02s_1_p2, w65c02s_1_p11, w65c02s_1_p12, w65c02s_1_p13, w65c02s_1_p14, w65c02s_1_p15,
       w65c816s_1_p1, w65c816s_1_p2, w65c816s_1_p3, w65c816s_1_p14, w65c816s_1_p15, w65c816s_1_p16,
       w65c816s_1_p17, w65c816s_1_p18, w65c816s_1_p19;
  wire [7:0] controlled_buffer_3_out, controlled_buffer_4_out, w65c02s_1_p10, w65c816s_1_p13;
  wire [15:0] w65c02s_1_p9, w65c816s_1_p12;

  Clock clock_1 (.out(clock_1_out));
  Button Abort_816 (.out(Abort_816_out));
  Button IRQ_816 (.out(IRQ_816_out));
  Button NMI_816 (.out(NMI_816_out));
  Button Reset_816 (.out(Reset_816_out));
  Clock clock_2 (.out(clock_2_out));
  Button IRQ_02 (.out(IRQ_02_out));
  Button NMI_02 (.out(NMI_02_out));
  Button Reset_02 (.out(Reset_02_out));
  not not_1 (not_1_out, Abort_816_out);
  not not_2 (not_2_out, IRQ_816_out);
  not not_3 (not_3_out, NMI_816_out);
  not not_4 (not_4_out, Reset_816_out);
  not not_5 (not_5_out, IRQ_02_out);
  not not_6 (not_6_out, NMI_02_out);
  not not_7 (not_7_out, Reset_02_out);
  // W65C816S w65c816s_1: pin names not known; wires that end beside it: w65c816s_1_p1, w65c816s_1_p2, w65c816s_1_p3, not_1_out, not_2_out, not_3_out, not_4_out, clock_1_out, w65c816s_1_p1, w65c816s_1_p2, w65c816s_1_p3, w65c816s_1_p12, w65c816s_1_p13, w65c816s_1_p14, w65c816s_1_p15, w65c816s_1_p16, w65c816s_1_p17, w65c816s_1_p18, w65c816s_1_p19, w65c816s_1_p16, w65c816s_1_p17, w65c816s_1_p18, w65c816s_1_p19
  // W65C02S w65c02s_1: pin names not known; wires that end beside it: w65c02s_1_p1, w65c02s_1_p2, not_5_out, not_6_out, not_7_out, clock_2_out, w65c02s_1_p1, w65c02s_1_p2, w65c02s_1_p9, w65c02s_1_p10, w65c02s_1_p11, w65c02s_1_p12, w65c02s_1_p13, w65c02s_1_p14, w65c02s_1_p15, w65c02s_1_p13, w65c02s_1_p14, w65c02s_1_p15
  Register #(.trigger("high")) register_1 (.D(w65c816s_1_p13), .clk(clock_1_out));  // open: en, Q, clr
  not not_8 (not_8_out, clock_1_out);
  // Probe on w65c816s_1_p13
  Pull_Resistor #(.pull(1)) pull_resistor_1 (.node(w65c816s_1_p15));
  // Probe on w65c02s_1_p10
  Pull_Resistor #(.pull(1)) pull_resistor_2 (.node(w65c02s_1_p12));
  assign w65c816s_1_p13 = and_1_out ? controlled_buffer_3_out : 8'bz;  // Controlled_Buffer controlled_buffer_1
  and and_1 (and_1_out, w65c816s_1_p14, not_8_out);
  not not_9 (not_9_out, w65c816s_1_p14);
  assign w65c02s_1_p10 = w65c02s_1_p11 ? controlled_buffer_4_out : 8'bz;  // Controlled_Buffer controlled_buffer_2
  not not_10 (not_10_out, w65c02s_1_p11);
  assign controlled_buffer_3_out = and_2_out ? w65c816s_1_p13 : 8'bz;  // Controlled_Buffer controlled_buffer_3
  and and_2 (and_2_out, not_8_out, not_9_out);
  Pull_Resistor #(.pull(1)) pull_resistor_3 (.node(pull_resistor_3_node));
  assign controlled_buffer_4_out = not_10_out ? w65c02s_1_p10 : 8'bz;  // Controlled_Buffer controlled_buffer_4
  Pull_Resistor #(.pull(1)) pull_resistor_4 (.node(pull_resistor_4_node));
  // Probe on w65c816s_1_p12
  RAM #(.addrWidth(16), .databus("bidir"), .enables("line"), .trigger("high"), .\type ("nonvolatile")) ram_1 (
    .addr(w65c816s_1_p12), .data(controlled_buffer_3_out));  // open: we, oe, clk
  RAM #(.addrWidth(16), .databus("bidir"), .enables("line"), .trigger("high"), .\type ("nonvolatile")) ram_2 (
    .addr(w65c02s_1_p9), .data(controlled_buffer_4_out));  // open: we, oe, clk
  // Probe on controlled_buffer_3_out
  // Probe on controlled_buffer_4_out
endmodule
