// Logisim project demo2.circ as structural Verilog: 1 circuit, main circuit main
module main (
);

  wire clock_2_out, ds1813_1_p2, not_1_out, not_2_out, not_3_out, PHI2, pull_resistor_1_node,
       pull_resistor_3_node, RWB, wdc65816_1_p10, wdc65816_1_p12;
  wire [7:0] A0_7, A8_15, BA0_7, D;

  Clock clock_1 (.out(PHI2));
  Clock clock_2 (.out(clock_2_out));
  // DS1813 ds1813_1: pin names not known; wires that end beside it: clock_2_out, ds1813_1_p2
  Pull_Resistor #(.pull(1)) pull_resistor_1 (.node(pull_resistor_1_node));
  // Probe on {BA0_7, A8_15, A0_7}
  RAM #(.addrWidth(24), .databus("bidir"), .enables("line"), .trigger("high"), .\type ("nonvolatile")) ram_1 (
    .addr({BA0_7, A8_15, A0_7}), .data(D));  // open: we, oe, clk
  not not_1 (not_1_out, RWB);
  // WDC65816 wdc65816_1: pin names not known; wires that end beside it: pull_resistor_1_node, pull_resistor_1_node, pull_resistor_1_node, ds1813_1_p2, PHI2, RWB, not_1_out, PHI2, {A8_15, A0_7}, wdc65816_1_p10, RWB, wdc65816_1_p12
  Pull_Resistor #(.pull(1)) pull_resistor_2 (.node(wdc65816_1_p12));
  // Probe on D
  // Probe on wdc65816_1_p10
  Pull_Resistor pull_resistor_3 (.node(pull_resistor_3_node));
  not not_2 (not_2_out, PHI2);
  not not_3 (not_3_out, PHI2);
  // LVC573 lvc573_1: pin names not known; wires that end beside it: pull_resistor_3_node, wdc65816_1_p10, not_2_out, BA0_7
  // LVC4245 lvc4245_1: pin names not known; wires that end beside it: not_3_out, wdc65816_1_p10, RWB, D
  // Probe on BA0_7
  // Probe on D
endmodule
