// Logisim project demo3.circ as structural Verilog: 1 circuit, main circuit main
module main (
  input  in_1
);

  wire lvc4245_1_p1;

  // DS1813 ds1813_1: pin names not known; wires that end beside it: in_1
  // LVC4245 lvc4245_1: pin names not known; wires that end beside it: lvc4245_1_p1
  Clock clock_1 (.out(lvc4245_1_p1));
endmodule
